// Logisim project HSnakeProject (Win screen).circ as structural Verilog: 7 circuits, main circuit main
module main (
);

  wire and_1_out, cdm_8_mark5_1_data_inst, cdm_8_mark5_1_mem_cycle, code, data, IAck, IOsel, IRQ,
       keyboard_1_avail, not_1_out, R_W, tck;
  wire [2:0] IOaddr, vec;
  wire [3:0] Direction;
  wire [6:0] keyboardButton;
  wire [7:0] cdm_8_mark5_1_data_out, cdm_8_mark5_1_pc, cdm_8_mark5_1_ps, cdm_8_mark5_1_r0, cdm_8_mark5_1_r1,
       cdm_8_mark5_1_r2, cdm_8_mark5_1_r3, cdm_8_mark5_1_sp, controlled_buffer_2_out, IOdat,
       scorechip_1_to_score_screen;
  wire [7:3] cdm_8_mark5_1_addr;
  wire [31:0] displaycontrollerchip_1_out_8, displaycontrollerchip_1_out_9, displaycontrollerchip_1_out_10,
       displaycontrollerchip_1_out_11, displaycontrollerchip_1_out_12, displaycontrollerchip_1_out_13,
       displaycontrollerchip_1_out_14, displaycontrollerchip_1_out_15, displaycontrollerchip_1_out_16,
       displaycontrollerchip_1_out_17, displaycontrollerchip_1_out_18, displaycontrollerchip_1_out_19,
       displaycontrollerchip_1_out_20, displaycontrollerchip_1_out_21, displaycontrollerchip_1_out_22,
       displaycontrollerchip_1_out_23;

  Pull_Resistor pull_resistor_1 (.node(IRQ));
  Pull_Resistor pull_resistor_2 (.node(code));
  Pull_Resistor pull_resistor_3 (.node(data));
  // Probe on cdm_8_mark5_1_r3
  // Probe on cdm_8_mark5_1_r2
  // Probe on cdm_8_mark5_1_r1
  // Probe on cdm_8_mark5_1_r0
  Clock clock_1 (.out(tck));
  // Probe on cdm_8_mark5_1_sp
  // Probe on cdm_8_mark5_1_ps
  // Probe on cdm_8_mark5_1_pc
  CdM_8_mark5 cdm_8_mark5_1 (
    .clock(tck), .addr({cdm_8_mark5_1_addr, IOaddr}), .mem_read(R_W), .mem_cycle(cdm_8_mark5_1_mem_cycle),
    .data_inst(cdm_8_mark5_1_data_inst), .data_out(cdm_8_mark5_1_data_out),
    .data_in(controlled_buffer_2_out), .r0(cdm_8_mark5_1_r0), .r1(cdm_8_mark5_1_r1), .r2(cdm_8_mark5_1_r2),
    .r3(cdm_8_mark5_1_r3), .PC(cdm_8_mark5_1_pc), .SP(cdm_8_mark5_1_sp), .PS(cdm_8_mark5_1_ps), .IAck(IAck),
    .IRQ(IRQ), .vec(vec));
  randomGenChip randomgenchip_1 (.ADDR(IOaddr), .SEL(IOsel), .R_W(R_W), .DATA(IOdat));
  keyboardChip keyboardchip_1 (
    .ADDRESS(IOaddr), .SEL(IOsel), .R_W(R_W), .DATA_2(IOdat), .DATA(IOdat), .Control(Direction));
  Decoder #(.disabled(0)) decoder_1 (
    .out0(code), .out1(data), .sel(cdm_8_mark5_1_data_inst), .en(cdm_8_mark5_1_mem_cycle));
  not not_1 (not_1_out, R_W);
  assign IOdat = not_1_out ? cdm_8_mark5_1_data_out : 8'bz;  // Controlled_Buffer controlled_buffer_1
  assign controlled_buffer_2_out = R_W ? IOdat : 8'bz;  // Controlled_Buffer controlled_buffer_2
  and and_1 (and_1_out, ~IOsel, data);  // AND_Gate
  Comparator #(.width(7)) comparator_1 (.a(keyboardButton), .b(7'b1100001), .eq(Direction[0]));  // open: gt, lt
  Comparator #(.width(7)) comparator_2 (.a(keyboardButton), .b(7'b1100100), .eq(Direction[1]));  // open: gt, lt
  Comparator #(.width(7)) comparator_3 (.a(keyboardButton), .b(7'b1110111), .eq(Direction[2]));  // open: gt, lt
  Comparator #(.width(7)) comparator_4 (.a(keyboardButton), .b(7'b1110011), .eq(Direction[3]));  // open: gt, lt
  and and_2 (IOsel, cdm_8_mark5_1_addr[3], cdm_8_mark5_1_addr[4], cdm_8_mark5_1_addr[5], cdm_8_mark5_1_addr[7], cdm_8_mark5_1_addr[6], data);
  ROM rom_1 (.addr({cdm_8_mark5_1_addr, IOaddr}), .data(IOdat), .sel(code));
  RAM ram_1 (.addr({cdm_8_mark5_1_addr, IOaddr}), .data(IOdat), .sel(and_1_out), .clk(tck), .ld(R_W));  // open: clr
  DotMatrix #(.matrixcols(32), .matrixrows(32)) dotmatrix_1 (
    .col0(displaycontrollerchip_1_out_8), .col1(displaycontrollerchip_1_out_8),
    .col2(displaycontrollerchip_1_out_9), .col3(displaycontrollerchip_1_out_9),
    .col4(displaycontrollerchip_1_out_10), .col5(displaycontrollerchip_1_out_10),
    .col6(displaycontrollerchip_1_out_11), .col7(displaycontrollerchip_1_out_11),
    .col8(displaycontrollerchip_1_out_12), .col9(displaycontrollerchip_1_out_12),
    .col10(displaycontrollerchip_1_out_13), .col11(displaycontrollerchip_1_out_13),
    .col12(displaycontrollerchip_1_out_14), .col13(displaycontrollerchip_1_out_14),
    .col14(displaycontrollerchip_1_out_15), .col15(displaycontrollerchip_1_out_15),
    .col16(displaycontrollerchip_1_out_16), .col17(displaycontrollerchip_1_out_16),
    .col18(displaycontrollerchip_1_out_17), .col19(displaycontrollerchip_1_out_17),
    .col20(displaycontrollerchip_1_out_18), .col21(displaycontrollerchip_1_out_18),
    .col22(displaycontrollerchip_1_out_19), .col23(displaycontrollerchip_1_out_19),
    .col24(displaycontrollerchip_1_out_20), .col25(displaycontrollerchip_1_out_20),
    .col26(displaycontrollerchip_1_out_21), .col27(displaycontrollerchip_1_out_21),
    .col28(displaycontrollerchip_1_out_22), .col29(displaycontrollerchip_1_out_22),
    .col30(displaycontrollerchip_1_out_23), .col31(displaycontrollerchip_1_out_23));
  // Probe on scorechip_1_to_score_screen
  displayControllerChip displaycontrollerchip_1 (
    .ADDRESS(IOaddr), .SEL(IOsel), .R_W(R_W), .DATA(IOdat), .out_17(displaycontrollerchip_1_out_17),
    .out_18(displaycontrollerchip_1_out_18), .out_19(displaycontrollerchip_1_out_19),
    .out_20(displaycontrollerchip_1_out_20), .out_21(displaycontrollerchip_1_out_21),
    .out_22(displaycontrollerchip_1_out_22), .out_23(displaycontrollerchip_1_out_23),
    .out_8(displaycontrollerchip_1_out_8), .out_9(displaycontrollerchip_1_out_9),
    .out_10(displaycontrollerchip_1_out_10), .out_11(displaycontrollerchip_1_out_11),
    .out_12(displaycontrollerchip_1_out_12), .out_13(displaycontrollerchip_1_out_13),
    .out_14(displaycontrollerchip_1_out_14), .out_15(displaycontrollerchip_1_out_15),
    .out_16(displaycontrollerchip_1_out_16), .IRQ(IRQ), .IACK(IAck), .VEC(vec), .TICK(tck), .DATA_2(IOdat));
  Keyboard keyboard_1 (.clk(keyboard_1_avail), .avail(keyboard_1_avail), .data(keyboardButton));  // open: re, clr
  scoreChip scorechip_1 (
    .ADDRESS(IOaddr), .SEL(IOsel), .R_W(R_W), .DATA(IOdat), .DATA_2(IOdat),
    .to_Score_screen(scorechip_1_to_score_screen), .tck(tck));

  // Notes on the sheet:
  //   contents of rom_1 (hex, n*v repeats v):
  //   cd af d0 9 c0 d0 80 c0 d9 d0 fb d1 3e a1 d1 43 a1 d1 48 a1 d1 4d a1 d0 f8 d3 f3 d1 6 ad a1 8f ad a1
  //   d1 0 a1 d0 f1 d1 b0 d2 66 a6 a1 d1 fb b4 0 e0 2f d6 9f d0 f8 d1 fb b5 c1 d7 ee 37 d6 99 8a ee 50 d6
  //   99 8e ee 50 d6 99 8d ee 50 d6 99 89 d0 f8 a1 a2 d3 f0 47 e1 ac d3 f0 4b e1 ac d3 f3 ad 8f ae b1 d3
  //   f0 bf 77 e0 b8 d1 f1 b5 b7 a3 d3 f2 bf 8f d1 b0 b2 b4 78 e0 ac 8d 8b e1 76 d0 f8 d1 f1 b5 b3 a7 89
  //   d2 b0 76 d3 f2 bf ea 90 1e 9 b2 d0 f1 a1 8f d0 f8 ee 37 d3 f4 be 8b bd d7 d0 f9 b1 8c a1 d0 f0 a1 d7
  //   d1 10 ee ae d1 0 d0 fd a1 d3 10 a1 8b e1 b3 d4 c0 c1 c2 d2 40 d6 9f d0 f2 b1 8d 76 e0 a8 a1 d0 fc a1
  //   c6 c5 c4 ee 6a 39*0 b8 1
endmodule

module displayControllerChip (
  input  [2:0] ADDRESS,
  input  SEL,
  input  R_W,
  input  [7:0] DATA,
  input  TICK,
  input  IACK,
  output [7:0] DATA_2,
  output [31:0] out_8,
  output [31:0] out_9,
  output [31:0] out_10,
  output [31:0] out_11,
  output [31:0] out_12,
  output [31:0] out_13,
  output [31:0] out_14,
  output [31:0] out_15,
  output [31:0] out_16,
  output [31:0] out_17,
  output [31:0] out_18,
  output [31:0] out_19,
  output [31:0] out_20,
  output [31:0] out_21,
  output [31:0] out_22,
  output [31:0] out_23,
  output IRQ,
  output [2:0] VEC
);

  wire and_2_out, comparator_1_eq, comparator_2_eq, controlled_buffer_1_out, controlled_inverter_1_out,
       d_ff_1_q, enable_apple, Free_lock, IO_0_Read, IO_0_update, IO_2_update, IO_5_update, j_k_ff_1_q,
       LoadImageNum, multiplexer_1_out, nor_1_out, not_1_out, not_2_out, not_3_out, pull_resistor_1_node,
       register_1_q, register_2_q, restart_cap, T1, T2, T3, undriven, update_screen;
  wire [1:0] counter_3_q;
  wire [3:0] APPLEX, APPLEY, Free_X, HEADX, HEADY, multiplexer_2_out;
  wire [7:0] controlled_buffer_4_out, controlled_buffer_5_out, controlled_buffer_8_out,
       controlled_buffer_9_out, Coordinate, counter_1_q, register_5_q;
  wire [15:0] capacitormodule_16x16_1_c1, capacitormodule_16x16_1_c1_2, capacitormodule_16x16_1_c1_3,
       capacitormodule_16x16_1_c1_4, capacitormodule_16x16_1_c1_5, capacitormodule_16x16_1_c1_6,
       capacitormodule_16x16_1_c1_7, capacitormodule_16x16_1_c1_8, capacitormodule_16x16_1_c1_9,
       capacitormodule_16x16_1_c1_10, capacitormodule_16x16_1_c1_11, capacitormodule_16x16_1_c1_12,
       capacitormodule_16x16_1_c1_13, capacitormodule_16x16_1_c1_14, capacitormodule_16x16_1_c1_15,
       capacitormodule_16x16_1_c1_16, decoder_2_out0, decoder_3_out0, demultiplexer_1_out0,
       demultiplexer_1_out1, demultiplexer_1_out2, demultiplexer_1_out3, demultiplexer_1_out4,
       demultiplexer_1_out5, demultiplexer_1_out6, demultiplexer_1_out7, demultiplexer_1_out8,
       demultiplexer_1_out9, demultiplexer_1_out10, demultiplexer_1_out11, demultiplexer_1_out12,
       demultiplexer_1_out13, demultiplexer_1_out14, demultiplexer_1_out15, demultiplexer_2_out0,
       demultiplexer_2_out1, demultiplexer_2_out2, demultiplexer_2_out3, demultiplexer_2_out4,
       demultiplexer_2_out5, demultiplexer_2_out6, demultiplexer_2_out7, demultiplexer_2_out8,
       demultiplexer_2_out9, demultiplexer_2_out10, demultiplexer_2_out11, demultiplexer_2_out12,
       demultiplexer_2_out13, demultiplexer_2_out14, demultiplexer_2_out15, demultiplexer_3_out0,
       demultiplexer_4_out0, demultiplexer_4_out1, demultiplexer_4_out2, demultiplexer_4_out3,
       demultiplexer_4_out4, demultiplexer_4_out5, demultiplexer_4_out6, demultiplexer_4_out7,
       demultiplexer_4_out8, demultiplexer_4_out9, demultiplexer_4_out10, demultiplexer_4_out11,
       demultiplexer_4_out12, demultiplexer_4_out13, demultiplexer_4_out14, demultiplexer_4_out15,
       Free_Column, multiplexer_3_out, smallor_16_bit_1_out_3, smallor_16_bit_2_out_3,
       smallor_16_bit_3_out_3, smallor_16_bit_4_out_3, smallor_16_bit_5_out_3, smallor_16_bit_6_out_3,
       smallor_16_bit_7_out_3, smallor_16_bit_8_out_3, smallor_16_bit_9_out_3, smallor_16_bit_10_out_3,
       smallor_16_bit_11_out_3, smallor_16_bit_12_out_3, smallor_16_bit_13_out_3, smallor_16_bit_14_out_3,
       smallor_16_bit_15_out_3, smallor_16_bit_16_out_3;

  D_Flip_Flop d_ff_1 (.clk(IO_5_update), .D(IO_5_update), .Q(d_ff_1_q), .Qn(Free_lock));  // open: preset, en, reset
  D_Flip_Flop #(.trigger("falling")) d_ff_2 (
    .clk(IO_5_update), .D(1'b1), .Qn(LoadImageNum));  // open: Q, preset, en, reset
  assign controlled_buffer_1_out = LoadImageNum ? 1'b1 : 1'bz;  // Controlled_Buffer controlled_buffer_1
  Counter #(.ongoal("stay"), .trigger("falling")) counter_1 (
    .load(controlled_buffer_1_out), .D(DATA), .count(controlled_inverter_1_out), .Q(counter_1_q),
    .clk(IO_5_update));  // open: carry, clr
  assign controlled_inverter_1_out = LoadImageNum ? ~1'b1 : 1'bz;  // Controlled_Inverter controlled_inverter_1
  Comparator #(.width(4), .mode("unsigned")) comparator_1 (
    .a(APPLEX), .b(HEADX), .eq(comparator_1_eq));  // open: gt, lt
  Comparator #(.width(4), .mode("unsigned")) comparator_2 (
    .a(APPLEY), .b(HEADY), .eq(comparator_2_eq));  // open: gt, lt
  and IO_0R (IO_0_Read, R_W, SEL, ~ADDRESS[0], ~ADDRESS[1], ~ADDRESS[2]);  // AND_Gate
  and IO_0W (IO_0_update, ~R_W, SEL, ~ADDRESS[0], ~ADDRESS[1], ~ADDRESS[2]);  // AND_Gate
  and IO_2W (IO_2_update, ~R_W, SEL, ~ADDRESS[0], ADDRESS[1], ~ADDRESS[2]);  // AND_Gate
  and IO_5W (IO_5_update, ~R_W, SEL, ADDRESS[0], ~ADDRESS[1], ADDRESS[2]);  // AND_Gate
  not not_1 (not_1_out, d_ff_1_q);
  not not_2 (not_2_out, Free_lock);
  Counter #(.width(4), .max('hf), .ongoal("stay"), .trigger("falling")) counter_2 (
    .load(LoadImageNum), .Q(Free_X), .clk(IO_5_update));  // open: D, count, carry, clr
  and and_1 (restart_cap, not_1_out, d_ff_1_q);
  ROM #(.dataWidth(16)) rom_1 (.addr(counter_1_q), .data(Free_Column), .sel(not_2_out));
  and and_2 (and_2_out, comparator_1_eq, comparator_2_eq);
  Register #(.width(1)) register_1 (.D(and_2_out), .Q(register_1_q), .clk(update_screen), .clr(IACK));  // open: en
  Multiplexer #(.disabled(0)) multiplexer_1 (
    .in0(undriven), .in1(1'b0), .out(multiplexer_1_out), .sel(IACK), .en(enable_apple));
  Register #(.width(1)) register_2 (.D(multiplexer_1_out), .Q(register_2_q), .clk(TICK));  // open: en, clr
  assign Coordinate = IO_0_update ? DATA : 8'bz;  // Controlled_Buffer controlled_buffer_2
  assign IRQ = register_2_q ? 1'b1 : 1'bz;  // Controlled_Buffer controlled_buffer_3
  assign controlled_buffer_4_out = T2 ? Coordinate : 8'bz;  // Controlled_Buffer controlled_buffer_4
  Register #(.width(4), .trigger("falling")) register_3 (
    .D(controlled_buffer_4_out[3:0]), .Q(HEADX), .clk(IO_0_update));  // open: en, clr
  Register #(.width(4), .trigger("falling")) register_4 (
    .D(controlled_buffer_5_out[3:0]), .Q(HEADY), .clk(IO_0_update));  // open: en, clr
  assign controlled_buffer_5_out = T1 ? Coordinate : 8'bz;  // Controlled_Buffer controlled_buffer_5
  assign VEC = register_2_q ? 3'b011 : 3'bz;  // Controlled_Buffer controlled_buffer_6
  Decoder #(.select(2), .disabled(0)) decoder_1 (
    .out0(T1), .out1(T2), .out2(T3), .sel(counter_3_q), .en(IO_0_update));  // open: out3
  Counter #(.width(2), .max('h2), .trigger("falling")) counter_3 (
    .Q(counter_3_q), .clk(IO_0_update), .clr(IACK));  // open: load, D, count, carry
  Decoder #(.select(4), .disabled(0)) decoder_2 (
    .out0(decoder_2_out0[0]), .out1(decoder_2_out0[1]), .out2(decoder_2_out0[2]), .out3(decoder_2_out0[3]),
    .out4(decoder_2_out0[4]), .out5(decoder_2_out0[5]), .out6(decoder_2_out0[6]), .out7(decoder_2_out0[7]),
    .out8(decoder_2_out0[8]), .out9(decoder_2_out0[9]), .out10(decoder_2_out0[10]),
    .out11(decoder_2_out0[11]), .out12(decoder_2_out0[12]), .out13(decoder_2_out0[13]),
    .out14(decoder_2_out0[14]), .out15(decoder_2_out0[15]), .sel(HEADY));  // open: en
  assign DATA_2 = IO_0_Read ? {HEADY, HEADX} : 8'bz;  // Controlled_Buffer controlled_buffer_7
  assign controlled_buffer_8_out = T3 ? Coordinate : 8'bz;  // Controlled_Buffer controlled_buffer_8
  Multiplexer #(.width(4), .disabled(0)) multiplexer_2 (
    .in0(Free_X), .in1(HEADX), .out(multiplexer_2_out), .sel(Free_lock));  // open: en
  Multiplexer #(.width(16), .disabled(0)) multiplexer_3 (
    .in0(Free_Column), .in1(decoder_2_out0), .out(multiplexer_3_out), .sel(Free_lock));  // open: en
  or or_1 (update_screen, nor_1_out, IO_5_update);
  nor nor_1 (nor_1_out, not_3_out, T3);
  not not_3 (not_3_out, T3);
  Register #(.trigger("falling")) register_5 (
    .D(controlled_buffer_8_out), .Q(register_5_q), .clk(IO_0_update));  // open: en, clr
  Decoder #(.select(4), .disabled(0)) decoder_3 (
    .out0(decoder_3_out0[0]), .out1(decoder_3_out0[1]), .out2(decoder_3_out0[2]), .out3(decoder_3_out0[3]),
    .out4(decoder_3_out0[4]), .out5(decoder_3_out0[5]), .out6(decoder_3_out0[6]), .out7(decoder_3_out0[7]),
    .out8(decoder_3_out0[8]), .out9(decoder_3_out0[9]), .out10(decoder_3_out0[10]),
    .out11(decoder_3_out0[11]), .out12(decoder_3_out0[12]), .out13(decoder_3_out0[13]),
    .out14(decoder_3_out0[14]), .out15(decoder_3_out0[15]), .sel(register_5_q[7:4]), .en(T3));
  Demultiplexer #(.select(4), .width(16), .disabled(0)) demultiplexer_1 (
    .out0(demultiplexer_1_out0), .out1(demultiplexer_1_out1), .out2(demultiplexer_1_out2),
    .out3(demultiplexer_1_out3), .out4(demultiplexer_1_out4), .out5(demultiplexer_1_out5),
    .out6(demultiplexer_1_out6), .out7(demultiplexer_1_out7), .out8(demultiplexer_1_out8),
    .out9(demultiplexer_1_out9), .out10(demultiplexer_1_out10), .out11(demultiplexer_1_out11),
    .out12(demultiplexer_1_out12), .out13(demultiplexer_1_out13), .out14(demultiplexer_1_out14),
    .out15(demultiplexer_1_out15), .in(decoder_3_out0), .sel(register_5_q[3:0]), .en(Free_lock));
  assign controlled_buffer_9_out = IO_2_update ? DATA : 8'bz;  // Controlled_Buffer controlled_buffer_9
  J_K_Flip_Flop j_k_ff_1 (.J(IO_2_update), .clk(IO_2_update), .K(1'b0), .Q(j_k_ff_1_q));  // open: Qn, preset, en, reset
  Register #(.width(4), .trigger("falling")) register_6 (
    .D(controlled_buffer_9_out[3:0]), .Q(APPLEX), .clk(IO_2_update));  // open: en, clr
  Register #(.width(4), .trigger("falling")) register_7 (
    .D(controlled_buffer_9_out[7:4]), .Q(APPLEY), .clk(IO_2_update));  // open: en, clr
  assign enable_apple = Free_lock ? j_k_ff_1_q : 1'bz;  // Controlled_Buffer controlled_buffer_10
  capacitorModule__16x16 capacitormodule_16x16_1 (
    .B1(demultiplexer_1_out0), .B1_5(demultiplexer_1_out4), .B1_2(demultiplexer_1_out1),
    .B1_6(demultiplexer_1_out5), .B1_3(demultiplexer_1_out2), .B1_7(demultiplexer_1_out6),
    .B1_4(demultiplexer_1_out3), .B1_8(demultiplexer_1_out7), .B1_9(demultiplexer_1_out8),
    .B1_13(demultiplexer_1_out12), .B1_10(demultiplexer_1_out9), .B1_14(demultiplexer_1_out13),
    .B1_11(demultiplexer_1_out10), .B1_15(demultiplexer_1_out14), .B1_12(demultiplexer_1_out11),
    .B1_16(demultiplexer_1_out15), .TICK(update_screen), .C1(capacitormodule_16x16_1_c1),
    .C1_9(capacitormodule_16x16_1_c1_9), .C1_2(capacitormodule_16x16_1_c1_2),
    .C1_10(capacitormodule_16x16_1_c1_10), .C1_3(capacitormodule_16x16_1_c1_3),
    .C1_11(capacitormodule_16x16_1_c1_11), .C1_4(capacitormodule_16x16_1_c1_4),
    .C1_12(capacitormodule_16x16_1_c1_12), .C1_5(capacitormodule_16x16_1_c1_5),
    .C1_13(capacitormodule_16x16_1_c1_13), .C1_6(capacitormodule_16x16_1_c1_6),
    .C1_14(capacitormodule_16x16_1_c1_14), .C1_7(capacitormodule_16x16_1_c1_7),
    .C1_15(capacitormodule_16x16_1_c1_15), .C1_8(capacitormodule_16x16_1_c1_8),
    .C1_16(capacitormodule_16x16_1_c1_16), .A1(demultiplexer_2_out0), .A1_9(demultiplexer_2_out8),
    .A1_2(demultiplexer_2_out1), .A1_10(demultiplexer_2_out9), .A1_3(demultiplexer_2_out2),
    .A1_11(demultiplexer_2_out10), .A1_4(demultiplexer_2_out3), .A1_12(demultiplexer_2_out11),
    .A1_5(demultiplexer_2_out4), .A1_13(demultiplexer_2_out12), .A1_6(demultiplexer_2_out5),
    .A1_14(demultiplexer_2_out13), .A1_7(demultiplexer_2_out6), .A1_15(demultiplexer_2_out14),
    .A1_8(demultiplexer_2_out7), .A1_16(demultiplexer_2_out15), .to_Zero(restart_cap));
  Demultiplexer #(.select(4), .width(16), .disabled(0)) demultiplexer_2 (
    .out0(demultiplexer_2_out0), .out1(demultiplexer_2_out1), .out2(demultiplexer_2_out2),
    .out3(demultiplexer_2_out3), .out4(demultiplexer_2_out4), .out5(demultiplexer_2_out5),
    .out6(demultiplexer_2_out6), .out7(demultiplexer_2_out7), .out8(demultiplexer_2_out8),
    .out9(demultiplexer_2_out9), .out10(demultiplexer_2_out10), .out11(demultiplexer_2_out11),
    .out12(demultiplexer_2_out12), .out13(demultiplexer_2_out13), .out14(demultiplexer_2_out14),
    .out15(demultiplexer_2_out15), .in(multiplexer_3_out), .sel(multiplexer_2_out));  // open: en
  Demultiplexer #(.select(4), .disabled(0)) demultiplexer_3 (
    .out0(demultiplexer_3_out0[0]), .out1(demultiplexer_3_out0[1]), .out2(demultiplexer_3_out0[2]),
    .out3(demultiplexer_3_out0[3]), .out4(demultiplexer_3_out0[4]), .out5(demultiplexer_3_out0[5]),
    .out6(demultiplexer_3_out0[6]), .out7(demultiplexer_3_out0[7]), .out8(demultiplexer_3_out0[8]),
    .out9(demultiplexer_3_out0[9]), .out10(demultiplexer_3_out0[10]), .out11(demultiplexer_3_out0[11]),
    .out12(demultiplexer_3_out0[12]), .out13(demultiplexer_3_out0[13]), .out14(demultiplexer_3_out0[14]),
    .out15(demultiplexer_3_out0[15]), .in(pull_resistor_1_node), .sel(APPLEY));  // open: en
  Pull_Resistor #(.pull("X")) pull_resistor_1 (.node(pull_resistor_1_node));
  Demultiplexer #(.select(4), .width(16), .disabled(0)) demultiplexer_4 (
    .out0(demultiplexer_4_out0), .out1(demultiplexer_4_out1), .out2(demultiplexer_4_out2),
    .out3(demultiplexer_4_out3), .out4(demultiplexer_4_out4), .out5(demultiplexer_4_out5),
    .out6(demultiplexer_4_out6), .out7(demultiplexer_4_out7), .out8(demultiplexer_4_out8),
    .out9(demultiplexer_4_out9), .out10(demultiplexer_4_out10), .out11(demultiplexer_4_out11),
    .out12(demultiplexer_4_out12), .out13(demultiplexer_4_out13), .out14(demultiplexer_4_out14),
    .out15(demultiplexer_4_out15), .in(demultiplexer_3_out0), .sel(APPLEX), .en(enable_apple));
  bitExtender__16_32 bitextender_16_32_1 (.in_1(smallor_16_bit_1_out_3), .out_2(out_10));
  bitExtender__16_32 bitextender_16_32_2 (.in_1(smallor_16_bit_2_out_3), .out_2(out_11));
  bitExtender__16_32 bitextender_16_32_3 (.in_1(smallor_16_bit_3_out_3), .out_2(out_8));
  bitExtender__16_32 bitextender_16_32_4 (.in_1(smallor_16_bit_4_out_3), .out_2(out_9));
  smallOR__16_bit smallor_16_bit_1 (
    .in_1(capacitormodule_16x16_1_c1_3), .in_2(demultiplexer_4_out2), .out_3(smallor_16_bit_1_out_3));
  smallOR__16_bit smallor_16_bit_2 (
    .in_1(capacitormodule_16x16_1_c1_4), .in_2(demultiplexer_4_out3), .out_3(smallor_16_bit_2_out_3));
  smallOR__16_bit smallor_16_bit_3 (
    .in_1(capacitormodule_16x16_1_c1), .in_2(demultiplexer_4_out0), .out_3(smallor_16_bit_3_out_3));
  smallOR__16_bit smallor_16_bit_4 (
    .in_1(capacitormodule_16x16_1_c1_2), .in_2(demultiplexer_4_out1), .out_3(smallor_16_bit_4_out_3));
  bitExtender__16_32 bitextender_16_32_5 (.in_1(smallor_16_bit_8_out_3), .out_2(out_12));
  bitExtender__16_32 bitextender_16_32_6 (.in_1(smallor_16_bit_7_out_3), .out_2(out_14));
  bitExtender__16_32 bitextender_16_32_7 (.in_1(smallor_16_bit_6_out_3), .out_2(out_13));
  bitExtender__16_32 bitextender_16_32_8 (.in_1(smallor_16_bit_5_out_3), .out_2(out_15));
  smallOR__16_bit smallor_16_bit_5 (
    .in_1(capacitormodule_16x16_1_c1_8), .in_2(demultiplexer_4_out7), .out_3(smallor_16_bit_5_out_3));
  smallOR__16_bit smallor_16_bit_6 (
    .in_1(capacitormodule_16x16_1_c1_6), .in_2(demultiplexer_4_out5), .out_3(smallor_16_bit_6_out_3));
  smallOR__16_bit smallor_16_bit_7 (
    .in_1(capacitormodule_16x16_1_c1_7), .in_2(demultiplexer_4_out6), .out_3(smallor_16_bit_7_out_3));
  smallOR__16_bit smallor_16_bit_8 (
    .in_1(capacitormodule_16x16_1_c1_5), .in_2(demultiplexer_4_out4), .out_3(smallor_16_bit_8_out_3));
  bitExtender__16_32 bitextender_16_32_9 (.in_1(smallor_16_bit_10_out_3), .out_2(out_17));
  bitExtender__16_32 bitextender_16_32_10 (.in_1(smallor_16_bit_11_out_3), .out_2(out_19));
  bitExtender__16_32 bitextender_16_32_11 (.in_1(smallor_16_bit_9_out_3), .out_2(out_16));
  bitExtender__16_32 bitextender_16_32_12 (.in_1(smallor_16_bit_12_out_3), .out_2(out_18));
  smallOR__16_bit smallor_16_bit_9 (
    .in_1(capacitormodule_16x16_1_c1_9), .in_2(demultiplexer_4_out8), .out_3(smallor_16_bit_9_out_3));
  smallOR__16_bit smallor_16_bit_10 (
    .in_1(capacitormodule_16x16_1_c1_10), .in_2(demultiplexer_4_out9), .out_3(smallor_16_bit_10_out_3));
  smallOR__16_bit smallor_16_bit_11 (
    .in_1(capacitormodule_16x16_1_c1_12), .in_2(demultiplexer_4_out11), .out_3(smallor_16_bit_11_out_3));
  smallOR__16_bit smallor_16_bit_12 (
    .in_1(capacitormodule_16x16_1_c1_11), .in_2(demultiplexer_4_out10), .out_3(smallor_16_bit_12_out_3));
  bitExtender__16_32 bitextender_16_32_13 (.in_1(smallor_16_bit_15_out_3), .out_2(out_23));
  bitExtender__16_32 bitextender_16_32_14 (.in_1(smallor_16_bit_13_out_3), .out_2(out_21));
  bitExtender__16_32 bitextender_16_32_15 (.in_1(smallor_16_bit_14_out_3), .out_2(out_20));
  bitExtender__16_32 bitextender_16_32_16 (.in_1(smallor_16_bit_16_out_3), .out_2(out_22));
  smallOR__16_bit smallor_16_bit_13 (
    .in_1(capacitormodule_16x16_1_c1_14), .in_2(demultiplexer_4_out13), .out_3(smallor_16_bit_13_out_3));
  smallOR__16_bit smallor_16_bit_14 (
    .in_1(capacitormodule_16x16_1_c1_13), .in_2(demultiplexer_4_out12), .out_3(smallor_16_bit_14_out_3));
  smallOR__16_bit smallor_16_bit_15 (
    .in_1(capacitormodule_16x16_1_c1_16), .in_2(demultiplexer_4_out15), .out_3(smallor_16_bit_15_out_3));
  smallOR__16_bit smallor_16_bit_16 (
    .in_1(capacitormodule_16x16_1_c1_15), .in_2(demultiplexer_4_out14), .out_3(smallor_16_bit_16_out_3));

  // Other names for the same wires on the sheet: Preload_IMG[15:0] = Free_Column

  // Notes on the sheet:
  //   0 - "Lose"
  //   16 - "Win"
  //   Eat apple
  //   I/O interface
  //   Free draw block
  //   Preloaded images
  //   Disable other drawing devices
  //   contents of rom_1 (hex, n*v repeats v):
  //   0 1ff8 8 0 1ff8 1008 1ff8 0 f08 1088 1070 0 1ff8 1088 1008 0 0 ff8 4 7f8 4 ff8 0 bfc 0 ffc 400 380
  //   70 8 ffc
  //   Preloaded images
  //   Draw processor
  //   Interuptions
  //   Snake head
  //   Data out
  //   Selector
  //   Snake tail
  //   Screen update
  //   Apple draw
  //   Show apple
  //   To screen
endmodule

module keyboardChip (
  input  [2:0] ADDRESS,
  input  SEL,
  input  R_W,
  input  [3:0] Control,
  input  [7:0] DATA,
  output [7:0] DATA_2
);

  wire IO_3R, IO_3W, not_1_out, not_2_out, not_3_out, not_4_out, or_1_out, t1, t2, t3, t4;
  wire [1:0] selector;
  wire [3:0] controlled_buffer_8_out, Direction, Previous_Direction;
  wire [7:0] controlled_buffer_1_out, data_out, demultiplexer_1_out0, demultiplexer_1_out1,
       demultiplexer_1_out2, demultiplexer_1_out3, register_1_q, register_2_q, register_3_q, register_4_q;

  Demultiplexer #(.select(2), .width(8)) demultiplexer_1 (
    .out0(demultiplexer_1_out0), .out1(demultiplexer_1_out1), .out2(demultiplexer_1_out2),
    .out3(demultiplexer_1_out3), .in(controlled_buffer_1_out), .sel(selector), .en(IO_3W));
  assign controlled_buffer_1_out = IO_3W ? DATA : 8'bz;  // Controlled_Buffer controlled_buffer_1
  and u_IO_3R (IO_3R, R_W, SEL, ADDRESS[0], ADDRESS[1], ~ADDRESS[2]);  // AND_Gate
  and u_IO_3W (IO_3W, ~R_W, SEL, ADDRESS[0], ADDRESS[1], ~ADDRESS[2]);  // AND_Gate
  Decoder #(.select(2)) decoder_1 (.out0(t1), .out1(t2), .out2(t3), .out3(t4), .sel(selector), .en(IO_3W));
  Counter #(.width(2), .max('h3), .ongoal("stay"), .trigger("falling")) counter_1 (
    .Q(selector), .clk(IO_3W));  // open: load, D, count, carry, clr
  Register #(.trigger("high")) register_1 (.D(demultiplexer_1_out0), .Q(register_1_q), .clk(t1));  // open: en, clr
  Register #(.trigger("high")) register_2 (.D(demultiplexer_1_out1), .Q(register_2_q), .clk(t2));  // open: en, clr
  Register #(.trigger("high")) register_3 (.D(demultiplexer_1_out2), .Q(register_3_q), .clk(t3));  // open: en, clr
  Register #(.trigger("high")) register_4 (.D(demultiplexer_1_out3), .Q(register_4_q), .clk(t4));  // open: en, clr
  assign data_out = Direction[3] ? register_4_q : 8'bz;  // Controlled_Buffer controlled_buffer_2
  assign controlled_buffer_8_out[2] = not_1_out ? Control[2] : 1'bz;  // Controlled_Buffer controlled_buffer_3
  assign controlled_buffer_8_out[3] = not_2_out ? Control[3] : 1'bz;  // Controlled_Buffer controlled_buffer_4
  not not_1 (not_1_out, Previous_Direction[3]);
  not not_2 (not_2_out, Previous_Direction[2]);
  assign data_out = Direction[0] ? register_1_q : 8'bz;  // Controlled_Buffer controlled_buffer_5
  assign data_out = Direction[1] ? register_2_q : 8'bz;  // Controlled_Buffer controlled_buffer_6
  assign data_out = Direction[2] ? register_3_q : 8'bz;  // Controlled_Buffer controlled_buffer_7
  assign controlled_buffer_8_out[0] = not_3_out ? Control[0] : 1'bz;  // Controlled_Buffer controlled_buffer_8
  assign controlled_buffer_8_out[1] = not_4_out ? Control[1] : 1'bz;  // Controlled_Buffer controlled_buffer_9
  not not_3 (not_3_out, Previous_Direction[1]);
  not not_4 (not_4_out, Previous_Direction[0]);
  Pull_Resistor pull_resistor_1 (.node(data_out));
  assign DATA_2 = IO_3R ? data_out : 8'bz;  // Controlled_Buffer controlled_buffer_10
  Pull_Resistor pull_resistor_2 (.node(controlled_buffer_8_out[0]));
  Pull_Resistor pull_resistor_3 (.node(controlled_buffer_8_out[1]));
  Pull_Resistor pull_resistor_4 (.node(controlled_buffer_8_out[2]));
  Pull_Resistor pull_resistor_5 (.node(controlled_buffer_8_out[3]));
  or or_1 (or_1_out, controlled_buffer_8_out[0], controlled_buffer_8_out[1], controlled_buffer_8_out[2], controlled_buffer_8_out[3]);
  Register #(.width(4), .trigger("falling")) register_5 (
    .D(Direction), .Q(Previous_Direction), .clk(IO_3R));  // open: en, clr
  Register #(.width(4)) register_6 (.D(controlled_buffer_8_out), .Q(Direction), .clk(or_1_out));  // open: en, clr

  // Notes on the sheet:
  //   Address storage
  //   I/O interface
  //   LEFT
  //   RIGHT
  //   UP
  //   DOWN
  //   Key controller
endmodule

module randomGenChip (
  input  [2:0] ADDR,
  input  SEL,
  input  R_W,
  output [7:0] DATA
);

  wire IO_1R_out;
  wire [7:0] random_1_out;

  and IO_1R (IO_1R_out, R_W, SEL, ADDR[0], ~ADDR[1], ~ADDR[2]);  // AND_Gate
  Random random_1 (.clk(IO_1R_out), .out(random_1_out));  // open: next, clr
  assign DATA = IO_1R_out ? random_1_out : 8'bz;  // Controlled_Buffer controlled_buffer_1
endmodule

module scoreChip (
  input  [2:0] ADDRESS,
  input  SEL,
  input  R_W,
  input  [7:0] DATA,
  input  tck,
  output [7:0] to_Score_screen,
  output [7:0] DATA_2
);

  wire IO_4R_out, IO_4W_out;
  wire [7:0] controlled_buffer_1_out, Score_q;

  and IO_4W (IO_4W_out, ~R_W, SEL, ~ADDRESS[0], ~ADDRESS[1], ADDRESS[2]);  // AND_Gate
  assign controlled_buffer_1_out = IO_4W_out ? DATA : 8'bz;  // Controlled_Buffer controlled_buffer_1
  and IO_4R (IO_4R_out, R_W, SEL, ~ADDRESS[0], ~ADDRESS[1], ADDRESS[2]);  // AND_Gate
  Register #(.trigger("falling")) Score (.D(controlled_buffer_1_out), .Q(Score_q), .clk(tck));  // open: en, clr
  assign DATA_2 = IO_4R_out ? Score_q : 8'bz;  // Controlled_Buffer controlled_buffer_2
  inc inc_1 (.in(Score_q), .out(to_Score_screen), .\disable (1'b1));
endmodule

module capacitorModule__16x16 (
  input  [15:0] A1,
  input  [15:0] A1_2,
  input  [15:0] A1_3,
  input  [15:0] A1_4,
  input  [15:0] A1_5,
  input  [15:0] A1_6,
  input  [15:0] A1_7,
  input  [15:0] A1_8,
  input  [15:0] B1,
  input  [15:0] B1_2,
  input  [15:0] B1_3,
  input  [15:0] B1_4,
  input  [15:0] B1_5,
  input  [15:0] B1_6,
  input  [15:0] B1_7,
  input  [15:0] B1_8,
  input  to_Zero,
  input  TICK,
  input  [15:0] A1_9,
  input  [15:0] A1_10,
  input  [15:0] A1_11,
  input  [15:0] A1_12,
  input  [15:0] A1_13,
  input  [15:0] A1_14,
  input  [15:0] A1_15,
  input  [15:0] A1_16,
  input  [15:0] B1_9,
  input  [15:0] B1_10,
  input  [15:0] B1_11,
  input  [15:0] B1_12,
  input  [15:0] B1_13,
  input  [15:0] B1_14,
  input  [15:0] B1_15,
  input  [15:0] B1_16,
  output [15:0] C1,
  output [15:0] C1_2,
  output [15:0] C1_3,
  output [15:0] C1_4,
  output [15:0] C1_5,
  output [15:0] C1_6,
  output [15:0] C1_7,
  output [15:0] C1_8,
  output [15:0] C1_9,
  output [15:0] C1_10,
  output [15:0] C1_11,
  output [15:0] C1_12,
  output [15:0] C1_13,
  output [15:0] C1_14,
  output [15:0] C1_15,
  output [15:0] C1_16
);

  CapacitorElement capacitorelement_1 (.NewValue(A1), .Out_Value(C1), .DeleteValue(B1), .CLOCK(TICK), .ZERO(to_Zero));
  CapacitorElement capacitorelement_2 (
    .NewValue(A1_9), .Out_Value(C1_9), .DeleteValue(B1_9), .CLOCK(TICK), .ZERO(to_Zero));
  CapacitorElement capacitorelement_3 (
    .NewValue(A1_2), .Out_Value(C1_2), .DeleteValue(B1_2), .CLOCK(TICK), .ZERO(to_Zero));
  CapacitorElement capacitorelement_4 (
    .NewValue(A1_10), .Out_Value(C1_10), .DeleteValue(B1_10), .CLOCK(TICK), .ZERO(to_Zero));
  CapacitorElement capacitorelement_5 (
    .NewValue(A1_3), .Out_Value(C1_3), .DeleteValue(B1_3), .CLOCK(TICK), .ZERO(to_Zero));
  CapacitorElement capacitorelement_6 (
    .NewValue(A1_11), .Out_Value(C1_11), .DeleteValue(B1_11), .CLOCK(TICK), .ZERO(to_Zero));
  CapacitorElement capacitorelement_7 (
    .NewValue(A1_4), .Out_Value(C1_4), .DeleteValue(B1_4), .CLOCK(TICK), .ZERO(to_Zero));
  CapacitorElement capacitorelement_8 (
    .NewValue(A1_12), .Out_Value(C1_12), .DeleteValue(B1_12), .CLOCK(TICK), .ZERO(to_Zero));
  CapacitorElement capacitorelement_9 (
    .NewValue(A1_5), .Out_Value(C1_5), .DeleteValue(B1_5), .CLOCK(TICK), .ZERO(to_Zero));
  CapacitorElement capacitorelement_10 (
    .NewValue(A1_13), .Out_Value(C1_13), .DeleteValue(B1_13), .CLOCK(TICK), .ZERO(to_Zero));
  CapacitorElement capacitorelement_11 (
    .NewValue(A1_6), .Out_Value(C1_6), .DeleteValue(B1_6), .CLOCK(TICK), .ZERO(to_Zero));
  CapacitorElement capacitorelement_12 (
    .NewValue(A1_14), .Out_Value(C1_14), .DeleteValue(B1_14), .CLOCK(TICK), .ZERO(to_Zero));
  CapacitorElement capacitorelement_13 (
    .NewValue(A1_7), .Out_Value(C1_7), .DeleteValue(B1_7), .CLOCK(TICK), .ZERO(to_Zero));
  CapacitorElement capacitorelement_14 (
    .NewValue(A1_15), .Out_Value(C1_15), .DeleteValue(B1_15), .CLOCK(TICK), .ZERO(to_Zero));
  CapacitorElement capacitorelement_15 (
    .NewValue(A1_8), .Out_Value(C1_8), .DeleteValue(B1_8), .CLOCK(TICK), .ZERO(to_Zero));
  CapacitorElement capacitorelement_16 (
    .NewValue(A1_16), .Out_Value(C1_16), .DeleteValue(B1_16), .CLOCK(TICK), .ZERO(to_Zero));

  // Other names for the same wires on the sheet: zero = to_Zero
endmodule

module CapacitorElement (
  input  [15:0] NewValue,
  input  CLOCK,
  input  ZERO,
  input  [15:0] DeleteValue,
  output [15:0] Out_Value
);

  wire [15:0] and_1_out, or_1_out;

  assign and_1_out = ~DeleteValue & Out_Value;  // AND_Gate and_1, 16 bits wide
  assign or_1_out = NewValue | and_1_out;  // OR_Gate or_1, 16 bits wide
  Register #(.width(16)) register_1 (.D(or_1_out), .Q(Out_Value), .clk(CLOCK), .clr(ZERO));  // open: en
endmodule
