// Logisim project additional.circ as structural Verilog: 8 circuits, main circuit buttons
module buttons (
);

  wire D, L, or_1_out, R, U;
  wire [6:0] keyboard_1_data;
  wire [7:0] bit_extender_1_out;

  Button button_1 (.out(U));
  Button button_2 (.out(R));
  Button button_3 (.out(L));
  Button button_4 (.out(D));
  Keyboard keyboard_1 (.clk(or_1_out), .data(keyboard_1_data));  // open: re, clr, avail
  or or_1 (or_1_out, L, R, D, U);
  assign bit_extender_1_out = {{1{1'b0}}, keyboard_1_data};  // Bit_Extender bit_extender_1
  Comparator comparator_1 (.a(bit_extender_1_out), .b(8'h61), .eq(L));  // open: gt, lt
  Comparator comparator_2 (.a(bit_extender_1_out), .b(8'h64), .eq(R));  // open: gt, lt
  Comparator comparator_3 (.a(bit_extender_1_out), .b(8'h77), .eq(U));  // open: gt, lt
  Comparator comparator_4 (.a(bit_extender_1_out), .b(8'h73), .eq(D));  // open: gt, lt
endmodule

module bitExtender__1_2 (
  input  in_1,
  output [1:0] out_2
);


  assign out_2 = {2{in_1}};
endmodule

module dec__5_bit (
  input  [4:0] in_1,
  output [4:0] out_2
);

  wire [4:1] or_1_out;
  wire [4:4] or_1_out_2;

  assign {or_1_out_2[4], or_1_out} = in_1 | {or_1_out, 1'b0};  // OR_Gate or_1, 5 bits wide
  assign out_2 = ~({or_1_out, 1'b0} ^ in_1);  // XNOR_Gate xnor_1, 5 bits wide
endmodule

module smallOR__16_bit (
  input  [15:0] in_1,
  input  [15:0] in_2,
  output [15:0] out_3
);

  assign out_3 = in_1 | in_2;  // OR_Gate or_1, 16 bits wide
endmodule

module bitReducer__16_1 (
  input  [15:0] in_1,
  output out_2
);

  wire or_1_out;

  assign out_2 = or_1_out ? or_1_out : 1'bz;  // Controlled_Buffer controlled_buffer_1
  or or_1 (or_1_out, in_1[8], in_1[15], in_1[14], in_1[13], in_1[12], in_1[11], in_1[10], in_1[9], in_1[7], in_1[6], in_1[5], in_1[4], in_1[3], in_1[2], in_1[1], in_1[0]);
endmodule

module bitExtender__16_32 (
  input  [15:0] in_1,
  output [31:0] out_2
);

  bitExtender__1_2 bitextender_1_2_1 (.in_1(in_1[0]), .out_2(out_2[1:0]));
  bitExtender__1_2 bitextender_1_2_2 (.in_1(in_1[1]), .out_2(out_2[3:2]));
  bitExtender__1_2 bitextender_1_2_3 (.in_1(in_1[2]), .out_2(out_2[5:4]));
  bitExtender__1_2 bitextender_1_2_4 (.in_1(in_1[3]), .out_2(out_2[7:6]));
  bitExtender__1_2 bitextender_1_2_5 (.in_1(in_1[4]), .out_2(out_2[9:8]));
  bitExtender__1_2 bitextender_1_2_6 (.in_1(in_1[5]), .out_2(out_2[11:10]));
  bitExtender__1_2 bitextender_1_2_7 (.in_1(in_1[6]), .out_2(out_2[13:12]));
  bitExtender__1_2 bitextender_1_2_8 (.in_1(in_1[7]), .out_2(out_2[15:14]));
  bitExtender__1_2 bitextender_1_2_9 (.in_1(in_1[8]), .out_2(out_2[17:16]));
  bitExtender__1_2 bitextender_1_2_10 (.in_1(in_1[9]), .out_2(out_2[19:18]));
  bitExtender__1_2 bitextender_1_2_11 (.in_1(in_1[10]), .out_2(out_2[21:20]));
  bitExtender__1_2 bitextender_1_2_12 (.in_1(in_1[11]), .out_2(out_2[23:22]));
  bitExtender__1_2 bitextender_1_2_13 (.in_1(in_1[12]), .out_2(out_2[25:24]));
  bitExtender__1_2 bitextender_1_2_14 (.in_1(in_1[13]), .out_2(out_2[27:26]));
  bitExtender__1_2 bitextender_1_2_15 (.in_1(in_1[14]), .out_2(out_2[29:28]));
  bitExtender__1_2 bitextender_1_2_16 (.in_1(in_1[15]), .out_2(out_2[31:30]));

  // Notes on the sheet:
  //   out_2: pull=down
endmodule

module ScoreDisplayDriver (
  input  [7:0] in_1,
  output [3:0] out_2,
  output [3:0] out_3
);

  wire [7:4] divider_1_out, divider_1_rem;

  Divider divider_1 (.a(in_1), .b(8'ha), .out({divider_1_out, out_2}), .rem({divider_1_rem, out_3}));  // open: upper
endmodule

module converter_coords__4bit__16bit (
  input  [3:0] in_1,
  output [15:0] out_2
);

  Decoder #(.select(4), .disabled(0)) decoder_1 (
    .out0(out_2[0]), .out1(out_2[1]), .out2(out_2[2]), .out3(out_2[3]), .out4(out_2[4]), .out5(out_2[5]),
    .out6(out_2[6]), .out7(out_2[7]), .out8(out_2[8]), .out9(out_2[9]), .out10(out_2[10]), .out11(out_2[11]),
    .out12(out_2[12]), .out13(out_2[13]), .out14(out_2[14]), .out15(out_2[15]), .sel(in_1));  // open: en
endmodule
