// Logisim project LSnakeProject (AI).circ as structural Verilog: 9 circuits, main circuit main
module main (
);

  wire and_1_out, bot_mem, cdm_8_mark5_1_data_inst, cdm_8_mark5_1_mem_cycle, code, data, IAck, IOsel, IRQ,
       keyboard_1_avail, main_mem, not_1_out, R_W, tck;
  wire [2:0] IOaddr, vec;
  wire [3:0] Direction, scoredisplaydriver_1_out_2, scoredisplaydriver_1_out_3, scoredisplaydriver_2_out_2,
       scoredisplaydriver_2_out_3;
  wire [6:0] keyboardButton;
  wire [7:0] BotScore, cdm_8_mark5_1_data_out, cdm_8_mark5_1_pc, cdm_8_mark5_1_ps, cdm_8_mark5_1_r0,
       cdm_8_mark5_1_r1, cdm_8_mark5_1_r2, cdm_8_mark5_1_r3, cdm_8_mark5_1_sp, controlled_buffer_2_out,
       IOdat, PlayerScore;
  wire [7:3] cdm_8_mark5_1_addr;
  wire [31:0] displaycontrollerchip_1_out_8, displaycontrollerchip_1_out_9, displaycontrollerchip_1_out_10,
       displaycontrollerchip_1_out_11, displaycontrollerchip_1_out_12, displaycontrollerchip_1_out_13,
       displaycontrollerchip_1_out_14, displaycontrollerchip_1_out_15, displaycontrollerchip_1_out_16,
       displaycontrollerchip_1_out_17, displaycontrollerchip_1_out_18, displaycontrollerchip_1_out_19,
       displaycontrollerchip_1_out_20, displaycontrollerchip_1_out_21, displaycontrollerchip_1_out_22,
       displaycontrollerchip_1_out_23;

  MemorySelector memoryselector_1 (
    .Sel(IOsel), .Addres(IOaddr), .Bot_memory(bot_mem), .Main_memory(main_mem), .Code(code));
  Pull_Resistor pull_resistor_1 (.node(IRQ));
  Pull_Resistor pull_resistor_2 (.node(code));
  Pull_Resistor pull_resistor_3 (.node(data));
  // Probe on cdm_8_mark5_1_r3
  // Probe on cdm_8_mark5_1_r2
  // Probe on cdm_8_mark5_1_r1
  // Probe on cdm_8_mark5_1_r0
  Clock clock_1 (.out(tck));
  // Probe on cdm_8_mark5_1_pc
  // Probe on cdm_8_mark5_1_sp
  // Probe on cdm_8_mark5_1_ps
  CdM_8_mark5 cdm_8_mark5_1 (
    .clock(tck), .addr({cdm_8_mark5_1_addr, IOaddr}), .mem_read(R_W), .mem_cycle(cdm_8_mark5_1_mem_cycle),
    .data_inst(cdm_8_mark5_1_data_inst), .data_out(cdm_8_mark5_1_data_out),
    .data_in(controlled_buffer_2_out), .r0(cdm_8_mark5_1_r0), .r1(cdm_8_mark5_1_r1), .r2(cdm_8_mark5_1_r2),
    .r3(cdm_8_mark5_1_r3), .PC(cdm_8_mark5_1_pc), .SP(cdm_8_mark5_1_sp), .PS(cdm_8_mark5_1_ps), .IAck(IAck),
    .IRQ(IRQ), .vec(vec));
  scoreChip scorechip_1 (
    .ADDRESS(IOaddr), .SEL(IOsel), .R_W(R_W), .DATA(IOdat), .DATA_2(IOdat), .to_Score_screen(PlayerScore),
    .to_Score_screen_2(BotScore));
  randomGenChip randomgenchip_1 (.ADDR(IOaddr), .SEL(IOsel), .R_W(R_W), .DATA(IOdat));
  keyboardChip keyboardchip_1 (
    .ADDRESS(IOaddr), .SEL(IOsel), .R_W(R_W), .DATA_2(IOdat), .DATA(IOdat), .Control(Direction));
  Decoder #(.disabled(0)) decoder_1 (
    .out0(code), .out1(data), .sel(cdm_8_mark5_1_data_inst), .en(cdm_8_mark5_1_mem_cycle));
  not not_1 (not_1_out, R_W);
  assign IOdat = not_1_out ? cdm_8_mark5_1_data_out : 8'bz;  // Controlled_Buffer controlled_buffer_1
  assign controlled_buffer_2_out = R_W ? IOdat : 8'bz;  // Controlled_Buffer controlled_buffer_2
  and and_1 (and_1_out, ~IOsel, data);  // AND_Gate
  Comparator #(.width(7)) comparator_1 (.a(keyboardButton), .b(7'b1100001), .eq(Direction[0]));  // open: gt, lt
  Comparator #(.width(7)) comparator_2 (.a(keyboardButton), .b(7'b1100100), .eq(Direction[1]));  // open: gt, lt
  Comparator #(.width(7)) comparator_3 (.a(keyboardButton), .b(7'b1110111), .eq(Direction[2]));  // open: gt, lt
  Comparator #(.width(7)) comparator_4 (.a(keyboardButton), .b(7'b1110011), .eq(Direction[3]));  // open: gt, lt
  and and_2 (IOsel, cdm_8_mark5_1_addr[3], cdm_8_mark5_1_addr[4], cdm_8_mark5_1_addr[5], cdm_8_mark5_1_addr[7], cdm_8_mark5_1_addr[6], data);
  ROM rom_1 (.addr({cdm_8_mark5_1_addr, IOaddr}), .data(IOdat), .sel(main_mem));
  ROM rom_2 (.addr({cdm_8_mark5_1_addr, IOaddr}), .data(IOdat), .sel(bot_mem));
  RAM ram_1 (.addr({cdm_8_mark5_1_addr, IOaddr}), .data(IOdat), .sel(and_1_out), .clk(tck), .ld(R_W));  // open: clr
  ScoreDisplayDriver scoredisplaydriver_1 (
    .in_1(PlayerScore), .out_2(scoredisplaydriver_1_out_2), .out_3(scoredisplaydriver_1_out_3));
  Hex_Digit_Display hex_digit_display_1 (.value(scoredisplaydriver_1_out_3));  // open: dp
  Hex_Digit_Display hex_digit_display_2 (.value(scoredisplaydriver_1_out_2));  // open: dp
  DotMatrix #(.matrixcols(32), .matrixrows(32), .persist(22)) dotmatrix_1 (
    .col0(displaycontrollerchip_1_out_8), .col1(displaycontrollerchip_1_out_8),
    .col2(displaycontrollerchip_1_out_9), .col3(displaycontrollerchip_1_out_9),
    .col4(displaycontrollerchip_1_out_10), .col5(displaycontrollerchip_1_out_10),
    .col6(displaycontrollerchip_1_out_11), .col7(displaycontrollerchip_1_out_11),
    .col8(displaycontrollerchip_1_out_12), .col9(displaycontrollerchip_1_out_12),
    .col10(displaycontrollerchip_1_out_13), .col11(displaycontrollerchip_1_out_13),
    .col12(displaycontrollerchip_1_out_14), .col13(displaycontrollerchip_1_out_14),
    .col14(displaycontrollerchip_1_out_15), .col15(displaycontrollerchip_1_out_15),
    .col16(displaycontrollerchip_1_out_16), .col17(displaycontrollerchip_1_out_16),
    .col18(displaycontrollerchip_1_out_17), .col19(displaycontrollerchip_1_out_17),
    .col20(displaycontrollerchip_1_out_18), .col21(displaycontrollerchip_1_out_18),
    .col22(displaycontrollerchip_1_out_19), .col23(displaycontrollerchip_1_out_19),
    .col24(displaycontrollerchip_1_out_20), .col25(displaycontrollerchip_1_out_20),
    .col26(displaycontrollerchip_1_out_21), .col27(displaycontrollerchip_1_out_21),
    .col28(displaycontrollerchip_1_out_22), .col29(displaycontrollerchip_1_out_22),
    .col30(displaycontrollerchip_1_out_23), .col31(displaycontrollerchip_1_out_23));
  displayControllerChip displaycontrollerchip_1 (
    .ADDRESS(IOaddr), .SEL(IOsel), .R_W(R_W), .DATA(IOdat), .out_17(displaycontrollerchip_1_out_17),
    .out_18(displaycontrollerchip_1_out_18), .out_19(displaycontrollerchip_1_out_19),
    .out_20(displaycontrollerchip_1_out_20), .out_21(displaycontrollerchip_1_out_21),
    .out_22(displaycontrollerchip_1_out_22), .out_23(displaycontrollerchip_1_out_23),
    .out_8(displaycontrollerchip_1_out_8), .out_9(displaycontrollerchip_1_out_9),
    .out_10(displaycontrollerchip_1_out_10), .out_11(displaycontrollerchip_1_out_11),
    .out_12(displaycontrollerchip_1_out_12), .out_13(displaycontrollerchip_1_out_13),
    .out_14(displaycontrollerchip_1_out_14), .out_15(displaycontrollerchip_1_out_15),
    .out_16(displaycontrollerchip_1_out_16), .IRQ(IRQ), .IACK(IAck), .VEC(vec), .TICK(tck), .DATA_2(IOdat));
  Keyboard keyboard_1 (.clk(keyboard_1_avail), .avail(keyboard_1_avail), .data(keyboardButton));  // open: re, clr
  // Probe on keyboardButton
  Hex_Digit_Display hex_digit_display_3 (.value(scoredisplaydriver_2_out_2));  // open: dp
  ScoreDisplayDriver scoredisplaydriver_2 (
    .in_1(BotScore), .out_2(scoredisplaydriver_2_out_2), .out_3(scoredisplaydriver_2_out_3));
  Hex_Digit_Display hex_digit_display_4 (.value(scoredisplaydriver_2_out_3));  // open: dp

  // Notes on the sheet:
  //   contents of rom_1 (hex, n*v repeats v):
  //   ee 6 d0 fe a1 0 cd 5f d0 f c0 d0 80 c0 d9 d0 fb d1 48 a1 d1 4d a1 d1 52 a1 d1 57 a1 d0 f8 d3 c8 d1 6
  //   ad a1 8f ad a1 d1 0 a1 d0 c3 d1 60 d2 66 a6 a1 8c d1 90 a1 d1 fb b4 0 e0 39 d6 80 d0 f8 d1 fb b5 c1
  //   d7 ee 41 d6 7a 8a ee 5a d6 7a 8e ee 5a d6 7a 8d ee 5a d6 7a 89 a1 a2 d3 c8 ad 8f ae d1 c3 b5 b7 a3
  //   b3 a7 89 d2 60 76 ea 73 d3 c5 bf 1e 9 d0 c3 a1 d0 f8 ee 2 d3 c9 be 8b bd d7 d0 f9 b1 8c a1 d0 c2 a1
  //   d7 d1 10 ee 8f d1 0 d0 fd a1 d3 10 a1 8b e1 94 d4 c0 c1 c2 d2 30 d6 80 d0 c5 b1 8d 76 e0 89 a1 d2 80
  //   59 d0 fc a1 c6 c5 c4 d9 57*0 ee 41 7*0 8d 1 99 1
  //   contents of rom_2 (hex, n*v repeats v):
  //   5*0 d0 c1 b1 d2 c2 ba d3 f 4e 79 e0 4e ea 2f 89 88 c0 d2 c7 bb c2 d2 8 6b c6 b8 7c c4 ed 49 ab b2 d3
  //   ff ae ad bf f e1 5f ee 49 8d 88 c0 d2 c7 bb c2 d2 4 6b c6 b8 7c c4 ed 49 ab b2 d3 ff ae ad bf f e1
  //   7b b2 8c a1 ee 98 d0 c0 b2 d1 c2 b5 d3 f0 4d 4*91 76 b1 ec 7b 8a 8c c0 d1 c7 b7 c1 d1 2 67 c5 b4 7c
  //   c4 ed 95 a7 b1 d3 ff ae ad bf f e1 2f ee 95 8e 8c c0 d1 c7 b7 c1 d1 1 67 c5 b4 7c c4 ed 95 a7 b1 d3
  //   ff ae ad bf f e1 13 b1 88 a2 d0 c7 3f a3 d0 f8 a2 a1 d1 c4 b5 b7 a3 b3 a7 89 d2 90 76 ea b2 d3 c6 bf
  //   1e 9 d0 c4 a1 d0 f8 ee e8 d0 f9 b1 8c a1 d0 c2 a1 d7 d1 0 ee c8 d1 10 d0 fd a1 d3 10 a1 8b e1 cd d4
  //   c0 c1 c2 d2 30 d6 b9 d0 c6 b1 8d 76 e0 c2 a1 d0 fc a1 c6 c5 c4 d9 d1 fe a5 9*0 c6 1 d2 1
endmodule

module displayControllerChip (
  input  [2:0] ADDRESS,
  input  SEL,
  input  R_W,
  input  [7:0] DATA,
  input  TICK,
  input  IACK,
  output [7:0] DATA_2,
  output [31:0] out_8,
  output [31:0] out_9,
  output [31:0] out_10,
  output [31:0] out_11,
  output [31:0] out_12,
  output [31:0] out_13,
  output [31:0] out_14,
  output [31:0] out_15,
  output [31:0] out_16,
  output [31:0] out_17,
  output [31:0] out_18,
  output [31:0] out_19,
  output [31:0] out_20,
  output [31:0] out_21,
  output [31:0] out_22,
  output [31:0] out_23,
  output IRQ,
  output [2:0] VEC
);

  wire and_2_out, comparator_1_eq, comparator_2_eq, controlled_buffer_1_out, controlled_inverter_1_out,
       counter_3_carry, d_ff_1_q, enable_apple, Free_lock, IO_0_Read, IO_0_update, IO_2_update, IO_5_update,
       IO_7_request, IO_7_send, j_k_ff_1_q, LoadImageNum, multiplexer_1_out, multiplexer_2_out, nor_1_out,
       not_1_out, not_2_out, not_3_out, or_1_out, or_2_out, pull_resistor_3_node, register_1_q, register_2_q,
       register_3_q, register_4_q, register_5_q, restart_cap, T1, T2, T3, tailBump, update_screen;
  wire [1:0] counter_4_q;
  wire [3:0] APPLEX, APPLEY, boteyes_1_rowselector, Free_X, HEADX, HEADY, multiplexer_3_out;
  wire [7:0] controlled_buffer_6_out, controlled_buffer_7_out, controlled_buffer_11_out,
       controlled_buffer_12_out, Coordinate, counter_1_q, pull_resistor_1_node, register_8_q;
  wire [15:0] capacitormodule_16x16_1_c1, capacitormodule_16x16_1_c1_2, capacitormodule_16x16_1_c1_3,
       capacitormodule_16x16_1_c1_4, capacitormodule_16x16_1_c1_5, capacitormodule_16x16_1_c1_6,
       capacitormodule_16x16_1_c1_7, capacitormodule_16x16_1_c1_8, capacitormodule_16x16_1_c1_9,
       capacitormodule_16x16_1_c1_10, capacitormodule_16x16_1_c1_11, capacitormodule_16x16_1_c1_12,
       capacitormodule_16x16_1_c1_13, capacitormodule_16x16_1_c1_14, capacitormodule_16x16_1_c1_15,
       capacitormodule_16x16_1_c1_16, decoder_2_out0, decoder_3_out0, demultiplexer_1_out0,
       demultiplexer_1_out1, demultiplexer_1_out2, demultiplexer_1_out3, demultiplexer_1_out4,
       demultiplexer_1_out5, demultiplexer_1_out6, demultiplexer_1_out7, demultiplexer_1_out8,
       demultiplexer_1_out9, demultiplexer_1_out10, demultiplexer_1_out11, demultiplexer_1_out12,
       demultiplexer_1_out13, demultiplexer_1_out14, demultiplexer_1_out15, demultiplexer_2_out0,
       demultiplexer_2_out1, demultiplexer_2_out2, demultiplexer_2_out3, demultiplexer_2_out4,
       demultiplexer_2_out5, demultiplexer_2_out6, demultiplexer_2_out7, demultiplexer_2_out8,
       demultiplexer_2_out9, demultiplexer_2_out10, demultiplexer_2_out11, demultiplexer_2_out12,
       demultiplexer_2_out13, demultiplexer_2_out14, demultiplexer_2_out15, demultiplexer_3_out0,
       demultiplexer_4_out0, demultiplexer_4_out1, demultiplexer_4_out2, demultiplexer_4_out3,
       demultiplexer_4_out4, demultiplexer_4_out5, demultiplexer_4_out6, demultiplexer_4_out7,
       demultiplexer_4_out8, demultiplexer_4_out9, demultiplexer_4_out10, demultiplexer_4_out11,
       demultiplexer_4_out12, demultiplexer_4_out13, demultiplexer_4_out14, demultiplexer_4_out15,
       Free_Column, multiplexer_4_out, multiplexer_5_out, smallor_16_bit_1_out_3, smallor_16_bit_2_out_3,
       smallor_16_bit_3_out_3, smallor_16_bit_4_out_3, smallor_16_bit_5_out_3, smallor_16_bit_6_out_3,
       smallor_16_bit_7_out_3, smallor_16_bit_8_out_3, smallor_16_bit_9_out_3, smallor_16_bit_10_out_3,
       smallor_16_bit_11_out_3, smallor_16_bit_12_out_3, smallor_16_bit_13_out_3, smallor_16_bit_14_out_3,
       smallor_16_bit_15_out_3, smallor_16_bit_16_out_3;

  D_Flip_Flop d_ff_1 (.clk(IO_5_update), .D(IO_5_update), .Q(d_ff_1_q), .Qn(Free_lock));  // open: preset, en, reset
  D_Flip_Flop #(.trigger("falling")) d_ff_2 (
    .clk(IO_5_update), .D(1'b1), .Qn(LoadImageNum));  // open: Q, preset, en, reset
  assign controlled_buffer_1_out = LoadImageNum ? 1'b1 : 1'bz;  // Controlled_Buffer controlled_buffer_1
  Counter #(.ongoal("stay"), .trigger("falling")) counter_1 (
    .load(controlled_buffer_1_out), .D(DATA), .count(controlled_inverter_1_out), .Q(counter_1_q),
    .clk(IO_5_update));  // open: carry, clr
  assign controlled_inverter_1_out = LoadImageNum ? ~1'b1 : 1'bz;  // Controlled_Inverter controlled_inverter_1
  Comparator #(.width(4), .mode("unsigned")) comparator_1 (
    .a(APPLEX), .b(HEADX), .eq(comparator_1_eq));  // open: gt, lt
  Comparator #(.width(4), .mode("unsigned")) comparator_2 (
    .a(APPLEY), .b(HEADY), .eq(comparator_2_eq));  // open: gt, lt
  Pull_Resistor pull_resistor_1 (.node(pull_resistor_1_node));
  assign pull_resistor_1_node = or_1_out ? Coordinate : 8'bz;  // Controlled_Buffer controlled_buffer_2
  or or_1 (or_1_out, T1, T2);
  and IO_0R (IO_0_Read, R_W, SEL, ~ADDRESS[0], ~ADDRESS[1], ~ADDRESS[2]);  // AND_Gate
  and IO_0W (IO_0_update, ~R_W, SEL, ~ADDRESS[0], ~ADDRESS[1], ~ADDRESS[2]);  // AND_Gate
  and IO_2W (IO_2_update, ~R_W, SEL, ~ADDRESS[0], ADDRESS[1], ~ADDRESS[2]);  // AND_Gate
  and IO_5W (IO_5_update, ~R_W, SEL, ADDRESS[0], ~ADDRESS[1], ADDRESS[2]);  // AND_Gate
  and IO_7R (IO_7_send, R_W, SEL, ADDRESS[0], ADDRESS[1], ADDRESS[2]);
  and IO_7W (IO_7_request, ~R_W, SEL, ADDRESS[0], ADDRESS[1], ADDRESS[2]);  // AND_Gate
  not not_1 (not_1_out, d_ff_1_q);
  not not_2 (not_2_out, Free_lock);
  Counter #(.width(4), .max('hf), .ongoal("stay"), .trigger("falling")) counter_2 (
    .load(LoadImageNum), .Q(Free_X), .clk(IO_5_update));  // open: D, count, carry, clr
  or or_2 (or_2_out, pull_resistor_1_node[4], pull_resistor_1_node[5], pull_resistor_1_node[6], pull_resistor_1_node[7], register_1_q);
  Register #(.width(1)) register_1 (.D(tailBump), .Q(register_1_q), .clk(update_screen), .clr(IACK));  // open: en
  and and_1 (restart_cap, not_1_out, d_ff_1_q);
  ROM #(.dataWidth(16)) rom_1 (.addr(counter_1_q), .data(Free_Column), .sel(not_2_out));
  Register #(.width(1)) register_2 (.D(and_2_out), .Q(register_2_q), .clk(update_screen), .clr(IACK));  // open: en
  and and_2 (and_2_out, comparator_1_eq, comparator_2_eq);
  Register #(.width(1), .trigger("high")) register_3 (
    .D(or_2_out), .Q(register_3_q), .clk(or_2_out), .clr(counter_3_carry));  // open: en
  Counter #(.width(3), .max('h2), .ongoal("stay")) counter_3 (
    .count(IACK), .carry(counter_3_carry), .clk(TICK), .clr(counter_3_carry));  // open: load, D, Q
  Multiplexer #(.disabled(0)) multiplexer_1 (
    .in0(register_2_q), .in1(1'b0), .out(multiplexer_1_out), .sel(IACK), .en(enable_apple));
  Multiplexer #(.disabled(0)) multiplexer_2 (
    .in0(register_3_q), .in1(1'b0), .out(multiplexer_2_out), .sel(counter_3_carry), .en(enable_apple));
  Register #(.width(1)) register_4 (.D(multiplexer_1_out), .Q(register_4_q), .clk(TICK));  // open: en, clr
  Register #(.width(1)) register_5 (.D(multiplexer_2_out), .Q(register_5_q), .clk(TICK));  // open: en, clr
  assign Coordinate = IO_0_update ? DATA : 8'bz;  // Controlled_Buffer controlled_buffer_3
  assign IRQ = register_4_q ? 1'b1 : 1'bz;  // Controlled_Buffer controlled_buffer_4
  assign IRQ = register_5_q ? 1'b1 : 1'bz;  // Controlled_Buffer controlled_buffer_5
  Counter #(.width(2), .max('h2), .trigger("falling")) counter_4 (
    .Q(counter_4_q), .clk(IO_0_update), .clr(IACK));  // open: load, D, count, carry
  Decoder #(.select(2), .disabled(0)) decoder_1 (
    .out0(T1), .out1(T2), .out2(T3), .sel(counter_4_q), .en(IO_0_update));  // open: out3
  assign controlled_buffer_6_out = T2 ? Coordinate : 8'bz;  // Controlled_Buffer controlled_buffer_6
  Register #(.width(4), .trigger("falling")) register_6 (
    .D(controlled_buffer_6_out[3:0]), .Q(HEADX), .clk(IO_0_update));  // open: en, clr
  Register #(.width(4), .trigger("falling")) register_7 (
    .D(controlled_buffer_7_out[3:0]), .Q(HEADY), .clk(IO_0_update));  // open: en, clr
  assign controlled_buffer_7_out = T1 ? Coordinate : 8'bz;  // Controlled_Buffer controlled_buffer_7
  assign VEC = register_4_q ? 3'b011 : 3'bz;  // Controlled_Buffer controlled_buffer_8
  assign VEC = register_5_q ? 3'b010 : 3'bz;  // Controlled_Buffer controlled_buffer_9
  assign DATA_2 = IO_0_Read ? {HEADY, HEADX} : 8'bz;  // Controlled_Buffer controlled_buffer_10
  Decoder #(.select(4), .disabled(0)) decoder_2 (
    .out0(decoder_2_out0[0]), .out1(decoder_2_out0[1]), .out2(decoder_2_out0[2]), .out3(decoder_2_out0[3]),
    .out4(decoder_2_out0[4]), .out5(decoder_2_out0[5]), .out6(decoder_2_out0[6]), .out7(decoder_2_out0[7]),
    .out8(decoder_2_out0[8]), .out9(decoder_2_out0[9]), .out10(decoder_2_out0[10]),
    .out11(decoder_2_out0[11]), .out12(decoder_2_out0[12]), .out13(decoder_2_out0[13]),
    .out14(decoder_2_out0[14]), .out15(decoder_2_out0[15]), .sel(HEADY));  // open: en
  assign controlled_buffer_11_out = T3 ? Coordinate : 8'bz;  // Controlled_Buffer controlled_buffer_11
  Multiplexer #(.width(4), .disabled(0)) multiplexer_3 (
    .in0(Free_X), .in1(HEADX), .out(multiplexer_3_out), .sel(Free_lock));  // open: en
  Multiplexer #(.width(16), .disabled(0)) multiplexer_4 (
    .in0(Free_Column), .in1(decoder_2_out0), .out(multiplexer_4_out), .sel(Free_lock));  // open: en
  or or_3 (update_screen, nor_1_out, IO_5_update);
  nor nor_1 (nor_1_out, not_3_out, T3);
  not not_3 (not_3_out, T3);
  Register #(.trigger("falling")) register_8 (
    .D(controlled_buffer_11_out), .Q(register_8_q), .clk(IO_0_update));  // open: en, clr
  Decoder #(.select(4), .disabled(0)) decoder_3 (
    .out0(decoder_3_out0[0]), .out1(decoder_3_out0[1]), .out2(decoder_3_out0[2]), .out3(decoder_3_out0[3]),
    .out4(decoder_3_out0[4]), .out5(decoder_3_out0[5]), .out6(decoder_3_out0[6]), .out7(decoder_3_out0[7]),
    .out8(decoder_3_out0[8]), .out9(decoder_3_out0[9]), .out10(decoder_3_out0[10]),
    .out11(decoder_3_out0[11]), .out12(decoder_3_out0[12]), .out13(decoder_3_out0[13]),
    .out14(decoder_3_out0[14]), .out15(decoder_3_out0[15]), .sel(register_8_q[7:4]), .en(T3));
  Demultiplexer #(.select(4), .width(16), .disabled(0)) demultiplexer_1 (
    .out0(demultiplexer_1_out0), .out1(demultiplexer_1_out1), .out2(demultiplexer_1_out2),
    .out3(demultiplexer_1_out3), .out4(demultiplexer_1_out4), .out5(demultiplexer_1_out5),
    .out6(demultiplexer_1_out6), .out7(demultiplexer_1_out7), .out8(demultiplexer_1_out8),
    .out9(demultiplexer_1_out9), .out10(demultiplexer_1_out10), .out11(demultiplexer_1_out11),
    .out12(demultiplexer_1_out12), .out13(demultiplexer_1_out13), .out14(demultiplexer_1_out14),
    .out15(demultiplexer_1_out15), .in(decoder_3_out0), .sel(register_8_q[3:0]), .en(Free_lock));
  assign controlled_buffer_12_out = IO_2_update ? DATA : 8'bz;  // Controlled_Buffer controlled_buffer_12
  J_K_Flip_Flop j_k_ff_1 (.J(IO_2_update), .clk(IO_2_update), .K(1'b0), .Q(j_k_ff_1_q));  // open: Qn, preset, en, reset
  BotEyes boteyes_1 (
    .SEND(IO_7_send), .REQ(IO_7_request), .DATA(DATA), .DATA_2(DATA_2), .RowSelector(boteyes_1_rowselector),
    .DATA_FROM_SCREEN(multiplexer_5_out));
  Register #(.width(4), .trigger("falling")) register_9 (
    .D(controlled_buffer_12_out[3:0]), .Q(APPLEX), .clk(IO_2_update));  // open: en, clr
  Register #(.width(4), .trigger("falling")) register_10 (
    .D(controlled_buffer_12_out[7:4]), .Q(APPLEY), .clk(IO_2_update));  // open: en, clr
  Pull_Resistor pull_resistor_2 (.node(enable_apple));
  assign enable_apple = Free_lock ? j_k_ff_1_q : 1'bz;  // Controlled_Buffer controlled_buffer_13
  Multiplexer #(.select(4), .width(16), .disabled(0), .enable("false")) multiplexer_5 (
    .in0(capacitormodule_16x16_1_c1), .in1(capacitormodule_16x16_1_c1_2), .in2(capacitormodule_16x16_1_c1_3),
    .in3(capacitormodule_16x16_1_c1_4), .in4(capacitormodule_16x16_1_c1_5),
    .in5(capacitormodule_16x16_1_c1_6), .in6(capacitormodule_16x16_1_c1_7),
    .in7(capacitormodule_16x16_1_c1_8), .in8(capacitormodule_16x16_1_c1_9),
    .in9(capacitormodule_16x16_1_c1_10), .in10(capacitormodule_16x16_1_c1_11),
    .in11(capacitormodule_16x16_1_c1_12), .in12(capacitormodule_16x16_1_c1_13),
    .in13(capacitormodule_16x16_1_c1_14), .in14(capacitormodule_16x16_1_c1_15),
    .in15(capacitormodule_16x16_1_c1_16), .out(multiplexer_5_out), .sel(boteyes_1_rowselector));
  capacitorModule__16x16 capacitormodule_16x16_1 (
    .B1(demultiplexer_1_out0), .B1_5(demultiplexer_1_out4), .B1_2(demultiplexer_1_out1),
    .B1_6(demultiplexer_1_out5), .B1_3(demultiplexer_1_out2), .B1_7(demultiplexer_1_out6),
    .B1_4(demultiplexer_1_out3), .B1_8(demultiplexer_1_out7), .B1_9(demultiplexer_1_out8),
    .B1_13(demultiplexer_1_out12), .B1_10(demultiplexer_1_out9), .B1_14(demultiplexer_1_out13),
    .B1_11(demultiplexer_1_out10), .B1_15(demultiplexer_1_out14), .B1_12(demultiplexer_1_out11),
    .B1_16(demultiplexer_1_out15), .TICK(update_screen), .C1(capacitormodule_16x16_1_c1),
    .C1_9(capacitormodule_16x16_1_c1_9), .C1_2(capacitormodule_16x16_1_c1_2),
    .C1_10(capacitormodule_16x16_1_c1_10), .C1_3(capacitormodule_16x16_1_c1_3),
    .C1_11(capacitormodule_16x16_1_c1_11), .C1_4(capacitormodule_16x16_1_c1_4),
    .C1_12(capacitormodule_16x16_1_c1_12), .C1_5(capacitormodule_16x16_1_c1_5),
    .C1_13(capacitormodule_16x16_1_c1_13), .C1_6(capacitormodule_16x16_1_c1_6),
    .C1_14(capacitormodule_16x16_1_c1_14), .C1_7(capacitormodule_16x16_1_c1_7),
    .C1_15(capacitormodule_16x16_1_c1_15), .C1_8(capacitormodule_16x16_1_c1_8),
    .C1_16(capacitormodule_16x16_1_c1_16), .A1(demultiplexer_2_out0), .A1_9(demultiplexer_2_out8),
    .A1_2(demultiplexer_2_out1), .A1_10(demultiplexer_2_out9), .A1_3(demultiplexer_2_out2),
    .A1_11(demultiplexer_2_out10), .A1_4(demultiplexer_2_out3), .A1_12(demultiplexer_2_out11),
    .A1_5(demultiplexer_2_out4), .A1_13(demultiplexer_2_out12), .A1_6(demultiplexer_2_out5),
    .A1_14(demultiplexer_2_out13), .A1_7(demultiplexer_2_out6), .A1_15(demultiplexer_2_out14),
    .A1_8(demultiplexer_2_out7), .A1_16(demultiplexer_2_out15), .result(tailBump), .to_Zero(restart_cap));
  Demultiplexer #(.select(4), .width(16), .disabled(0)) demultiplexer_2 (
    .out0(demultiplexer_2_out0), .out1(demultiplexer_2_out1), .out2(demultiplexer_2_out2),
    .out3(demultiplexer_2_out3), .out4(demultiplexer_2_out4), .out5(demultiplexer_2_out5),
    .out6(demultiplexer_2_out6), .out7(demultiplexer_2_out7), .out8(demultiplexer_2_out8),
    .out9(demultiplexer_2_out9), .out10(demultiplexer_2_out10), .out11(demultiplexer_2_out11),
    .out12(demultiplexer_2_out12), .out13(demultiplexer_2_out13), .out14(demultiplexer_2_out14),
    .out15(demultiplexer_2_out15), .in(multiplexer_4_out), .sel(multiplexer_3_out));  // open: en
  Demultiplexer #(.select(4), .disabled(0)) demultiplexer_3 (
    .out0(demultiplexer_3_out0[0]), .out1(demultiplexer_3_out0[1]), .out2(demultiplexer_3_out0[2]),
    .out3(demultiplexer_3_out0[3]), .out4(demultiplexer_3_out0[4]), .out5(demultiplexer_3_out0[5]),
    .out6(demultiplexer_3_out0[6]), .out7(demultiplexer_3_out0[7]), .out8(demultiplexer_3_out0[8]),
    .out9(demultiplexer_3_out0[9]), .out10(demultiplexer_3_out0[10]), .out11(demultiplexer_3_out0[11]),
    .out12(demultiplexer_3_out0[12]), .out13(demultiplexer_3_out0[13]), .out14(demultiplexer_3_out0[14]),
    .out15(demultiplexer_3_out0[15]), .in(pull_resistor_3_node), .sel(APPLEY));  // open: en
  Pull_Resistor #(.pull("X")) pull_resistor_3 (.node(pull_resistor_3_node));
  Demultiplexer #(.select(4), .width(16), .disabled(0)) demultiplexer_4 (
    .out0(demultiplexer_4_out0), .out1(demultiplexer_4_out1), .out2(demultiplexer_4_out2),
    .out3(demultiplexer_4_out3), .out4(demultiplexer_4_out4), .out5(demultiplexer_4_out5),
    .out6(demultiplexer_4_out6), .out7(demultiplexer_4_out7), .out8(demultiplexer_4_out8),
    .out9(demultiplexer_4_out9), .out10(demultiplexer_4_out10), .out11(demultiplexer_4_out11),
    .out12(demultiplexer_4_out12), .out13(demultiplexer_4_out13), .out14(demultiplexer_4_out14),
    .out15(demultiplexer_4_out15), .in(demultiplexer_3_out0), .sel(APPLEX), .en(enable_apple));
  bitExtender__16_32 bitextender_16_32_1 (.in_1(smallor_16_bit_4_out_3), .out_2(out_9));
  bitExtender__16_32 bitextender_16_32_2 (.in_1(smallor_16_bit_1_out_3), .out_2(out_8));
  bitExtender__16_32 bitextender_16_32_3 (.in_1(smallor_16_bit_3_out_3), .out_2(out_10));
  bitExtender__16_32 bitextender_16_32_4 (.in_1(smallor_16_bit_2_out_3), .out_2(out_11));
  smallOR__16_bit smallor_16_bit_1 (
    .in_1(capacitormodule_16x16_1_c1), .in_2(demultiplexer_4_out0), .out_3(smallor_16_bit_1_out_3));
  smallOR__16_bit smallor_16_bit_2 (
    .in_1(capacitormodule_16x16_1_c1_4), .in_2(demultiplexer_4_out3), .out_3(smallor_16_bit_2_out_3));
  smallOR__16_bit smallor_16_bit_3 (
    .in_1(capacitormodule_16x16_1_c1_3), .in_2(demultiplexer_4_out2), .out_3(smallor_16_bit_3_out_3));
  smallOR__16_bit smallor_16_bit_4 (
    .in_1(capacitormodule_16x16_1_c1_2), .in_2(demultiplexer_4_out1), .out_3(smallor_16_bit_4_out_3));
  bitExtender__16_32 bitextender_16_32_5 (.in_1(smallor_16_bit_8_out_3), .out_2(out_13));
  bitExtender__16_32 bitextender_16_32_6 (.in_1(smallor_16_bit_5_out_3), .out_2(out_15));
  bitExtender__16_32 bitextender_16_32_7 (.in_1(smallor_16_bit_7_out_3), .out_2(out_14));
  bitExtender__16_32 bitextender_16_32_8 (.in_1(smallor_16_bit_6_out_3), .out_2(out_12));
  smallOR__16_bit smallor_16_bit_5 (
    .in_1(capacitormodule_16x16_1_c1_8), .in_2(demultiplexer_4_out7), .out_3(smallor_16_bit_5_out_3));
  smallOR__16_bit smallor_16_bit_6 (
    .in_1(capacitormodule_16x16_1_c1_5), .in_2(demultiplexer_4_out4), .out_3(smallor_16_bit_6_out_3));
  smallOR__16_bit smallor_16_bit_7 (
    .in_1(capacitormodule_16x16_1_c1_7), .in_2(demultiplexer_4_out6), .out_3(smallor_16_bit_7_out_3));
  smallOR__16_bit smallor_16_bit_8 (
    .in_1(capacitormodule_16x16_1_c1_6), .in_2(demultiplexer_4_out5), .out_3(smallor_16_bit_8_out_3));
  bitExtender__16_32 bitextender_16_32_9 (.in_1(smallor_16_bit_11_out_3), .out_2(out_18));
  bitExtender__16_32 bitextender_16_32_10 (.in_1(smallor_16_bit_9_out_3), .out_2(out_17));
  bitExtender__16_32 bitextender_16_32_11 (.in_1(smallor_16_bit_10_out_3), .out_2(out_19));
  bitExtender__16_32 bitextender_16_32_12 (.in_1(smallor_16_bit_12_out_3), .out_2(out_16));
  smallOR__16_bit smallor_16_bit_9 (
    .in_1(capacitormodule_16x16_1_c1_10), .in_2(demultiplexer_4_out9), .out_3(smallor_16_bit_9_out_3));
  smallOR__16_bit smallor_16_bit_10 (
    .in_1(capacitormodule_16x16_1_c1_12), .in_2(demultiplexer_4_out11), .out_3(smallor_16_bit_10_out_3));
  smallOR__16_bit smallor_16_bit_11 (
    .in_1(capacitormodule_16x16_1_c1_11), .in_2(demultiplexer_4_out10), .out_3(smallor_16_bit_11_out_3));
  smallOR__16_bit smallor_16_bit_12 (
    .in_1(capacitormodule_16x16_1_c1_9), .in_2(demultiplexer_4_out8), .out_3(smallor_16_bit_12_out_3));
  bitExtender__16_32 bitextender_16_32_13 (.in_1(smallor_16_bit_14_out_3), .out_2(out_21));
  bitExtender__16_32 bitextender_16_32_14 (.in_1(smallor_16_bit_16_out_3), .out_2(out_23));
  bitExtender__16_32 bitextender_16_32_15 (.in_1(smallor_16_bit_13_out_3), .out_2(out_22));
  bitExtender__16_32 bitextender_16_32_16 (.in_1(smallor_16_bit_15_out_3), .out_2(out_20));
  smallOR__16_bit smallor_16_bit_13 (
    .in_1(capacitormodule_16x16_1_c1_15), .in_2(demultiplexer_4_out14), .out_3(smallor_16_bit_13_out_3));
  smallOR__16_bit smallor_16_bit_14 (
    .in_1(capacitormodule_16x16_1_c1_14), .in_2(demultiplexer_4_out13), .out_3(smallor_16_bit_14_out_3));
  smallOR__16_bit smallor_16_bit_15 (
    .in_1(capacitormodule_16x16_1_c1_13), .in_2(demultiplexer_4_out12), .out_3(smallor_16_bit_15_out_3));
  smallOR__16_bit smallor_16_bit_16 (
    .in_1(capacitormodule_16x16_1_c1_16), .in_2(demultiplexer_4_out15), .out_3(smallor_16_bit_16_out_3));

  // Other names for the same wires on the sheet: DataOut[7:0] = DATA_2; Preload_IMG[15:0] = Free_Column

  // Notes on the sheet:
  //   0 - "Lose"
  //   16 - "Win"
  //   Eat apple
  //   Bump wall/tail
  //   I/O interface
  //   Free draw block
  //   Preloaded images
  //   Disable other drawing devices
  //   contents of rom_1 (hex, n*v repeats v):
  //   0 1ff8 8 0 1ff8 1008 1ff8 0 f08 1088 1070 0 1ff8 1088 1008 0 0 ff8 4 7f8 4 ff8 0 bfc 0 ffc 400 380
  //   70 8 ffc
  //   Preloaded images
  //   Draw processor
  //   Interuptions
  //   Snake head
  //   Data out
  //   Selector
  //   Snake tail
  //   Screen update
  //   Apple draw
  //   Show apple
  //   To screen
endmodule

module MemorySelector (
  input  Code,
  input  Sel,
  input  [2:0] Addres,
  output Bot_memory,
  output Main_memory
);

  wire IO_6W_out, t_ff_1_q, t_ff_1_qn;

  and IO_6W (IO_6W_out, Sel, ~Addres[0], Addres[1], Addres[2]);  // AND_Gate
  T_Flip_Flop t_ff_1 (.clk(IO_6W_out), .T(IO_6W_out), .Q(t_ff_1_q), .Qn(t_ff_1_qn));  // open: preset, reset, en
  and and_1 (Bot_memory, Code, t_ff_1_q);
  and and_2 (Main_memory, t_ff_1_qn, Code);
endmodule

module keyboardChip (
  input  [2:0] ADDRESS,
  input  SEL,
  input  R_W,
  input  [3:0] Control,
  input  [7:0] DATA,
  output [7:0] DATA_2
);

  wire IO_3R, IO_3W, or_1_out, t1, t2, t3, t4;
  wire [1:0] selector;
  wire [3:0] controlled_buffer_8_out, Direction, Previous_Direction, register_6_q;
  wire [7:0] controlled_buffer_1_out, data_out, demultiplexer_1_out0, demultiplexer_1_out1,
       demultiplexer_1_out2, demultiplexer_1_out3, register_1_q, register_2_q, register_3_q, register_4_q;

  Demultiplexer #(.select(2), .width(8)) demultiplexer_1 (
    .out0(demultiplexer_1_out0), .out1(demultiplexer_1_out1), .out2(demultiplexer_1_out2),
    .out3(demultiplexer_1_out3), .in(controlled_buffer_1_out), .sel(selector), .en(IO_3W));
  assign controlled_buffer_1_out = IO_3W ? DATA : 8'bz;  // Controlled_Buffer controlled_buffer_1
  and u_IO_3R (IO_3R, R_W, SEL, ADDRESS[0], ADDRESS[1], ~ADDRESS[2]);  // AND_Gate
  and u_IO_3W (IO_3W, ~R_W, SEL, ADDRESS[0], ADDRESS[1], ~ADDRESS[2]);  // AND_Gate
  Decoder #(.select(2)) decoder_1 (.out0(t1), .out1(t2), .out2(t3), .out3(t4), .sel(selector), .en(IO_3W));
  Counter #(.width(2), .max('h3), .ongoal("stay"), .trigger("falling")) counter_1 (
    .Q(selector), .clk(IO_3W));  // open: load, D, count, carry, clr
  Register #(.trigger("high")) register_1 (.D(demultiplexer_1_out0), .Q(register_1_q), .clk(t1));  // open: en, clr
  Register #(.trigger("high")) register_2 (.D(demultiplexer_1_out1), .Q(register_2_q), .clk(t2));  // open: en, clr
  Register #(.trigger("high")) register_3 (.D(demultiplexer_1_out2), .Q(register_3_q), .clk(t3));  // open: en, clr
  Register #(.trigger("high")) register_4 (.D(demultiplexer_1_out3), .Q(register_4_q), .clk(t4));  // open: en, clr
  assign data_out = Direction[3] ? register_4_q : 8'bz;  // Controlled_Buffer controlled_buffer_2
  assign controlled_buffer_8_out[2] = Previous_Direction[3] ? Control[2] : 1'bz;  // Controlled_Buffer controlled_buffer_3
  assign controlled_buffer_8_out[3] = Previous_Direction[2] ? Control[3] : 1'bz;  // Controlled_Buffer controlled_buffer_4
  assign data_out = Direction[0] ? register_1_q : 8'bz;  // Controlled_Buffer controlled_buffer_5
  assign data_out = Direction[1] ? register_2_q : 8'bz;  // Controlled_Buffer controlled_buffer_6
  assign data_out = Direction[2] ? register_3_q : 8'bz;  // Controlled_Buffer controlled_buffer_7
  assign controlled_buffer_8_out[0] = Previous_Direction[1] ? Control[0] : 1'bz;  // Controlled_Buffer controlled_buffer_8
  assign controlled_buffer_8_out[1] = Previous_Direction[0] ? Control[1] : 1'bz;  // Controlled_Buffer controlled_buffer_9
  Pull_Resistor pull_resistor_1 (.node(data_out));
  assign DATA_2 = IO_3R ? data_out : 8'bz;  // Controlled_Buffer controlled_buffer_10
  Pull_Resistor pull_resistor_2 (.node(controlled_buffer_8_out[0]));
  Pull_Resistor pull_resistor_3 (.node(controlled_buffer_8_out[1]));
  Pull_Resistor pull_resistor_4 (.node(controlled_buffer_8_out[2]));
  Pull_Resistor pull_resistor_5 (.node(controlled_buffer_8_out[3]));
  or or_1 (or_1_out, controlled_buffer_8_out[0], controlled_buffer_8_out[1], controlled_buffer_8_out[2], controlled_buffer_8_out[3]);
  Register #(.width(4)) register_5 (.D(controlled_buffer_8_out), .Q(Direction), .clk(or_1_out));  // open: en, clr
  Register #(.width(4), .trigger("falling")) register_6 (
    .D(Direction), .Q(register_6_q), .clk(IO_3R));  // open: en, clr
  assign Previous_Direction = ~register_6_q;  // NOT_Gate not_1, 4 bits wide

  // Notes on the sheet:
  //   Address storage
  //   I/O interface
  //   LEFT
  //   RIGHT
  //   UP
  //   DOWN
  //   Key controller
endmodule

module randomGenChip (
  input  [2:0] ADDR,
  input  SEL,
  input  R_W,
  output [7:0] DATA
);

  wire IO_1R_out;
  wire [7:0] random_1_out;

  and IO_1R (IO_1R_out, R_W, SEL, ADDR[0], ~ADDR[1], ~ADDR[2]);  // AND_Gate
  Random random_1 (.clk(IO_1R_out), .out(random_1_out));  // open: next, clr
  assign DATA = IO_1R_out ? random_1_out : 8'bz;  // Controlled_Buffer controlled_buffer_1
endmodule

module scoreChip (
  input  [2:0] ADDRESS,
  input  SEL,
  input  R_W,
  input  [7:0] DATA,
  output [7:0] to_Score_screen,
  output [7:0] to_Score_screen_2,
  output [7:0] DATA_2
);

  wire Bot, controlled_buffer_2_out, controlled_buffer_4_out, IO_4R_out, IO_4W_out, Player;
  wire [7:0] Bot_q, data_t, Player_q;

  Decoder #(.disabled(0)) decoder_1 (.out0(Bot), .out1(Player), .sel(data_t[7]));  // open: en
  Pull_Resistor pull_resistor_1 (.node(data_t[7]));
  assign data_t = IO_4W_out ? DATA : 8'bz;  // Controlled_Buffer controlled_buffer_1
  and IO_4W (IO_4W_out, ~R_W, SEL, ~ADDRESS[0], ~ADDRESS[1], ADDRESS[2]);  // AND_Gate
  and IO_4R (IO_4R_out, R_W, SEL, ~ADDRESS[0], ~ADDRESS[1], ADDRESS[2]);  // AND_Gate
  Register #(.trigger("high")) u_Player (
    .D({1'b0, data_t[6:0]}), .Q(Player_q), .clk(controlled_buffer_2_out));  // open: en, clr
  assign controlled_buffer_2_out = Player ? 1'b1 : 1'bz;  // Controlled_Buffer controlled_buffer_2
  assign DATA_2 = IO_4R_out ? Player_q : 8'bz;  // Controlled_Buffer controlled_buffer_3
  inc inc_1 (.in(Player_q), .out(to_Score_screen), .\disable (1'b1));
  Register #(.trigger("high")) u_Bot (.D(data_t), .Q(Bot_q), .clk(controlled_buffer_4_out));  // open: en, clr
  assign controlled_buffer_4_out = Bot ? 1'b1 : 1'bz;  // Controlled_Buffer controlled_buffer_4
  inc inc_2 (.in(Bot_q), .out(to_Score_screen_2), .\disable (1'b1));
endmodule

module BotEyes (
  input  SEND,
  input  REQ,
  input  [7:0] DATA,
  input  [15:0] DATA_FROM_SCREEN,
  output [7:0] DATA_2,
  output [3:0] RowSelector
);

  wire bitfinder_1_found, bitfinder_2_found, isBorder, j_k_ff_1_q, or_1_out, reset;
  wire [3:0] controlled_buffer_2_out, controlled_buffer_3_out, register_2_q;
  wire [7:0] STATE;
  wire [15:0] and_1_out, converter_coords_4bit_16bit_1_out_2;

  BitFinder #(.width(4)) bitfinder_1 (.in(DATA[7:4]), .found(bitfinder_1_found));  // open: index
  Register #(.width(1), .trigger("falling")) register_1 (
    .D(bitfinder_1_found), .Q(isBorder), .clk(REQ), .clr(reset));  // open: en
  assign DATA_2 = SEND ? STATE : 8'bz;  // Controlled_Buffer controlled_buffer_1
  Register #(.width(4), .trigger("falling")) register_2 (
    .D(controlled_buffer_2_out), .Q(register_2_q), .clk(REQ));  // open: en, clr
  assign controlled_buffer_2_out = j_k_ff_1_q ? DATA[3:0] : 4'bz;  // Controlled_Buffer controlled_buffer_2
  converter_coords__4bit__16bit converter_coords_4bit_16bit_1 (
    .in_1(register_2_q), .out_2(converter_coords_4bit_16bit_1_out_2));
  J_K_Flip_Flop j_k_ff_1 (.J(REQ), .clk(REQ), .K(REQ), .Q(j_k_ff_1_q), .Qn(reset));  // open: preset, en, reset
  Register #(.width(4), .trigger("falling")) register_3 (
    .D(controlled_buffer_3_out), .Q(RowSelector), .clk(REQ));  // open: en, clr
  assign controlled_buffer_3_out = reset ? DATA[3:0] : 4'bz;  // Controlled_Buffer controlled_buffer_3
  assign and_1_out = converter_coords_4bit_16bit_1_out_2 & DATA_FROM_SCREEN;  // AND_Gate and_1, 16 bits wide
  BitFinder #(.width(16)) bitfinder_2 (.in(and_1_out), .found(bitfinder_2_found));  // open: index
  or or_1 (or_1_out, bitfinder_2_found, isBorder);
  assign STATE = {{7{1'b0}}, or_1_out};  // Bit_Extender bit_extender_1

  // Other names for the same wires on the sheet: DATA_IN[7:0] = DATA; isBrd[3:0] = DATA[7:4]; RQ = REQ; SD = SEND

  // Notes on the sheet:
  //   Check for some elements
  //   on the screen
  //   Check for borders
endmodule

module capacitorModule__16x16 (
  input  [15:0] A1,
  input  [15:0] A1_2,
  input  [15:0] A1_3,
  input  [15:0] A1_4,
  input  [15:0] A1_5,
  input  [15:0] A1_6,
  input  [15:0] A1_7,
  input  [15:0] A1_8,
  input  [15:0] B1,
  input  [15:0] B1_2,
  input  [15:0] B1_3,
  input  [15:0] B1_4,
  input  [15:0] B1_5,
  input  [15:0] B1_6,
  input  [15:0] B1_7,
  input  [15:0] B1_8,
  input  to_Zero,
  input  TICK,
  input  [15:0] A1_9,
  input  [15:0] A1_10,
  input  [15:0] A1_11,
  input  [15:0] A1_12,
  input  [15:0] A1_13,
  input  [15:0] A1_14,
  input  [15:0] A1_15,
  input  [15:0] A1_16,
  input  [15:0] B1_9,
  input  [15:0] B1_10,
  input  [15:0] B1_11,
  input  [15:0] B1_12,
  input  [15:0] B1_13,
  input  [15:0] B1_14,
  input  [15:0] B1_15,
  input  [15:0] B1_16,
  output [15:0] C1,
  output [15:0] C1_2,
  output [15:0] C1_3,
  output [15:0] C1_4,
  output [15:0] C1_5,
  output [15:0] C1_6,
  output [15:0] C1_7,
  output [15:0] C1_8,
  output result,
  output [15:0] C1_9,
  output [15:0] C1_10,
  output [15:0] C1_11,
  output [15:0] C1_12,
  output [15:0] C1_13,
  output [15:0] C1_14,
  output [15:0] C1_15,
  output [15:0] C1_16
);

  Pull_Resistor pull_resistor_1 (.node(result));
  CapacitorElement capacitorelement_1 (
    .NewValue(A1), .Out_Value(C1), .Check(result), .DeleteValue(B1), .CLOCK(TICK), .ZERO(to_Zero));
  CapacitorElement capacitorelement_2 (
    .NewValue(A1_9), .Out_Value(C1_9), .Check(result), .DeleteValue(B1_9), .CLOCK(TICK), .ZERO(to_Zero));
  CapacitorElement capacitorelement_3 (
    .NewValue(A1_2), .Out_Value(C1_2), .Check(result), .DeleteValue(B1_2), .CLOCK(TICK), .ZERO(to_Zero));
  CapacitorElement capacitorelement_4 (
    .NewValue(A1_10), .Out_Value(C1_10), .Check(result), .DeleteValue(B1_10), .CLOCK(TICK), .ZERO(to_Zero));
  CapacitorElement capacitorelement_5 (
    .NewValue(A1_3), .Out_Value(C1_3), .Check(result), .DeleteValue(B1_3), .CLOCK(TICK), .ZERO(to_Zero));
  CapacitorElement capacitorelement_6 (
    .NewValue(A1_11), .Out_Value(C1_11), .Check(result), .DeleteValue(B1_11), .CLOCK(TICK), .ZERO(to_Zero));
  CapacitorElement capacitorelement_7 (
    .NewValue(A1_4), .Out_Value(C1_4), .Check(result), .DeleteValue(B1_4), .CLOCK(TICK), .ZERO(to_Zero));
  CapacitorElement capacitorelement_8 (
    .NewValue(A1_12), .Out_Value(C1_12), .Check(result), .DeleteValue(B1_12), .CLOCK(TICK), .ZERO(to_Zero));
  CapacitorElement capacitorelement_9 (
    .NewValue(A1_5), .Out_Value(C1_5), .Check(result), .DeleteValue(B1_5), .CLOCK(TICK), .ZERO(to_Zero));
  CapacitorElement capacitorelement_10 (
    .NewValue(A1_13), .Out_Value(C1_13), .Check(result), .DeleteValue(B1_13), .CLOCK(TICK), .ZERO(to_Zero));
  CapacitorElement capacitorelement_11 (
    .NewValue(A1_6), .Out_Value(C1_6), .Check(result), .DeleteValue(B1_6), .CLOCK(TICK), .ZERO(to_Zero));
  CapacitorElement capacitorelement_12 (
    .NewValue(A1_14), .Out_Value(C1_14), .Check(result), .DeleteValue(B1_14), .CLOCK(TICK), .ZERO(to_Zero));
  CapacitorElement capacitorelement_13 (
    .NewValue(A1_7), .Out_Value(C1_7), .Check(result), .DeleteValue(B1_7), .CLOCK(TICK), .ZERO(to_Zero));
  CapacitorElement capacitorelement_14 (
    .NewValue(A1_15), .Out_Value(C1_15), .Check(result), .DeleteValue(B1_15), .CLOCK(TICK), .ZERO(to_Zero));
  CapacitorElement capacitorelement_15 (
    .NewValue(A1_8), .Out_Value(C1_8), .Check(result), .DeleteValue(B1_8), .CLOCK(TICK), .ZERO(to_Zero));
  CapacitorElement capacitorelement_16 (
    .NewValue(A1_16), .Out_Value(C1_16), .Check(result), .DeleteValue(B1_16), .CLOCK(TICK), .ZERO(to_Zero));

  // Other names for the same wires on the sheet: res = result; zero = to_Zero
endmodule

module CapacitorElement (
  input  [15:0] NewValue,
  input  CLOCK,
  input  ZERO,
  input  [15:0] DeleteValue,
  output [15:0] Out_Value,
  output Check
);

  wire bitfinder_1_found;
  wire [15:0] and_1_out, and_2_out, or_1_out;

  assign and_1_out = NewValue & and_2_out;  // AND_Gate and_1, 16 bits wide
  BitFinder #(.width(16)) bitfinder_1 (.in(and_1_out), .found(bitfinder_1_found));  // open: index
  assign Check = bitfinder_1_found ? bitfinder_1_found : 1'bz;  // Controlled_Buffer controlled_buffer_1
  assign and_2_out = ~DeleteValue & Out_Value;  // AND_Gate and_2, 16 bits wide
  assign or_1_out = NewValue | and_2_out;  // OR_Gate or_1, 16 bits wide
  Register #(.width(16)) register_1 (.D(or_1_out), .Q(Out_Value), .clk(CLOCK), .clr(ZERO));  // open: en
endmodule
