// Logisim project SnakeProject (Lose Screen).circ as structural Verilog: 11 circuits, main circuit main
module main (
);

  wire and_2_out, ButtonPressed, cdm_8_mark5_1_data_inst, cdm_8_mark5_1_mem_cycle, D, decoder_1_out0,
       decoder_1_out1, IAck, IOsel, IRQ, L, not_1_out, R, READwrite, tick, U;
  wire [2:0] IOaddr, vec;
  wire [4:0] scorechip_1_out_6;
  wire [6:0] keyboardButton;
  wire [7:0] bit_extender_1_out, cdm_8_mark5_1_data_out, cdm_8_mark5_1_pc, cdm_8_mark5_1_ps,
       cdm_8_mark5_1_r0, cdm_8_mark5_1_r1, cdm_8_mark5_1_r2, cdm_8_mark5_1_r3, cdm_8_mark5_1_sp,
       controlled_buffer_2_out, IOdat;
  wire [7:3] cdm_8_mark5_1_addr;
  wire [31:0] displaycontrollerchip_1_out_7, displaycontrollerchip_1_out_8, displaycontrollerchip_1_out_9,
       displaycontrollerchip_1_out_10, displaycontrollerchip_1_out_11, displaycontrollerchip_1_out_12,
       displaycontrollerchip_1_out_13, displaycontrollerchip_1_out_14, displaycontrollerchip_1_out_15,
       displaycontrollerchip_1_out_16, displaycontrollerchip_1_out_17, displaycontrollerchip_1_out_18,
       displaycontrollerchip_1_out_19, displaycontrollerchip_1_out_20, displaycontrollerchip_1_out_21,
       displaycontrollerchip_1_out_22;

  Clock clock_1 (.out(tick));
  // Probe on cdm_8_mark5_1_r3
  // Probe on cdm_8_mark5_1_r2
  // Probe on cdm_8_mark5_1_r1
  // Probe on cdm_8_mark5_1_r0
  Pull_Resistor pull_resistor_1 (.node(IRQ));
  // Probe on cdm_8_mark5_1_ps
  // Probe on cdm_8_mark5_1_sp
  // Probe on cdm_8_mark5_1_pc
  CdM_8_mark5 cdm_8_mark5_1 (
    .clock(tick), .addr({cdm_8_mark5_1_addr, IOaddr}), .mem_read(READwrite),
    .mem_cycle(cdm_8_mark5_1_mem_cycle), .data_inst(cdm_8_mark5_1_data_inst),
    .data_out(cdm_8_mark5_1_data_out), .data_in(controlled_buffer_2_out), .r0(cdm_8_mark5_1_r0),
    .r1(cdm_8_mark5_1_r1), .r2(cdm_8_mark5_1_r2), .r3(cdm_8_mark5_1_r3), .PC(cdm_8_mark5_1_pc),
    .SP(cdm_8_mark5_1_sp), .PS(cdm_8_mark5_1_ps), .IAck(IAck), .IRQ(IRQ), .vec(vec));
  Decoder #(.disabled(0)) decoder_1 (
    .out0(decoder_1_out0), .out1(decoder_1_out1), .sel(cdm_8_mark5_1_data_inst), .en(cdm_8_mark5_1_mem_cycle));
  not not_1 (not_1_out, READwrite);
  assign IOdat = not_1_out ? cdm_8_mark5_1_data_out : 8'bz;  // Controlled_Buffer controlled_buffer_1
  assign controlled_buffer_2_out = READwrite ? IOdat : 8'bz;  // Controlled_Buffer controlled_buffer_2
  and and_1 (IOsel, cdm_8_mark5_1_addr[3], cdm_8_mark5_1_addr[4], cdm_8_mark5_1_addr[5], cdm_8_mark5_1_addr[7], cdm_8_mark5_1_addr[6], decoder_1_out1);
  Pull_Resistor pull_resistor_2 (.node(decoder_1_out0));
  and and_2 (and_2_out, decoder_1_out1, ~IOsel);  // AND_Gate
  Pull_Resistor pull_resistor_3 (.node(and_2_out));
  ROM rom_1 (.addr({cdm_8_mark5_1_addr, IOaddr}), .data(IOdat), .sel(decoder_1_out0));
  RAM ram_1 (
    .addr({cdm_8_mark5_1_addr, IOaddr}), .data(IOdat), .sel(and_2_out), .clk(tick), .ld(READwrite));  // open: clr
  randomGenChip randomgenchip_1 (.ADDR(IOaddr), .SEL(IOsel), .R_W(READwrite), .DATA(IOdat));
  tailChip tailchip_1 (
    .ADDRESS(IOaddr), .SEL(IOsel), .R_W(READwrite), .DATA(IOdat), .DATA_2(IOdat), .SCORE(scorechip_1_out_6),
    .IACK(IAck));
  DotMatrix #(.matrixcols(32), .matrixrows(32), .persist(25)) dotmatrix_1 (
    .col0(displaycontrollerchip_1_out_7), .col1(displaycontrollerchip_1_out_7),
    .col2(displaycontrollerchip_1_out_8), .col3(displaycontrollerchip_1_out_8),
    .col4(displaycontrollerchip_1_out_9), .col5(displaycontrollerchip_1_out_9),
    .col6(displaycontrollerchip_1_out_10), .col7(displaycontrollerchip_1_out_10),
    .col8(displaycontrollerchip_1_out_11), .col9(displaycontrollerchip_1_out_11),
    .col10(displaycontrollerchip_1_out_12), .col11(displaycontrollerchip_1_out_12),
    .col12(displaycontrollerchip_1_out_13), .col13(displaycontrollerchip_1_out_13),
    .col14(displaycontrollerchip_1_out_14), .col15(displaycontrollerchip_1_out_14),
    .col16(displaycontrollerchip_1_out_15), .col17(displaycontrollerchip_1_out_15),
    .col18(displaycontrollerchip_1_out_16), .col19(displaycontrollerchip_1_out_16),
    .col20(displaycontrollerchip_1_out_17), .col21(displaycontrollerchip_1_out_17),
    .col22(displaycontrollerchip_1_out_18), .col23(displaycontrollerchip_1_out_18),
    .col24(displaycontrollerchip_1_out_19), .col25(displaycontrollerchip_1_out_19),
    .col26(displaycontrollerchip_1_out_20), .col27(displaycontrollerchip_1_out_20),
    .col28(displaycontrollerchip_1_out_21), .col29(displaycontrollerchip_1_out_21),
    .col30(displaycontrollerchip_1_out_22), .col31(displaycontrollerchip_1_out_22));
  scoreChip scorechip_1 (
    .ADDRESS(IOaddr), .SEL(IOsel), .R_W(READwrite), .DATA(IOdat), .DATA_2(IOdat), .out_6(scorechip_1_out_6),
    .tick(tick));
  // Probe on scorechip_1_out_6
  displayControllerChip displaycontrollerchip_1 (
    .ADDRESS(IOaddr), .SEL(IOsel), .R_W(READwrite), .DATA(IOdat), .out_16(displaycontrollerchip_1_out_16),
    .out_17(displaycontrollerchip_1_out_17), .out_18(displaycontrollerchip_1_out_18),
    .out_19(displaycontrollerchip_1_out_19), .out_20(displaycontrollerchip_1_out_20),
    .out_21(displaycontrollerchip_1_out_21), .out_22(displaycontrollerchip_1_out_22),
    .out_7(displaycontrollerchip_1_out_7), .out_8(displaycontrollerchip_1_out_8),
    .out_9(displaycontrollerchip_1_out_9), .out_10(displaycontrollerchip_1_out_10),
    .out_11(displaycontrollerchip_1_out_11), .out_12(displaycontrollerchip_1_out_12),
    .out_13(displaycontrollerchip_1_out_13), .out_14(displaycontrollerchip_1_out_14),
    .out_15(displaycontrollerchip_1_out_15), .IRQ(IRQ), .IACK(IAck), .VEC(vec), .TICK(tick));
  Keyboard keyboard_1 (.clk(ButtonPressed), .data(keyboardButton));  // open: re, clr, avail
  keyboardChip keyboardchip_1 (
    .LEFT(L), .RIGHT(R), .UP(U), .DOWN(D), .ADDRESS(IOaddr), .SEL(IOsel), .R_W(READwrite), .DATA(IOdat),
    .DATAIN(IOdat));
  or or_1 (ButtonPressed, L, R, D, U);
  assign bit_extender_1_out = {{1{1'b0}}, keyboardButton};  // Bit_Extender bit_extender_1
  Comparator comparator_1 (.a(bit_extender_1_out), .b(8'h61), .eq(L));  // open: gt, lt
  Comparator comparator_2 (.a(bit_extender_1_out), .b(8'h64), .eq(R));  // open: gt, lt
  Comparator comparator_3 (.a(bit_extender_1_out), .b(8'h77), .eq(U));  // open: gt, lt
  Comparator comparator_4 (.a(bit_extender_1_out), .b(8'h73), .eq(D));  // open: gt, lt

  // Notes on the sheet:
  //   contents of rom_1 (hex, n*v repeats v):
  //   d1 80 31 e0 b cd cf d0 80 c0 d9 d0 fb d1 38 a1 d1 3d a1 d1 42 a1 d1 47 a1 d0 f8 d3 f0 d1 6 ad a1 8f
  //   ad a1 d1 0 a1 d1 fb b5 5 e0 27 d6 5d d0 f8 d1 fb b5 c1 d7 ee 31 d6 57 8a ee 4c d6 57 8e ee 4c d6 57
  //   8d ee 4c d6 57 89 ee 4c b3 a1 a2 a3 d3 f0 ad 8f ae ee 31 d3 f1 be 8b bd d7 d0 f9 b1 8c a1 d7 d0 fd
  //   d3 20 d2 d0 b9 a1 8e 8b e1 69 d4 c0 c1 d6 5d d0 fc b1 8d a1 c5 c4 d9 ee 50 92*0 44 6e 4a 88 4a 88 4a
  //   4e 4a 28 4a 28 64 ce 12*0 63 1 70 1
endmodule

module displayControllerChip (
  input  [2:0] ADDRESS,
  input  SEL,
  input  R_W,
  input  [7:0] DATA,
  input  TICK,
  input  IACK,
  output [31:0] out_7,
  output [31:0] out_8,
  output [31:0] out_9,
  output [31:0] out_10,
  output [31:0] out_11,
  output [31:0] out_12,
  output [31:0] out_13,
  output [31:0] out_14,
  output [31:0] out_15,
  output [31:0] out_16,
  output [31:0] out_17,
  output [31:0] out_18,
  output [31:0] out_19,
  output [31:0] out_20,
  output [31:0] out_21,
  output [31:0] out_22,
  output IRQ,
  output [2:0] VEC
);

  wire and_2_out, apple_eated, comparator_1_eq, comparator_2_eq, controlled_buffer_15_out, counter_3_carry,
       d_ff_1_q, enable_apple, IO_0_update, IO_2_update, IO_5_LOCK, IO_5_update, j_k_ff_1_q, j_k_ff_1_qn,
       multiplexer_2_out, nor_1_out, not_1_out, not_3_out, not_4_out, not_5_out, not_6_out, or_1_out,
       or_2_out, pull_resistor_2_node, pull_resistor_3_node, register_1_q, register_2_q, register_3_q,
       register_7_q, register_8_q, restart_cap, T1, T2, T3, tailBump, update_screen;
  wire [1:0] counter_1_q;
  wire [3:0] APPLEX, APPLEY, controlled_buffer_7_out, counter_4_q, HEADX, HEADY;
  wire [7:0] allCord, controlled_buffer_1_out, controlled_buffer_3_out, controlled_buffer_4_out,
       controlled_buffer_5_out, controlled_buffer_6_out, counter_2_q, DataF, register_4_q, register_11_q,
       register_12_q;
  wire [15:0] capacitormodule_16x16_1_c1, capacitormodule_16x16_1_c1_2, capacitormodule_16x16_1_c1_3,
       capacitormodule_16x16_1_c1_4, capacitormodule_16x16_1_c1_5, capacitormodule_16x16_1_c1_6,
       capacitormodule_16x16_1_c1_7, capacitormodule_16x16_1_c1_8, capacitormodule_16x16_1_c1_9,
       capacitormodule_16x16_1_c1_10, capacitormodule_16x16_1_c1_11, capacitormodule_16x16_1_c1_12,
       capacitormodule_16x16_1_c1_13, capacitormodule_16x16_1_c1_14, capacitormodule_16x16_1_c1_15,
       capacitormodule_16x16_1_c1_16, controlled_buffer_10_out, controlled_buffer_17_out, decoder_2_out0,
       decoder_3_out0, demultiplexer_1_out0, demultiplexer_1_out1, demultiplexer_1_out2,
       demultiplexer_1_out3, demultiplexer_1_out4, demultiplexer_1_out5, demultiplexer_1_out6,
       demultiplexer_1_out7, demultiplexer_1_out8, demultiplexer_1_out9, demultiplexer_1_out10,
       demultiplexer_1_out11, demultiplexer_1_out12, demultiplexer_1_out13, demultiplexer_1_out14,
       demultiplexer_1_out15, demultiplexer_2_out0, demultiplexer_3_out0, demultiplexer_3_out1,
       demultiplexer_3_out2, demultiplexer_3_out3, demultiplexer_3_out4, demultiplexer_3_out5,
       demultiplexer_3_out6, demultiplexer_3_out7, demultiplexer_3_out8, demultiplexer_3_out9,
       demultiplexer_3_out10, demultiplexer_3_out11, demultiplexer_3_out12, demultiplexer_3_out13,
       demultiplexer_3_out14, demultiplexer_3_out15, demultiplexer_4_out0, demultiplexer_4_out1,
       demultiplexer_4_out2, demultiplexer_4_out3, demultiplexer_4_out4, demultiplexer_4_out5,
       demultiplexer_4_out6, demultiplexer_4_out7, demultiplexer_4_out8, demultiplexer_4_out9,
       demultiplexer_4_out10, demultiplexer_4_out11, demultiplexer_4_out12, demultiplexer_4_out13,
       demultiplexer_4_out14, demultiplexer_4_out15, smallor_16bit_1_out_3, smallor_16bit_2_out_3,
       smallor_16bit_3_out_3, smallor_16bit_4_out_3, smallor_16bit_5_out_3, smallor_16bit_6_out_3,
       smallor_16bit_7_out_3, smallor_16bit_8_out_3, smallor_16bit_9_out_3, smallor_16bit_10_out_3,
       smallor_16bit_11_out_3, smallor_16bit_12_out_3, smallor_16bit_13_out_3, smallor_16bit_14_out_3,
       smallor_16bit_15_out_3, smallor_16bit_16_out_3;

  D_Flip_Flop d_ff_1 (.clk(IO_5_update), .D(IO_5_update), .Q(d_ff_1_q));  // open: Qn, preset, en, reset
  not not_1 (not_1_out, d_ff_1_q);
  and and_1 (restart_cap, not_1_out, d_ff_1_q);
  not not_2 (IO_5_LOCK, d_ff_1_q);
  Counter #(.width(2), .max('h2), .trigger("falling")) counter_1 (
    .Q(counter_1_q), .clk(IO_0_update), .clr(IACK));  // open: load, D, count, carry
  Decoder #(.select(2), .disabled(0)) decoder_1 (
    .out0(T1), .out1(T2), .out2(T3), .sel(counter_1_q), .en(IO_0_update));  // open: out3
  and IO_0W (IO_0_update, ~R_W, SEL, ~ADDRESS[0], ~ADDRESS[1], ~ADDRESS[2]);  // AND_Gate
  and IO_2W (IO_2_update, ~R_W, SEL, ~ADDRESS[0], ADDRESS[1], ~ADDRESS[2]);  // AND_Gate
  and IO_5W (IO_5_update, ~R_W, SEL, ADDRESS[0], ~ADDRESS[1], ADDRESS[2]);  // AND_Gate
  Counter #(.ongoal("stay")) counter_2 (.Q(counter_2_q), .clk(IO_5_update));  // open: load, D, count, carry, clr
  Comparator #(.width(4), .mode("unsigned")) comparator_1 (
    .a(APPLEX), .b(HEADX), .eq(comparator_1_eq));  // open: gt, lt
  Comparator #(.width(4), .mode("unsigned")) comparator_2 (
    .a(APPLEY), .b(HEADY), .eq(comparator_2_eq));  // open: gt, lt
  assign controlled_buffer_1_out = or_1_out ? allCord : 8'bz;  // Controlled_Buffer controlled_buffer_1
  Pull_Resistor pull_resistor_1 (.node(controlled_buffer_1_out));
  or or_1 (or_1_out, T1, T2);
  assign allCord = IO_0_update ? DATA : 8'bz;  // Controlled_Buffer controlled_buffer_2
  assign controlled_buffer_3_out = T1 ? allCord : 8'bz;  // Controlled_Buffer controlled_buffer_3
  not not_3 (not_3_out, IO_5_LOCK);
  Register #(.width(1)) register_1 (.D(tailBump), .Q(register_1_q), .clk(update_screen), .clr(IACK));  // open: en
  nor nor_1 (nor_1_out, not_4_out, T3);
  not not_4 (not_4_out, T3);
  assign controlled_buffer_4_out = T2 ? allCord : 8'bz;  // Controlled_Buffer controlled_buffer_4
  assign controlled_buffer_5_out = T3 ? allCord : 8'bz;  // Controlled_Buffer controlled_buffer_5
  ROM rom_1 (.addr(counter_2_q), .data(DataF), .sel(not_3_out));
  Register #(.width(1)) register_2 (.D(and_2_out), .Q(register_2_q), .clk(update_screen), .clr(IACK));  // open: en
  and and_2 (and_2_out, comparator_1_eq, comparator_2_eq);
  Register #(.width(1), .trigger("high")) register_3 (
    .D(or_2_out), .Q(register_3_q), .clk(or_2_out), .clr(counter_3_carry));  // open: en
  or or_2 (or_2_out, controlled_buffer_1_out[4], controlled_buffer_1_out[5], register_1_q, controlled_buffer_1_out[7], controlled_buffer_1_out[6]);
  Counter #(.width(3), .max('h7), .ongoal("stay")) counter_3 (
    .count(IACK), .carry(counter_3_carry), .clk(TICK), .clr(counter_3_carry));  // open: load, D, Q
  or or_3 (update_screen, nor_1_out, IO_5_update);
  Register #(.trigger("falling")) register_4 (
    .D(controlled_buffer_5_out), .Q(register_4_q), .clk(IO_0_update));  // open: en, clr
  Register #(.width(4), .trigger("falling")) register_5 (
    .D(controlled_buffer_4_out[3:0]), .Q(HEADX), .clk(IO_0_update));  // open: en, clr
  Register #(.width(4), .trigger("falling")) register_6 (
    .D(controlled_buffer_3_out[3:0]), .Q(HEADY), .clk(IO_0_update));  // open: en, clr
  Decoder #(.select(4), .disabled(0)) decoder_2 (
    .out0(decoder_2_out0[0]), .out1(decoder_2_out0[1]), .out2(decoder_2_out0[2]), .out3(decoder_2_out0[3]),
    .out4(decoder_2_out0[4]), .out5(decoder_2_out0[5]), .out6(decoder_2_out0[6]), .out7(decoder_2_out0[7]),
    .out8(decoder_2_out0[8]), .out9(decoder_2_out0[9]), .out10(decoder_2_out0[10]),
    .out11(decoder_2_out0[11]), .out12(decoder_2_out0[12]), .out13(decoder_2_out0[13]),
    .out14(decoder_2_out0[14]), .out15(decoder_2_out0[15]), .sel(HEADY), .en(IO_5_LOCK));
  Multiplexer #(.disabled(0)) multiplexer_1 (
    .in0(register_2_q), .in1(1'b0), .out(apple_eated), .sel(IACK), .en(enable_apple));
  Multiplexer multiplexer_2 (
    .in0(register_3_q), .in1(1'b0), .out(multiplexer_2_out), .sel(counter_3_carry), .en(enable_apple));
  assign controlled_buffer_6_out = IO_2_update ? DATA : 8'bz;  // Controlled_Buffer controlled_buffer_6
  Register #(.width(1)) register_7 (.D(apple_eated), .Q(register_7_q), .clk(TICK));  // open: en, clr
  Register #(.width(1)) register_8 (.D(multiplexer_2_out), .Q(register_8_q), .clk(TICK));  // open: en, clr
  assign controlled_buffer_7_out = IO_5_LOCK ? HEADX : 4'bz;  // Controlled_Buffer controlled_buffer_7
  J_K_Flip_Flop j_k_ff_1 (
    .J(IO_5_update), .clk(IO_5_update), .K(IO_5_update), .Q(j_k_ff_1_q), .Qn(j_k_ff_1_qn));  // open: preset, en, reset
  J_K_Flip_Flop j_k_ff_2 (
    .J(IO_2_update), .clk(IO_2_update), .K(1'b0), .Q(enable_apple));  // open: Qn, preset, en, reset
  assign IRQ = register_7_q ? 1'b1 : 1'bz;  // Controlled_Buffer controlled_buffer_8
  assign IRQ = register_8_q ? 1'b1 : 1'bz;  // Controlled_Buffer controlled_buffer_9
  Decoder #(.select(4), .disabled(0)) decoder_3 (
    .out0(decoder_3_out0[0]), .out1(decoder_3_out0[1]), .out2(decoder_3_out0[2]), .out3(decoder_3_out0[3]),
    .out4(decoder_3_out0[4]), .out5(decoder_3_out0[5]), .out6(decoder_3_out0[6]), .out7(decoder_3_out0[7]),
    .out8(decoder_3_out0[8]), .out9(decoder_3_out0[9]), .out10(decoder_3_out0[10]),
    .out11(decoder_3_out0[11]), .out12(decoder_3_out0[12]), .out13(decoder_3_out0[13]),
    .out14(decoder_3_out0[14]), .out15(decoder_3_out0[15]), .sel(register_4_q[7:4]), .en(IO_5_LOCK));
  Demultiplexer #(.select(4), .width(16), .disabled(0)) demultiplexer_1 (
    .out0(demultiplexer_1_out0), .out1(demultiplexer_1_out1), .out2(demultiplexer_1_out2),
    .out3(demultiplexer_1_out3), .out4(demultiplexer_1_out4), .out5(demultiplexer_1_out5),
    .out6(demultiplexer_1_out6), .out7(demultiplexer_1_out7), .out8(demultiplexer_1_out8),
    .out9(demultiplexer_1_out9), .out10(demultiplexer_1_out10), .out11(demultiplexer_1_out11),
    .out12(demultiplexer_1_out12), .out13(demultiplexer_1_out13), .out14(demultiplexer_1_out14),
    .out15(demultiplexer_1_out15), .in(decoder_3_out0), .sel(register_4_q[3:0]), .en(IO_5_LOCK));
  assign controlled_buffer_10_out = IO_5_LOCK ? decoder_2_out0 : 16'bz;  // Controlled_Buffer controlled_buffer_10
  assign controlled_buffer_7_out = not_5_out ? counter_4_q : 4'bz;  // Controlled_Buffer controlled_buffer_11
  not not_5 (not_5_out, IO_5_LOCK);
  Counter #(.width(4), .max('hf), .ongoal("stay"), .trigger("falling")) counter_4 (
    .Q(counter_4_q), .clk(j_k_ff_1_q));  // open: load, D, count, carry, clr
  Register #(.width(4), .trigger("falling")) register_9 (
    .D(controlled_buffer_6_out[3:0]), .Q(APPLEX), .clk(IO_2_update));  // open: en, clr
  Register #(.width(4), .trigger("falling")) register_10 (
    .D(controlled_buffer_6_out[7:4]), .Q(APPLEY), .clk(IO_2_update));  // open: en, clr
  Pull_Resistor #(.pull("X")) pull_resistor_2 (.node(pull_resistor_2_node));
  Demultiplexer #(.select(4), .disabled(0)) demultiplexer_2 (
    .out0(demultiplexer_2_out0[0]), .out1(demultiplexer_2_out0[1]), .out2(demultiplexer_2_out0[2]),
    .out3(demultiplexer_2_out0[3]), .out4(demultiplexer_2_out0[4]), .out5(demultiplexer_2_out0[5]),
    .out6(demultiplexer_2_out0[6]), .out7(demultiplexer_2_out0[7]), .out8(demultiplexer_2_out0[8]),
    .out9(demultiplexer_2_out0[9]), .out10(demultiplexer_2_out0[10]), .out11(demultiplexer_2_out0[11]),
    .out12(demultiplexer_2_out0[12]), .out13(demultiplexer_2_out0[13]), .out14(demultiplexer_2_out0[14]),
    .out15(demultiplexer_2_out0[15]), .in(pull_resistor_2_node), .sel(APPLEY));  // open: en
  assign VEC = register_7_q ? 3'b011 : 3'bz;  // Controlled_Buffer controlled_buffer_12
  assign VEC = register_8_q ? 3'b010 : 3'bz;  // Controlled_Buffer controlled_buffer_13
  Register #(.trigger("falling")) register_11 (
    .D(DataF), .Q(register_11_q), .clk(pull_resistor_3_node));  // open: en, clr
  Pull_Resistor pull_resistor_3 (.node(pull_resistor_3_node));
  assign pull_resistor_3_node = j_k_ff_1_q ? IO_5_update : 1'bz;  // Controlled_Buffer controlled_buffer_14
  Register #(.trigger("falling")) register_12 (
    .D(DataF), .Q(register_12_q), .clk(controlled_buffer_15_out));  // open: en, clr
  assign controlled_buffer_15_out = j_k_ff_1_qn ? IO_5_update : 1'bz;  // Controlled_Buffer controlled_buffer_15
  Pull_Resistor pull_resistor_4 (.node(controlled_buffer_15_out));
  Demultiplexer #(.select(4), .width(16), .disabled(0)) demultiplexer_3 (
    .out0(demultiplexer_3_out0), .out1(demultiplexer_3_out1), .out2(demultiplexer_3_out2),
    .out3(demultiplexer_3_out3), .out4(demultiplexer_3_out4), .out5(demultiplexer_3_out5),
    .out6(demultiplexer_3_out6), .out7(demultiplexer_3_out7), .out8(demultiplexer_3_out8),
    .out9(demultiplexer_3_out9), .out10(demultiplexer_3_out10), .out11(demultiplexer_3_out11),
    .out12(demultiplexer_3_out12), .out13(demultiplexer_3_out13), .out14(demultiplexer_3_out14),
    .out15(demultiplexer_3_out15), .in(demultiplexer_2_out0), .sel(APPLEX), .en(enable_apple));
  capacitorModule__16x16 capacitormodule_16x16_1 (
    .B1(demultiplexer_1_out0), .B1_2(demultiplexer_1_out4), .B1_3(demultiplexer_1_out1),
    .B1_4(demultiplexer_1_out5), .B1_5(demultiplexer_1_out2), .B1_6(demultiplexer_1_out6),
    .B1_7(demultiplexer_1_out3), .B1_8(demultiplexer_1_out7), .B1_9(demultiplexer_1_out8),
    .B1_10(demultiplexer_1_out12), .B1_11(demultiplexer_1_out9), .B1_12(demultiplexer_1_out13),
    .B1_13(demultiplexer_1_out10), .B1_14(demultiplexer_1_out14), .B1_15(demultiplexer_1_out11),
    .B1_16(demultiplexer_1_out15), .TICK(update_screen), .C1(capacitormodule_16x16_1_c1),
    .C1_9(capacitormodule_16x16_1_c1_9), .C1_2(capacitormodule_16x16_1_c1_2),
    .C1_10(capacitormodule_16x16_1_c1_10), .C1_3(capacitormodule_16x16_1_c1_3),
    .C1_11(capacitormodule_16x16_1_c1_11), .C1_4(capacitormodule_16x16_1_c1_4),
    .C1_12(capacitormodule_16x16_1_c1_12), .C1_5(capacitormodule_16x16_1_c1_5),
    .C1_13(capacitormodule_16x16_1_c1_13), .C1_6(capacitormodule_16x16_1_c1_6),
    .C1_14(capacitormodule_16x16_1_c1_14), .C1_7(capacitormodule_16x16_1_c1_7),
    .C1_15(capacitormodule_16x16_1_c1_15), .C1_8(capacitormodule_16x16_1_c1_8),
    .C1_16(capacitormodule_16x16_1_c1_16), .A1(demultiplexer_4_out0), .A1_9(demultiplexer_4_out8),
    .A1_3(demultiplexer_4_out1), .A1_11(demultiplexer_4_out9), .A1_5(demultiplexer_4_out2),
    .A1_13(demultiplexer_4_out10), .A1_7(demultiplexer_4_out3), .A1_15(demultiplexer_4_out11),
    .A1_2(demultiplexer_4_out4), .A1_10(demultiplexer_4_out12), .A1_4(demultiplexer_4_out5),
    .A1_12(demultiplexer_4_out13), .A1_6(demultiplexer_4_out6), .A1_14(demultiplexer_4_out14),
    .A1_8(demultiplexer_4_out7), .A1_16(demultiplexer_4_out15), .result(tailBump), .to_Zero(restart_cap));
  Demultiplexer #(.select(4), .width(16), .disabled(0)) demultiplexer_4 (
    .out0(demultiplexer_4_out0), .out1(demultiplexer_4_out1), .out2(demultiplexer_4_out2),
    .out3(demultiplexer_4_out3), .out4(demultiplexer_4_out4), .out5(demultiplexer_4_out5),
    .out6(demultiplexer_4_out6), .out7(demultiplexer_4_out7), .out8(demultiplexer_4_out8),
    .out9(demultiplexer_4_out9), .out10(demultiplexer_4_out10), .out11(demultiplexer_4_out11),
    .out12(demultiplexer_4_out12), .out13(demultiplexer_4_out13), .out14(demultiplexer_4_out14),
    .out15(demultiplexer_4_out15), .in(controlled_buffer_10_out), .sel(controlled_buffer_7_out));  // open: en
  assign controlled_buffer_10_out = not_6_out ? controlled_buffer_17_out : 16'bz;  // Controlled_Buffer controlled_buffer_16
  not not_6 (not_6_out, IO_5_LOCK);
  assign controlled_buffer_17_out = j_k_ff_1_q ? {register_12_q, register_11_q} : 16'bz;  // Controlled_Buffer controlled_buffer_17
  bitExtender__16_32 bitextender_16_32_1 (.in_1(smallor_16bit_4_out_3), .out_2(out_8));
  bitExtender__16_32 bitextender_16_32_2 (.in_1(smallor_16bit_1_out_3), .out_2(out_10));
  bitExtender__16_32 bitextender_16_32_3 (.in_1(smallor_16bit_2_out_3), .out_2(out_7));
  bitExtender__16_32 bitextender_16_32_4 (.in_1(smallor_16bit_3_out_3), .out_2(out_9));
  smallOR__16bit smallor_16bit_1 (
    .in_1(capacitormodule_16x16_1_c1_4), .in_2(demultiplexer_3_out3), .out_3(smallor_16bit_1_out_3));
  smallOR__16bit smallor_16bit_2 (
    .in_1(capacitormodule_16x16_1_c1), .in_2(demultiplexer_3_out0), .out_3(smallor_16bit_2_out_3));
  smallOR__16bit smallor_16bit_3 (
    .in_1(capacitormodule_16x16_1_c1_3), .in_2(demultiplexer_3_out2), .out_3(smallor_16bit_3_out_3));
  smallOR__16bit smallor_16bit_4 (
    .in_1(capacitormodule_16x16_1_c1_2), .in_2(demultiplexer_3_out1), .out_3(smallor_16bit_4_out_3));
  bitExtender__16_32 bitextender_16_32_5 (.in_1(smallor_16bit_6_out_3), .out_2(out_12));
  bitExtender__16_32 bitextender_16_32_6 (.in_1(smallor_16bit_5_out_3), .out_2(out_13));
  bitExtender__16_32 bitextender_16_32_7 (.in_1(smallor_16bit_8_out_3), .out_2(out_11));
  bitExtender__16_32 bitextender_16_32_8 (.in_1(smallor_16bit_7_out_3), .out_2(out_14));
  smallOR__16bit smallor_16bit_5 (
    .in_1(capacitormodule_16x16_1_c1_7), .in_2(demultiplexer_3_out6), .out_3(smallor_16bit_5_out_3));
  smallOR__16bit smallor_16bit_6 (
    .in_1(capacitormodule_16x16_1_c1_6), .in_2(demultiplexer_3_out5), .out_3(smallor_16bit_6_out_3));
  smallOR__16bit smallor_16bit_7 (
    .in_1(capacitormodule_16x16_1_c1_8), .in_2(demultiplexer_3_out7), .out_3(smallor_16bit_7_out_3));
  smallOR__16bit smallor_16bit_8 (
    .in_1(capacitormodule_16x16_1_c1_5), .in_2(demultiplexer_3_out4), .out_3(smallor_16bit_8_out_3));
  bitExtender__16_32 bitextender_16_32_9 (.in_1(smallor_16bit_9_out_3), .out_2(out_17));
  bitExtender__16_32 bitextender_16_32_10 (.in_1(smallor_16bit_12_out_3), .out_2(out_15));
  bitExtender__16_32 bitextender_16_32_11 (.in_1(smallor_16bit_11_out_3), .out_2(out_16));
  bitExtender__16_32 bitextender_16_32_12 (.in_1(smallor_16bit_10_out_3), .out_2(out_18));
  smallOR__16bit smallor_16bit_9 (
    .in_1(capacitormodule_16x16_1_c1_11), .in_2(demultiplexer_3_out10), .out_3(smallor_16bit_9_out_3));
  smallOR__16bit smallor_16bit_10 (
    .in_1(capacitormodule_16x16_1_c1_12), .in_2(demultiplexer_3_out11), .out_3(smallor_16bit_10_out_3));
  smallOR__16bit smallor_16bit_11 (
    .in_1(capacitormodule_16x16_1_c1_10), .in_2(demultiplexer_3_out9), .out_3(smallor_16bit_11_out_3));
  smallOR__16bit smallor_16bit_12 (
    .in_1(capacitormodule_16x16_1_c1_9), .in_2(demultiplexer_3_out8), .out_3(smallor_16bit_12_out_3));
  bitExtender__16_32 bitextender_16_32_13 (.in_1(smallor_16bit_14_out_3), .out_2(out_22));
  bitExtender__16_32 bitextender_16_32_14 (.in_1(smallor_16bit_15_out_3), .out_2(out_21));
  bitExtender__16_32 bitextender_16_32_15 (.in_1(smallor_16bit_16_out_3), .out_2(out_19));
  bitExtender__16_32 bitextender_16_32_16 (.in_1(smallor_16bit_13_out_3), .out_2(out_20));
  smallOR__16bit smallor_16bit_13 (
    .in_1(capacitormodule_16x16_1_c1_14), .in_2(demultiplexer_3_out13), .out_3(smallor_16bit_13_out_3));
  smallOR__16bit smallor_16bit_14 (
    .in_1(capacitormodule_16x16_1_c1_16), .in_2(demultiplexer_3_out15), .out_3(smallor_16bit_14_out_3));
  smallOR__16bit smallor_16bit_15 (
    .in_1(capacitormodule_16x16_1_c1_15), .in_2(demultiplexer_3_out14), .out_3(smallor_16bit_15_out_3));
  smallOR__16bit smallor_16bit_16 (
    .in_1(capacitormodule_16x16_1_c1_13), .in_2(demultiplexer_3_out12), .out_3(smallor_16bit_16_out_3));

  // Notes on the sheet:
  //   HEAD DRAW
  //   and TAIL END 
  //   APPLE
  //   FREE DRAW
  //   Lose text
  //   contents of rom_1 (hex, n*v repeats v):
  //   0 0 f f0 0 10 0 0 f f0 8 10 f f0 0 0 7 10 8 90 8 60 0 0 f f0 8 90 8 10 0 0 f0 0 0 0 10 f f0 106*0 8
  //   10 8 90 f f0 0 0 8 60 8 90 7 10 0 0 f f0 8 10 f f0 0 0 0 10 f f0
  //   Eat apple
  //   bump wall/tail
  //   APPLE DRAW
  //   off pixel
  //   Draw from free
  //   on pixel
endmodule

module keyboardChip (
  input  [2:0] ADDRESS,
  input  SEL,
  input  R_W,
  input  [7:0] DATAIN,
  input  LEFT,
  input  RIGHT,
  input  UP,
  input  DOWN,
  output [7:0] DATA
);

  wire IO_3R_update, IO_3W_update, not_1_out, not_2_out, not_3_out, not_4_out, or_1_out, t1, t2, t3, t4;
  wire [1:0] selector;
  wire [3:0] controlled_buffer_4_out, register_5_q, register_5_q_2, register_6_q, register_6_q_2;
  wire [7:0] controlled_buffer_1_out, controlled_buffer_6_out, demultiplexer_1_out0, demultiplexer_1_out1,
       demultiplexer_1_out2, demultiplexer_1_out3, register_1_q, register_2_q, register_3_q, register_4_q;

  assign controlled_buffer_1_out = IO_3W_update ? DATAIN : 8'bz;  // Controlled_Buffer controlled_buffer_1
  Demultiplexer #(.select(2), .width(8)) demultiplexer_1 (
    .out0(demultiplexer_1_out0), .out1(demultiplexer_1_out1), .out2(demultiplexer_1_out2),
    .out3(demultiplexer_1_out3), .in(controlled_buffer_1_out), .sel(selector), .en(IO_3W_update));
  assign controlled_buffer_4_out[2] = not_2_out ? UP : 1'bz;  // Controlled_Buffer controlled_buffer_2
  assign controlled_buffer_4_out[3] = not_1_out ? DOWN : 1'bz;  // Controlled_Buffer controlled_buffer_3
  not not_1 (not_1_out, register_6_q[2]);
  not not_2 (not_2_out, register_6_q[3]);
  Decoder #(.select(2)) decoder_1 (.out0(t1), .out1(t2), .out2(t3), .out3(t4), .sel(selector), .en(IO_3W_update));
  assign controlled_buffer_4_out[0] = not_4_out ? LEFT : 1'bz;  // Controlled_Buffer controlled_buffer_4
  Pull_Resistor pull_resistor_1 (.node(controlled_buffer_4_out[0]));
  assign controlled_buffer_4_out[1] = not_3_out ? RIGHT : 1'bz;  // Controlled_Buffer controlled_buffer_5
  Pull_Resistor pull_resistor_2 (.node(controlled_buffer_4_out[1]));
  Pull_Resistor pull_resistor_3 (.node(controlled_buffer_4_out[2]));
  Pull_Resistor pull_resistor_4 (.node(controlled_buffer_4_out[3]));
  not not_3 (not_3_out, register_6_q[0]);
  not not_4 (not_4_out, register_6_q[1]);
  and IO_3R (IO_3R_update, R_W, SEL, ADDRESS[0], ADDRESS[1], ~ADDRESS[2]);  // AND_Gate
  and IO_3W (IO_3W_update, ~R_W, SEL, ADDRESS[0], ADDRESS[1], ~ADDRESS[2]);  // AND_Gate
  Counter #(.width(2), .max('h3), .ongoal("stay"), .trigger("falling")) counter_1 (
    .Q(selector), .clk(IO_3W_update));  // open: load, D, count, carry, clr
  Register #(.trigger("high")) register_1 (.D(demultiplexer_1_out0), .Q(register_1_q), .clk(t1));  // open: en, clr
  Register #(.trigger("high")) register_2 (.D(demultiplexer_1_out1), .Q(register_2_q), .clk(t2));  // open: en, clr
  Register #(.trigger("high")) register_3 (.D(demultiplexer_1_out2), .Q(register_3_q), .clk(t3));  // open: en, clr
  Register #(.trigger("high")) register_4 (.D(demultiplexer_1_out3), .Q(register_4_q), .clk(t4));  // open: en, clr
  assign controlled_buffer_6_out = register_5_q[3] ? register_4_q : 8'bz;  // Controlled_Buffer controlled_buffer_6
  or or_1 (or_1_out, controlled_buffer_4_out[0], controlled_buffer_4_out[1], controlled_buffer_4_out[2], controlled_buffer_4_out[3]);
  assign controlled_buffer_6_out = register_5_q[0] ? register_1_q : 8'bz;  // Controlled_Buffer controlled_buffer_7
  assign controlled_buffer_6_out = register_5_q[1] ? register_2_q : 8'bz;  // Controlled_Buffer controlled_buffer_8
  assign controlled_buffer_6_out = register_5_q[2] ? register_3_q : 8'bz;  // Controlled_Buffer controlled_buffer_9
  Register register_5 (
    .D({4'b0000, controlled_buffer_4_out}), .Q({register_5_q_2, register_5_q}), .clk(or_1_out));  // open: en, clr
  Register #(.trigger("falling")) register_6 (
    .D({register_5_q_2, register_5_q}), .Q({register_6_q_2, register_6_q}), .clk(IO_3R_update));  // open: en, clr
  assign DATA = IO_3R_update ? controlled_buffer_6_out : 8'bz;  // Controlled_Buffer controlled_buffer_10
  Pull_Resistor pull_resistor_5 (.node(controlled_buffer_6_out));
endmodule

module randomGenChip (
  input  [2:0] ADDR,
  input  SEL,
  input  R_W,
  output [7:0] DATA
);

  wire IO_1R_out;
  wire [7:0] random_1_out;

  and IO_1R (IO_1R_out, R_W, SEL, ADDR[0], ~ADDR[1], ~ADDR[2]);  // AND_Gate
  Random random_1 (.clk(IO_1R_out), .out(random_1_out));  // open: next, clr
  assign DATA = IO_1R_out ? random_1_out : 8'bz;  // Controlled_Buffer controlled_buffer_1
endmodule

module tailChip (
  input  [2:0] ADDRESS,
  input  SEL,
  input  R_W,
  input  [7:0] DATA,
  input  IACK,
  input  [4:0] SCORE,
  output [7:0] DATA_2
);

  wire IO_0_update, IO_0R_out, T1, T2, T3;
  wire [1:0] counter_1_q;
  wire [3:0] register_1_q, register_2_q;
  wire [4:0] dec_5bit_1_out_2, register_3_q;
  wire [7:0] controlled_buffer_1_out, controlled_buffer_2_out, controlled_buffer_3_out, multiplexer_1_out,
       shift_register_1_q0, shift_register_1_q1, shift_register_1_q2, shift_register_1_q3,
       shift_register_1_q4, shift_register_1_q5, shift_register_1_q6, shift_register_1_q7,
       shift_register_1_q8, shift_register_1_q9, shift_register_1_q10, shift_register_1_q11,
       shift_register_1_q12, shift_register_1_q13, shift_register_1_q14, shift_register_1_q15,
       shift_register_1_q16, shift_register_1_q17, shift_register_1_q18, shift_register_1_q19,
       shift_register_1_q20, shift_register_1_q21, shift_register_1_q22, shift_register_1_q23,
       shift_register_1_q24, shift_register_1_q25, shift_register_1_q26, shift_register_1_q27,
       shift_register_1_q28, shift_register_1_q29, shift_register_1_q30, shift_register_1_q31;

  Counter #(.width(2), .max('h2), .trigger("falling")) counter_1 (
    .Q(counter_1_q), .clk(IO_0_update), .clr(IACK));  // open: load, D, count, carry
  Decoder #(.select(2), .disabled(0)) decoder_1 (
    .out0(T1), .out1(T2), .out2(T3), .sel(counter_1_q), .en(IO_0_update));  // open: out3
  and IO_0W (IO_0_update, ~R_W, SEL, ~ADDRESS[0], ~ADDRESS[1], ~ADDRESS[2]);  // AND_Gate
  and IO_0R (IO_0R_out, R_W, SEL, ~ADDRESS[0], ~ADDRESS[1], ~ADDRESS[2]);  // AND_Gate
  assign controlled_buffer_1_out = T1 ? controlled_buffer_2_out : 8'bz;  // Controlled_Buffer controlled_buffer_1
  assign controlled_buffer_2_out = IO_0_update ? DATA : 8'bz;  // Controlled_Buffer controlled_buffer_2
  assign controlled_buffer_3_out = T2 ? controlled_buffer_2_out : 8'bz;  // Controlled_Buffer controlled_buffer_3
  Register #(.width(4), .trigger("falling")) register_1 (
    .D(controlled_buffer_3_out[3:0]), .Q(register_1_q), .clk(IO_0_update));  // open: en, clr
  Register #(.width(4), .trigger("falling")) register_2 (
    .D(controlled_buffer_1_out[3:0]), .Q(register_2_q), .clk(IO_0_update));  // open: en, clr
  Shift_Register #(.width(8), .length(32), .trigger("falling")) shift_register_1 (
    .in({register_2_q, register_1_q}), .clk(T3), .q0(shift_register_1_q0), .q1(shift_register_1_q1),
    .q2(shift_register_1_q2), .q3(shift_register_1_q3), .q4(shift_register_1_q4), .q5(shift_register_1_q5),
    .q6(shift_register_1_q6), .q7(shift_register_1_q7), .q8(shift_register_1_q8), .q9(shift_register_1_q9),
    .q10(shift_register_1_q10), .q11(shift_register_1_q11), .q12(shift_register_1_q12),
    .q13(shift_register_1_q13), .q14(shift_register_1_q14), .q15(shift_register_1_q15),
    .q16(shift_register_1_q16), .q17(shift_register_1_q17), .q18(shift_register_1_q18),
    .q19(shift_register_1_q19), .q20(shift_register_1_q20), .q21(shift_register_1_q21),
    .q22(shift_register_1_q22), .q23(shift_register_1_q23), .q24(shift_register_1_q24),
    .q25(shift_register_1_q25), .q26(shift_register_1_q26), .q27(shift_register_1_q27),
    .q28(shift_register_1_q28), .q29(shift_register_1_q29), .q30(shift_register_1_q30),
    .q31(shift_register_1_q31));  // open: shift, out, load, clr, d0, d1, d2, d3, d4, d5, d6, d7, d8, d9, d10, d11, d12, d13, d14, d15, d16, d17, d18, d19, d20, d21, d22, d23, d24, d25, d26, d27, d28, d29, d30, d31
  Multiplexer #(.select(5), .width(8)) multiplexer_1 (
    .in0(shift_register_1_q0), .in1(shift_register_1_q1), .in2(shift_register_1_q2),
    .in3(shift_register_1_q3), .in4(shift_register_1_q4), .in5(shift_register_1_q5),
    .in6(shift_register_1_q6), .in7(shift_register_1_q7), .in8(shift_register_1_q8),
    .in9(shift_register_1_q9), .in10(shift_register_1_q10), .in11(shift_register_1_q11),
    .in12(shift_register_1_q12), .in13(shift_register_1_q13), .in14(shift_register_1_q14),
    .in15(shift_register_1_q15), .in16(shift_register_1_q16), .in17(shift_register_1_q17),
    .in18(shift_register_1_q18), .in19(shift_register_1_q19), .in20(shift_register_1_q20),
    .in21(shift_register_1_q21), .in22(shift_register_1_q22), .in23(shift_register_1_q23),
    .in24(shift_register_1_q24), .in25(shift_register_1_q25), .in26(shift_register_1_q26),
    .in27(shift_register_1_q27), .in28(shift_register_1_q28), .in29(shift_register_1_q29),
    .in30(shift_register_1_q30), .in31(shift_register_1_q31), .out(multiplexer_1_out), .sel(dec_5bit_1_out_2));  // open: en
  assign DATA_2 = IO_0R_out ? multiplexer_1_out : 8'bz;  // Controlled_Buffer controlled_buffer_4
  dec__5bit dec_5bit_1 (.in_1(register_3_q), .out_2(dec_5bit_1_out_2));
  Register #(.width(5), .trigger("falling")) register_3 (.D(SCORE), .Q(register_3_q), .clk(T3));  // open: en, clr
endmodule

module scoreChip (
  input  [2:0] ADDRESS,
  input  SEL,
  input  R_W,
  input  [7:0] DATA,
  input  tick,
  output [4:0] out_6,
  output [7:0] DATA_2
);

  wire IO_4R_out, IO_4W_out, s_r_ff_1_q;
  wire [7:0] controlled_buffer_1_out, multiplexer_1_out;
  wire [7:5] register_1_q;

  assign controlled_buffer_1_out = IO_4W_out ? DATA : 8'bz;  // Controlled_Buffer controlled_buffer_1
  and IO_4W (IO_4W_out, ~R_W, SEL, ~ADDRESS[0], ~ADDRESS[1], ADDRESS[2]);  // AND_Gate
  and IO_4R (IO_4R_out, R_W, SEL, ~ADDRESS[0], ~ADDRESS[1], ADDRESS[2]);  // AND_Gate
  Multiplexer #(.width(8)) multiplexer_1 (
    .in0(8'h1), .in1(controlled_buffer_1_out), .out(multiplexer_1_out), .sel(s_r_ff_1_q));  // open: en
  S_R_Flip_Flop s_r_ff_1 (.S(IO_4W_out), .clk(IO_4W_out), .R(1'b0), .Q(s_r_ff_1_q));  // open: Qn, preset, reset, en
  Register #(.trigger("falling")) register_1 (
    .D(multiplexer_1_out), .Q({register_1_q, out_6}), .clk(tick));  // open: en, clr
  assign DATA_2 = IO_4R_out ? {register_1_q, out_6} : 8'bz;  // Controlled_Buffer controlled_buffer_2
endmodule

module capacitorModule__16x16 (
  input  [15:0] B1,
  input  [15:0] B1_2,
  input  [15:0] B1_3,
  input  [15:0] B1_4,
  input  [15:0] B1_5,
  input  [15:0] B1_6,
  input  [15:0] B1_7,
  input  [15:0] B1_8,
  input  [15:0] A1,
  input  [15:0] A1_2,
  input  [15:0] A1_3,
  input  [15:0] A1_4,
  input  [15:0] A1_5,
  input  [15:0] A1_6,
  input  [15:0] A1_7,
  input  [15:0] A1_8,
  input  [15:0] B1_9,
  input  [15:0] B1_10,
  input  [15:0] B1_11,
  input  [15:0] B1_12,
  input  to_Zero,
  input  [15:0] B1_13,
  input  [15:0] B1_14,
  input  [15:0] B1_15,
  input  [15:0] B1_16,
  input  TICK,
  input  [15:0] A1_9,
  input  [15:0] A1_10,
  input  [15:0] A1_11,
  input  [15:0] A1_12,
  input  [15:0] A1_13,
  input  [15:0] A1_14,
  input  [15:0] A1_15,
  input  [15:0] A1_16,
  output [15:0] C1,
  output [15:0] C1_2,
  output [15:0] C1_3,
  output [15:0] C1_4,
  output [15:0] C1_5,
  output [15:0] C1_6,
  output [15:0] C1_7,
  output [15:0] C1_8,
  output [15:0] C1_9,
  output [15:0] C1_10,
  output [15:0] C1_11,
  output [15:0] C1_12,
  output [15:0] C1_13,
  output [15:0] C1_14,
  output [15:0] C1_15,
  output [15:0] C1_16,
  output result
);

  wire [15:0] and_1_out, and_2_out, and_3_out, and_4_out, and_5_out, and_6_out, and_7_out, and_8_out,
       and_9_out, and_10_out, and_11_out, and_12_out, and_13_out, and_14_out, and_15_out, and_16_out,
       and_17_out, and_18_out, and_19_out, and_20_out, and_21_out, and_22_out, and_23_out, and_24_out,
       and_25_out, and_26_out, and_27_out, and_28_out, and_29_out, and_30_out, and_31_out, and_32_out,
       and_33_out, or_1_out, or_2_out, or_3_out, or_4_out, or_5_out, or_6_out, or_7_out, or_8_out, or_9_out,
       or_10_out, or_11_out, or_12_out, or_13_out, or_14_out, or_15_out, or_16_out, undriven;

  Pull_Resistor pull_resistor_1 (.node(result));
  assign and_1_out = ~B1 & or_1_out;  // AND_Gate and_1, 16 bits wide
  assign or_1_out = A1 | C1;  // OR_Gate or_1, 16 bits wide
  bitReducer__16_1 bitreducer_16_1_1 (.out_2(result), .in_1(and_2_out));
  assign and_2_out = A1 & C1;  // AND_Gate and_2, 16 bits wide
  assign or_2_out = A1_9 | C1_9;  // OR_Gate or_2, 16 bits wide
  Register #(.width(16)) register_1 (.D(and_1_out), .Q(C1), .clk(TICK), .clr(to_Zero));  // open: en
  assign and_3_out = ~B1_9 & or_2_out;  // AND_Gate and_3, 16 bits wide
  bitReducer__16_1 bitreducer_16_1_2 (.out_2(result), .in_1(and_4_out));
  assign and_4_out = A1_9 & C1_9;  // AND_Gate and_4, 16 bits wide
  Register #(.width(16)) register_2 (.D(and_3_out), .Q(C1_9), .clk(TICK), .clr(to_Zero));  // open: en
  assign or_3_out = A1_3 | C1_2;  // OR_Gate or_3, 16 bits wide
  assign or_4_out = A1_11 | C1_10;  // OR_Gate or_4, 16 bits wide
  assign and_5_out = ~B1_3 & or_3_out;  // AND_Gate and_5, 16 bits wide
  Register #(.width(16)) register_3 (.D(and_5_out), .Q(C1_2), .clk(TICK), .clr(to_Zero));  // open: en
  bitReducer__16_1 bitreducer_16_1_3 (.out_2(result), .in_1(and_6_out));
  assign and_6_out = A1_3 & C1_2;  // AND_Gate and_6, 16 bits wide
  assign and_7_out = ~B1_11 & or_4_out;  // AND_Gate and_7, 16 bits wide
  bitReducer__16_1 bitreducer_16_1_4 (.out_2(result), .in_1(and_8_out));
  assign and_8_out = A1_11 & C1_10;  // AND_Gate and_8, 16 bits wide
  Register #(.width(16)) register_4 (.D(and_7_out), .Q(C1_10), .clk(TICK), .clr(to_Zero));  // open: en
  assign or_5_out = A1_5 | C1_3;  // OR_Gate or_5, 16 bits wide
  assign or_6_out = A1_13 | C1_11;  // OR_Gate or_6, 16 bits wide
  assign and_9_out = ~B1_5 & or_5_out;  // AND_Gate and_9, 16 bits wide
  Register #(.width(16)) register_5 (.D(and_9_out), .Q(C1_3), .clk(TICK), .clr(to_Zero));  // open: en
  bitReducer__16_1 bitreducer_16_1_5 (.out_2(result), .in_1(and_10_out));
  assign and_10_out = A1_5 & C1_3;  // AND_Gate and_10, 16 bits wide
  assign and_11_out = ~B1_13 & or_6_out;  // AND_Gate and_11, 16 bits wide
  bitReducer__16_1 bitreducer_16_1_6 (.out_2(result), .in_1(and_12_out));
  assign and_12_out = A1_13 & C1_11;  // AND_Gate and_12, 16 bits wide
  Register #(.width(16)) register_6 (.D(and_11_out), .Q(C1_11), .clk(TICK), .clr(to_Zero));  // open: en
  assign or_7_out = A1_7 | C1_4;  // OR_Gate or_7, 16 bits wide
  assign and_13_out = ~B1_7 & or_7_out;  // AND_Gate and_13, 16 bits wide
  bitReducer__16_1 bitreducer_16_1_7 (.out_2(result), .in_1(and_14_out));
  assign and_14_out = A1_7 & C1_4;  // AND_Gate and_14, 16 bits wide
  assign and_15_out = ~B1_15 & or_8_out;  // AND_Gate and_15, 16 bits wide
  assign or_8_out = A1_15 | C1_12;  // OR_Gate or_8, 16 bits wide
  bitReducer__16_1 bitreducer_16_1_8 (.out_2(result), .in_1(and_16_out));
  assign and_16_out = A1_15 & C1_12;  // AND_Gate and_16, 16 bits wide
  Register #(.width(16)) register_7 (.D(and_13_out), .Q(C1_4), .clk(TICK), .clr(to_Zero));  // open: en
  Register #(.width(16)) register_8 (.D(and_15_out), .Q(C1_12), .clk(TICK), .clr(to_Zero));  // open: en
  assign or_9_out = A1_2 | C1_5;  // OR_Gate or_9, 16 bits wide
  bitReducer__16_1 bitreducer_16_1_9 (.out_2(result), .in_1(and_17_out));
  assign and_17_out = A1_2 & C1_5;  // AND_Gate and_17, 16 bits wide
  assign or_10_out = A1_10 | C1_13;  // OR_Gate or_10, 16 bits wide
  assign and_18_out = ~B1_2 & or_9_out;  // AND_Gate and_18, 16 bits wide
  Register #(.width(16)) register_9 (.D(and_18_out), .Q(C1_5), .clk(TICK), .clr(to_Zero));  // open: en
  assign and_19_out = ~B1_10 & or_10_out;  // AND_Gate and_19, 16 bits wide
  bitReducer__16_1 bitreducer_16_1_10 (.out_2(result), .in_1(and_20_out));
  assign and_20_out = A1_10 & C1_13;  // AND_Gate and_20, 16 bits wide
  Register #(.width(16)) register_10 (.D(and_19_out), .Q(C1_13), .clk(TICK), .clr(to_Zero));  // open: en
  assign or_11_out = A1_4 | C1_6;  // OR_Gate or_11, 16 bits wide
  assign and_21_out = ~B1_4 & or_11_out;  // AND_Gate and_21, 16 bits wide
  bitReducer__16_1 bitreducer_16_1_11 (.out_2(result), .in_1(and_22_out));
  bitReducer__16_1 bitreducer_16_1_12 (.out_2(result), .in_1(and_23_out));
  assign and_22_out = A1_4 & C1_6;  // AND_Gate and_22, 16 bits wide
  assign and_23_out = undriven & C1_6;  // AND_Gate and_23, 16 bits wide
  assign and_24_out = ~B1_12 & or_12_out;  // AND_Gate and_24, 16 bits wide
  assign or_12_out = A1_12 | C1_14;  // OR_Gate or_12, 16 bits wide
  bitReducer__16_1 bitreducer_16_1_13 (.out_2(result), .in_1(and_25_out));
  assign and_25_out = A1_12 & C1_14;  // AND_Gate and_25, 16 bits wide
  Register #(.width(16)) register_11 (.D(and_21_out), .Q(C1_6), .clk(TICK), .clr(to_Zero));  // open: en
  Register #(.width(16)) register_12 (.D(and_24_out), .Q(C1_14), .clk(TICK), .clr(to_Zero));  // open: en
  assign or_13_out = A1_6 | C1_7;  // OR_Gate or_13, 16 bits wide
  assign and_26_out = ~B1_6 & or_13_out;  // AND_Gate and_26, 16 bits wide
  bitReducer__16_1 bitreducer_16_1_14 (.out_2(result), .in_1(and_27_out));
  assign and_27_out = A1_6 & C1_7;  // AND_Gate and_27, 16 bits wide
  assign and_28_out = ~B1_14 & or_14_out;  // AND_Gate and_28, 16 bits wide
  assign or_14_out = A1_14 | C1_15;  // OR_Gate or_14, 16 bits wide
  bitReducer__16_1 bitreducer_16_1_15 (.out_2(result), .in_1(and_29_out));
  assign and_29_out = A1_14 & C1_15;  // AND_Gate and_29, 16 bits wide
  Register #(.width(16)) register_13 (.D(and_26_out), .Q(C1_7), .clk(TICK), .clr(to_Zero));  // open: en
  Register #(.width(16)) register_14 (.D(and_28_out), .Q(C1_15), .clk(TICK), .clr(to_Zero));  // open: en
  assign or_15_out = A1_8 | C1_8;  // OR_Gate or_15, 16 bits wide
  assign and_30_out = ~B1_8 & or_15_out;  // AND_Gate and_30, 16 bits wide
  bitReducer__16_1 bitreducer_16_1_16 (.out_2(result), .in_1(and_31_out));
  assign and_31_out = A1_8 & C1_8;  // AND_Gate and_31, 16 bits wide
  assign or_16_out = A1_16 | C1_16;  // OR_Gate or_16, 16 bits wide
  bitReducer__16_1 bitreducer_16_1_17 (.out_2(result), .in_1(and_32_out));
  assign and_32_out = A1_16 & C1_16;  // AND_Gate and_32, 16 bits wide
  Register #(.width(16)) register_15 (.D(and_30_out), .Q(C1_8), .clk(TICK), .clr(to_Zero));  // open: en
  assign and_33_out = ~B1_16 & or_16_out;  // AND_Gate and_33, 16 bits wide
  Register #(.width(16)) register_16 (.D(and_33_out), .Q(C1_16), .clk(TICK), .clr(to_Zero));  // open: en

  // Other names for the same wires on the sheet: res = result; zero = to_Zero
endmodule

module bitExtender__16_32 (
  input  [15:0] in_1,
  output [31:0] out_2
);


  assign out_2 = {{2{in_1[15]}}, {2{in_1[14]}}, {2{in_1[13]}}, {2{in_1[12]}}, {2{in_1[11]}}, {2{in_1[10]}}, {2{in_1[9]}}, {2{in_1[8]}}, {2{in_1[7]}}, {2{in_1[6]}}, {2{in_1[5]}}, {2{in_1[4]}}, {2{in_1[3]}}, {2{in_1[2]}}, {2{in_1[1]}}, {2{in_1[0]}}};
endmodule

module bitReducer__16_1 (
  input  [15:0] in_1,
  output out_2
);

  wire or_1_out;

  assign out_2 = or_1_out ? or_1_out : 1'bz;  // Controlled_Buffer controlled_buffer_1
  or or_1 (or_1_out, in_1[15], in_1[14], in_1[13], in_1[12], in_1[11], in_1[10], in_1[9], in_1[8], in_1[6], in_1[5], in_1[4], in_1[3], in_1[2], in_1[1], in_1[0], in_1[7]);
endmodule

module smallOR__16bit (
  input  [15:0] in_1,
  input  [15:0] in_2,
  output [15:0] out_3
);

  assign out_3 = in_1 | in_2;  // OR_Gate or_1, 16 bits wide
endmodule

module dec__5bit (
  input  [4:0] in_1,
  output [4:0] out_2
);

  wire [4:1] or_1_out;
  wire [4:4] or_1_out_2;

  assign {or_1_out_2[4], or_1_out} = in_1 | {or_1_out, 1'b0};  // OR_Gate or_1, 5 bits wide
  assign out_2 = ~({or_1_out, 1'b0} ^ in_1);  // XNOR_Gate xnor_1, 5 bits wide
endmodule
