// Logisim project additional.circ as structural Verilog
module buttons (
);

  wire D, L, or_1_out, R, U;
  wire [6:0] keyboard_1_data;
  wire [7:0] bit_extender_1_out;

  Button button_1 (.out(U));
  Button button_2 (.out(L));
  Button button_3 (.out(R));
  Button button_4 (.out(D));
  Keyboard keyboard_1 (.clk(or_1_out), .data(keyboard_1_data));  // open: re, clr, avail
  or or_1 (or_1_out, L, R, D, U);
  assign bit_extender_1_out = {{1{1'b0}}, keyboard_1_data};  // Bit_Extender bit_extender_1
  Comparator comparator_1 (.a(bit_extender_1_out), .b(8'h61), .eq(L));  // open: gt, lt
  Comparator comparator_2 (.a(bit_extender_1_out), .b(8'h64), .eq(R));  // open: gt, lt
  Comparator comparator_3 (.a(bit_extender_1_out), .b(8'h77), .eq(U));  // open: gt, lt
  Comparator comparator_4 (.a(bit_extender_1_out), .b(8'h73), .eq(D));  // open: gt, lt
endmodule
