// Logisim project SnakeProject (Beuty).circ as structural Verilog: 6 circuits, main circuit main
module main (
);

  wire and_1_out, cdm_8_mark5_1_data_inst, cdm_8_mark5_1_mem_cycle, code, data, IAck, IOsel, IRQ,
       keyboard_1_avail, not_1_out, R_W, tck;
  wire [2:0] IOaddr, vec;
  wire [3:0] Direction;
  wire [6:0] keyboardButton;
  wire [7:0] cdm_8_mark5_1_data_out, cdm_8_mark5_1_pc, cdm_8_mark5_1_ps, cdm_8_mark5_1_r0, cdm_8_mark5_1_r1,
       cdm_8_mark5_1_r2, cdm_8_mark5_1_r3, cdm_8_mark5_1_sp, controlled_buffer_2_out, IOdat,
       scorechip_1_to_score_screen;
  wire [7:3] cdm_8_mark5_1_addr;
  wire [31:0] displaycontrollerchip_1_out_8, displaycontrollerchip_1_out_9, displaycontrollerchip_1_out_10,
       displaycontrollerchip_1_out_11, displaycontrollerchip_1_out_12, displaycontrollerchip_1_out_13,
       displaycontrollerchip_1_out_14, displaycontrollerchip_1_out_15, displaycontrollerchip_1_out_16,
       displaycontrollerchip_1_out_17, displaycontrollerchip_1_out_18, displaycontrollerchip_1_out_19,
       displaycontrollerchip_1_out_20, displaycontrollerchip_1_out_21, displaycontrollerchip_1_out_22,
       displaycontrollerchip_1_out_23;

  Pull_Resistor pull_resistor_1 (.node(IRQ));
  Pull_Resistor pull_resistor_2 (.node(code));
  Pull_Resistor pull_resistor_3 (.node(data));
  // Probe on cdm_8_mark5_1_r3
  // Probe on cdm_8_mark5_1_r2
  // Probe on cdm_8_mark5_1_r1
  // Probe on cdm_8_mark5_1_r0
  Clock clock_1 (.out(tck));
  // Probe on cdm_8_mark5_1_ps
  // Probe on cdm_8_mark5_1_pc
  // Probe on cdm_8_mark5_1_sp
  CdM_8_mark5 cdm_8_mark5_1 (
    .clock(tck), .addr({cdm_8_mark5_1_addr, IOaddr}), .mem_read(R_W), .mem_cycle(cdm_8_mark5_1_mem_cycle),
    .data_inst(cdm_8_mark5_1_data_inst), .data_out(cdm_8_mark5_1_data_out),
    .data_in(controlled_buffer_2_out), .r0(cdm_8_mark5_1_r0), .r1(cdm_8_mark5_1_r1), .r2(cdm_8_mark5_1_r2),
    .r3(cdm_8_mark5_1_r3), .PC(cdm_8_mark5_1_pc), .SP(cdm_8_mark5_1_sp), .PS(cdm_8_mark5_1_ps), .IAck(IAck),
    .IRQ(IRQ), .vec(vec));
  randomGenChip randomgenchip_1 (.ADDR(IOaddr), .SEL(IOsel), .R_W(R_W), .DATA(IOdat));
  keyboardChip keyboardchip_1 (
    .ADDRESS(IOaddr), .SEL(IOsel), .R_W(R_W), .DATA_2(IOdat), .DATA(IOdat), .Control(Direction));
  Decoder #(.disabled(0)) decoder_1 (
    .out0(code), .out1(data), .sel(cdm_8_mark5_1_data_inst), .en(cdm_8_mark5_1_mem_cycle));
  not not_1 (not_1_out, R_W);
  assign IOdat = not_1_out ? cdm_8_mark5_1_data_out : 8'bz;  // Controlled_Buffer controlled_buffer_1
  assign controlled_buffer_2_out = R_W ? IOdat : 8'bz;  // Controlled_Buffer controlled_buffer_2
  and and_1 (and_1_out, ~IOsel, data);  // AND_Gate
  Comparator #(.width(7)) comparator_1 (.a(keyboardButton), .b(7'b1100001), .eq(Direction[0]));  // open: gt, lt
  Comparator #(.width(7)) comparator_2 (.a(keyboardButton), .b(7'b1100100), .eq(Direction[1]));  // open: gt, lt
  Comparator #(.width(7)) comparator_3 (.a(keyboardButton), .b(7'b1110111), .eq(Direction[2]));  // open: gt, lt
  Comparator #(.width(7)) comparator_4 (.a(keyboardButton), .b(7'b1110011), .eq(Direction[3]));  // open: gt, lt
  and and_2 (IOsel, cdm_8_mark5_1_addr[3], cdm_8_mark5_1_addr[4], cdm_8_mark5_1_addr[5], cdm_8_mark5_1_addr[7], cdm_8_mark5_1_addr[6], data);
  ROM rom_1 (.addr({cdm_8_mark5_1_addr, IOaddr}), .data(IOdat), .sel(code));
  RAM ram_1 (.addr({cdm_8_mark5_1_addr, IOaddr}), .data(IOdat), .sel(and_1_out), .clk(tck), .ld(R_W));  // open: clr
  DotMatrix #(.matrixcols(32), .matrixrows(32), .persist(22)) dotmatrix_1 (
    .col0(displaycontrollerchip_1_out_8), .col1(displaycontrollerchip_1_out_8),
    .col2(displaycontrollerchip_1_out_9), .col3(displaycontrollerchip_1_out_9),
    .col4(displaycontrollerchip_1_out_10), .col5(displaycontrollerchip_1_out_10),
    .col6(displaycontrollerchip_1_out_11), .col7(displaycontrollerchip_1_out_11),
    .col8(displaycontrollerchip_1_out_12), .col9(displaycontrollerchip_1_out_12),
    .col10(displaycontrollerchip_1_out_13), .col11(displaycontrollerchip_1_out_13),
    .col12(displaycontrollerchip_1_out_14), .col13(displaycontrollerchip_1_out_14),
    .col14(displaycontrollerchip_1_out_15), .col15(displaycontrollerchip_1_out_15),
    .col16(displaycontrollerchip_1_out_16), .col17(displaycontrollerchip_1_out_16),
    .col18(displaycontrollerchip_1_out_17), .col19(displaycontrollerchip_1_out_17),
    .col20(displaycontrollerchip_1_out_18), .col21(displaycontrollerchip_1_out_18),
    .col22(displaycontrollerchip_1_out_19), .col23(displaycontrollerchip_1_out_19),
    .col24(displaycontrollerchip_1_out_20), .col25(displaycontrollerchip_1_out_20),
    .col26(displaycontrollerchip_1_out_21), .col27(displaycontrollerchip_1_out_21),
    .col28(displaycontrollerchip_1_out_22), .col29(displaycontrollerchip_1_out_22),
    .col30(displaycontrollerchip_1_out_23), .col31(displaycontrollerchip_1_out_23));
  // Probe on scorechip_1_to_score_screen
  displayControllerChip displaycontrollerchip_1 (
    .ADDRESS(IOaddr), .SEL(IOsel), .R_W(R_W), .DATA(IOdat), .out_17(displaycontrollerchip_1_out_17),
    .out_18(displaycontrollerchip_1_out_18), .out_19(displaycontrollerchip_1_out_19),
    .out_20(displaycontrollerchip_1_out_20), .out_21(displaycontrollerchip_1_out_21),
    .out_22(displaycontrollerchip_1_out_22), .out_23(displaycontrollerchip_1_out_23),
    .out_8(displaycontrollerchip_1_out_8), .out_9(displaycontrollerchip_1_out_9),
    .out_10(displaycontrollerchip_1_out_10), .out_11(displaycontrollerchip_1_out_11),
    .out_12(displaycontrollerchip_1_out_12), .out_13(displaycontrollerchip_1_out_13),
    .out_14(displaycontrollerchip_1_out_14), .out_15(displaycontrollerchip_1_out_15),
    .out_16(displaycontrollerchip_1_out_16), .IRQ(IRQ), .IACK(IAck), .VEC(vec), .TICK(tck), .DATA_2(IOdat));
  Keyboard keyboard_1 (.clk(keyboard_1_avail), .avail(keyboard_1_avail), .data(keyboardButton));  // open: re, clr
  scoreChip scorechip_1 (
    .ADDRESS(IOaddr), .SEL(IOsel), .R_W(R_W), .DATA(IOdat), .DATA_2(IOdat),
    .to_Score_screen(scorechip_1_to_score_screen), .tck(tck));

  // Notes on the sheet:
  //   contents of rom_1 (hex, n*v repeats v):
  //   cd af d0 9 c0 d0 80 c0 d9 d0 fb d1 3e a1 d1 43 a1 d1 48 a1 d1 4d a1 d0 f8 d3 f2 d1 6 ad a1 8f ad a1
  //   d1 0 a1 d0 f0 d1 b0 d2 66 a6 a1 d1 fb b4 0 e0 2f d6 76 d0 f8 d1 fb b5 c1 d7 ee 37 d6 70 8a ee 50 d6
  //   70 8e ee 50 d6 70 8d ee 50 d6 70 89 a1 a2 d3 f2 ad 8f ae d1 f0 b5 b7 a3 b3 a7 89 d2 b0 76 ea 69 d3
  //   f1 bf 1e 9 d0 f0 a1 d0 f8 ee 37 d3 f3 be 8b bd d7 d0 f9 b1 8c a1 d7 d0 fd d3 20 a1 8b e1 80 d4 c0 c1
  //   d6 76 d0 f1 b1 8d a1 d0 fc a1 c5 c4 d9 96*0 7c 1 85 1
endmodule

module displayControllerChip (
  input  [2:0] ADDRESS,
  input  SEL,
  input  R_W,
  input  [7:0] DATA,
  input  TICK,
  input  IACK,
  output [7:0] DATA_2,
  output [31:0] out_8,
  output [31:0] out_9,
  output [31:0] out_10,
  output [31:0] out_11,
  output [31:0] out_12,
  output [31:0] out_13,
  output [31:0] out_14,
  output [31:0] out_15,
  output [31:0] out_16,
  output [31:0] out_17,
  output [31:0] out_18,
  output [31:0] out_19,
  output [31:0] out_20,
  output [31:0] out_21,
  output [31:0] out_22,
  output [31:0] out_23,
  output IRQ,
  output [2:0] VEC
);

  wire and_2_out, comparator_1_eq, comparator_2_eq, controlled_buffer_2_out, controlled_buffer_3_out,
       counter_3_carry, d_ff_1_q, enable_apple, Free_lock, IO_0_Read, IO_0_update, IO_2_update, IO_5_update,
       j_k_ff_1_q, j_k_ff_1_qn, multiplexer_1_out, multiplexer_2_out, nor_1_out, not_2_out, not_3_out,
       not_4_out, or_1_out, or_2_out, pull_resistor_2_node, register_3_q, register_4_q, register_5_q,
       register_6_q, register_7_q, restart_cap, T1, T2, T3, tailBump, update_screen;
  wire [1:0] counter_4_q;
  wire [3:0] APPLEX, APPLEY, Free_X, HEADX, HEADY, multiplexer_3_out;
  wire [7:0] controlled_buffer_8_out, controlled_buffer_9_out, controlled_buffer_13_out,
       controlled_buffer_14_out, Coordinate, counter_1_q, Lose_text, pull_resistor_1_node, register_1_q,
       register_2_q, register_10_q;
  wire [15:0] capacitormodule_16x16_1_c1, capacitormodule_16x16_1_c1_2, capacitormodule_16x16_1_c1_3,
       capacitormodule_16x16_1_c1_4, capacitormodule_16x16_1_c1_5, capacitormodule_16x16_1_c1_6,
       capacitormodule_16x16_1_c1_7, capacitormodule_16x16_1_c1_8, capacitormodule_16x16_1_c1_9,
       capacitormodule_16x16_1_c1_10, capacitormodule_16x16_1_c1_11, capacitormodule_16x16_1_c1_12,
       capacitormodule_16x16_1_c1_13, capacitormodule_16x16_1_c1_14, capacitormodule_16x16_1_c1_15,
       capacitormodule_16x16_1_c1_16, decoder_2_out0, decoder_3_out0, demultiplexer_1_out0,
       demultiplexer_1_out1, demultiplexer_1_out2, demultiplexer_1_out3, demultiplexer_1_out4,
       demultiplexer_1_out5, demultiplexer_1_out6, demultiplexer_1_out7, demultiplexer_1_out8,
       demultiplexer_1_out9, demultiplexer_1_out10, demultiplexer_1_out11, demultiplexer_1_out12,
       demultiplexer_1_out13, demultiplexer_1_out14, demultiplexer_1_out15, demultiplexer_2_out0,
       demultiplexer_2_out1, demultiplexer_2_out2, demultiplexer_2_out3, demultiplexer_2_out4,
       demultiplexer_2_out5, demultiplexer_2_out6, demultiplexer_2_out7, demultiplexer_2_out8,
       demultiplexer_2_out9, demultiplexer_2_out10, demultiplexer_2_out11, demultiplexer_2_out12,
       demultiplexer_2_out13, demultiplexer_2_out14, demultiplexer_2_out15, demultiplexer_3_out0,
       demultiplexer_4_out0, demultiplexer_4_out1, demultiplexer_4_out2, demultiplexer_4_out3,
       demultiplexer_4_out4, demultiplexer_4_out5, demultiplexer_4_out6, demultiplexer_4_out7,
       demultiplexer_4_out8, demultiplexer_4_out9, demultiplexer_4_out10, demultiplexer_4_out11,
       demultiplexer_4_out12, demultiplexer_4_out13, demultiplexer_4_out14, demultiplexer_4_out15,
       Free_Column, multiplexer_4_out, smallor_16_bit_1_out_3, smallor_16_bit_2_out_3,
       smallor_16_bit_3_out_3, smallor_16_bit_4_out_3, smallor_16_bit_5_out_3, smallor_16_bit_6_out_3,
       smallor_16_bit_7_out_3, smallor_16_bit_8_out_3, smallor_16_bit_9_out_3, smallor_16_bit_10_out_3,
       smallor_16_bit_11_out_3, smallor_16_bit_12_out_3, smallor_16_bit_13_out_3, smallor_16_bit_14_out_3,
       smallor_16_bit_15_out_3, smallor_16_bit_16_out_3;

  Counter #(.ongoal("stay")) counter_1 (.Q(counter_1_q), .clk(IO_5_update));  // open: load, D, count, carry, clr
  D_Flip_Flop d_ff_1 (.clk(IO_5_update), .D(IO_5_update), .Q(d_ff_1_q));  // open: Qn, preset, en, reset
  not not_1 (Free_lock, d_ff_1_q);
  not not_2 (not_2_out, Free_lock);
  Counter #(.width(4), .max('hf), .ongoal("stay"), .trigger("falling")) counter_2 (
    .Q(Free_X), .clk(j_k_ff_1_q));  // open: load, D, count, carry, clr
  J_K_Flip_Flop j_k_ff_1 (
    .J(IO_5_update), .clk(IO_5_update), .K(IO_5_update), .Q(j_k_ff_1_q), .Qn(j_k_ff_1_qn));  // open: preset, en, reset
  Comparator #(.width(4), .mode("unsigned")) comparator_1 (
    .a(APPLEX), .b(HEADX), .eq(comparator_1_eq));  // open: gt, lt
  Comparator #(.width(4), .mode("unsigned")) comparator_2 (
    .a(APPLEY), .b(HEADY), .eq(comparator_2_eq));  // open: gt, lt
  Pull_Resistor pull_resistor_1 (.node(pull_resistor_1_node));
  assign pull_resistor_1_node = or_1_out ? Coordinate : 8'bz;  // Controlled_Buffer controlled_buffer_1
  or or_1 (or_1_out, T1, T2);
  and IO_0R (IO_0_Read, R_W, SEL, ~ADDRESS[0], ~ADDRESS[1], ~ADDRESS[2]);  // AND_Gate
  and IO_0W (IO_0_update, ~R_W, SEL, ~ADDRESS[0], ~ADDRESS[1], ~ADDRESS[2]);  // AND_Gate
  and IO_2W (IO_2_update, ~R_W, SEL, ~ADDRESS[0], ADDRESS[1], ~ADDRESS[2]);  // AND_Gate
  and IO_5W (IO_5_update, ~R_W, SEL, ADDRESS[0], ~ADDRESS[1], ADDRESS[2]);  // AND_Gate
  not not_3 (not_3_out, d_ff_1_q);
  and and_1 (restart_cap, not_3_out, d_ff_1_q);
  ROM rom_1 (.addr(counter_1_q), .data(Lose_text), .sel(not_2_out));
  Register #(.trigger("falling")) register_1 (
    .D(Lose_text), .Q(register_1_q), .clk(controlled_buffer_2_out));  // open: en, clr
  assign controlled_buffer_2_out = j_k_ff_1_q ? IO_5_update : 1'bz;  // Controlled_Buffer controlled_buffer_2
  Register #(.trigger("falling")) register_2 (
    .D(Lose_text), .Q(register_2_q), .clk(controlled_buffer_3_out));  // open: en, clr
  assign controlled_buffer_3_out = j_k_ff_1_qn ? IO_5_update : 1'bz;  // Controlled_Buffer controlled_buffer_3
  or or_2 (or_2_out, pull_resistor_1_node[4], pull_resistor_1_node[5], pull_resistor_1_node[6], pull_resistor_1_node[7], register_3_q);
  Register #(.width(1)) register_3 (.D(tailBump), .Q(register_3_q), .clk(update_screen), .clr(IACK));  // open: en
  assign Free_Column = j_k_ff_1_q ? {register_2_q, register_1_q} : 16'bz;  // Controlled_Buffer controlled_buffer_4
  Register #(.width(1)) register_4 (.D(and_2_out), .Q(register_4_q), .clk(update_screen), .clr(IACK));  // open: en
  and and_2 (and_2_out, comparator_1_eq, comparator_2_eq);
  Register #(.width(1), .trigger("high")) register_5 (
    .D(or_2_out), .Q(register_5_q), .clk(or_2_out), .clr(counter_3_carry));  // open: en
  Counter #(.width(3), .max('h7), .ongoal("stay")) counter_3 (
    .count(IACK), .carry(counter_3_carry), .clk(TICK), .clr(counter_3_carry));  // open: load, D, Q
  Multiplexer #(.disabled(0)) multiplexer_1 (
    .in0(register_4_q), .in1(1'b0), .out(multiplexer_1_out), .sel(IACK), .en(enable_apple));
  Multiplexer #(.disabled(0)) multiplexer_2 (
    .in0(register_5_q), .in1(1'b0), .out(multiplexer_2_out), .sel(counter_3_carry), .en(enable_apple));
  Register #(.width(1)) register_6 (.D(multiplexer_1_out), .Q(register_6_q), .clk(TICK));  // open: en, clr
  Register #(.width(1)) register_7 (.D(multiplexer_2_out), .Q(register_7_q), .clk(TICK));  // open: en, clr
  assign Coordinate = IO_0_update ? DATA : 8'bz;  // Controlled_Buffer controlled_buffer_5
  assign IRQ = register_6_q ? 1'b1 : 1'bz;  // Controlled_Buffer controlled_buffer_6
  assign IRQ = register_7_q ? 1'b1 : 1'bz;  // Controlled_Buffer controlled_buffer_7
  Register #(.width(4), .trigger("falling")) register_8 (
    .D(controlled_buffer_8_out[3:0]), .Q(HEADX), .clk(IO_0_update));  // open: en, clr
  assign controlled_buffer_8_out = T2 ? Coordinate : 8'bz;  // Controlled_Buffer controlled_buffer_8
  Register #(.width(4), .trigger("falling")) register_9 (
    .D(controlled_buffer_9_out[3:0]), .Q(HEADY), .clk(IO_0_update));  // open: en, clr
  assign controlled_buffer_9_out = T1 ? Coordinate : 8'bz;  // Controlled_Buffer controlled_buffer_9
  assign VEC = register_6_q ? 3'b011 : 3'bz;  // Controlled_Buffer controlled_buffer_10
  assign VEC = register_7_q ? 3'b010 : 3'bz;  // Controlled_Buffer controlled_buffer_11
  Decoder #(.select(2), .disabled(0)) decoder_1 (
    .out0(T1), .out1(T2), .out2(T3), .sel(counter_4_q), .en(IO_0_update));  // open: out3
  Counter #(.width(2), .max('h2), .trigger("falling")) counter_4 (
    .Q(counter_4_q), .clk(IO_0_update), .clr(IACK));  // open: load, D, count, carry
  Decoder #(.select(4), .disabled(0)) decoder_2 (
    .out0(decoder_2_out0[0]), .out1(decoder_2_out0[1]), .out2(decoder_2_out0[2]), .out3(decoder_2_out0[3]),
    .out4(decoder_2_out0[4]), .out5(decoder_2_out0[5]), .out6(decoder_2_out0[6]), .out7(decoder_2_out0[7]),
    .out8(decoder_2_out0[8]), .out9(decoder_2_out0[9]), .out10(decoder_2_out0[10]),
    .out11(decoder_2_out0[11]), .out12(decoder_2_out0[12]), .out13(decoder_2_out0[13]),
    .out14(decoder_2_out0[14]), .out15(decoder_2_out0[15]), .sel(HEADY));  // open: en
  assign DATA_2 = IO_0_Read ? {HEADY, HEADX} : 8'bz;  // Controlled_Buffer controlled_buffer_12
  assign controlled_buffer_13_out = T3 ? Coordinate : 8'bz;  // Controlled_Buffer controlled_buffer_13
  Multiplexer #(.width(4), .disabled(0)) multiplexer_3 (
    .in0(Free_X), .in1(HEADX), .out(multiplexer_3_out), .sel(Free_lock));  // open: en
  Multiplexer #(.width(16), .disabled(0)) multiplexer_4 (
    .in0(Free_Column), .in1(decoder_2_out0), .out(multiplexer_4_out), .sel(Free_lock));  // open: en
  or or_3 (update_screen, nor_1_out, IO_5_update);
  nor nor_1 (nor_1_out, not_4_out, T3);
  not not_4 (not_4_out, T3);
  Register #(.trigger("falling")) register_10 (
    .D(controlled_buffer_13_out), .Q(register_10_q), .clk(IO_0_update));  // open: en, clr
  Decoder #(.select(4), .disabled(0)) decoder_3 (
    .out0(decoder_3_out0[0]), .out1(decoder_3_out0[1]), .out2(decoder_3_out0[2]), .out3(decoder_3_out0[3]),
    .out4(decoder_3_out0[4]), .out5(decoder_3_out0[5]), .out6(decoder_3_out0[6]), .out7(decoder_3_out0[7]),
    .out8(decoder_3_out0[8]), .out9(decoder_3_out0[9]), .out10(decoder_3_out0[10]),
    .out11(decoder_3_out0[11]), .out12(decoder_3_out0[12]), .out13(decoder_3_out0[13]),
    .out14(decoder_3_out0[14]), .out15(decoder_3_out0[15]), .sel(register_10_q[7:4]), .en(T3));
  Demultiplexer #(.select(4), .width(16), .disabled(0)) demultiplexer_1 (
    .out0(demultiplexer_1_out0), .out1(demultiplexer_1_out1), .out2(demultiplexer_1_out2),
    .out3(demultiplexer_1_out3), .out4(demultiplexer_1_out4), .out5(demultiplexer_1_out5),
    .out6(demultiplexer_1_out6), .out7(demultiplexer_1_out7), .out8(demultiplexer_1_out8),
    .out9(demultiplexer_1_out9), .out10(demultiplexer_1_out10), .out11(demultiplexer_1_out11),
    .out12(demultiplexer_1_out12), .out13(demultiplexer_1_out13), .out14(demultiplexer_1_out14),
    .out15(demultiplexer_1_out15), .in(decoder_3_out0), .sel(register_10_q[3:0]), .en(Free_lock));
  assign controlled_buffer_14_out = IO_2_update ? DATA : 8'bz;  // Controlled_Buffer controlled_buffer_14
  Register #(.width(4), .trigger("falling")) register_11 (
    .D(controlled_buffer_14_out[3:0]), .Q(APPLEX), .clk(IO_2_update));  // open: en, clr
  Register #(.width(4), .trigger("falling")) register_12 (
    .D(controlled_buffer_14_out[7:4]), .Q(APPLEY), .clk(IO_2_update));  // open: en, clr
  J_K_Flip_Flop j_k_ff_2 (
    .J(IO_2_update), .clk(IO_2_update), .K(1'b0), .Q(enable_apple));  // open: Qn, preset, en, reset
  capacitorModule__16x16 capacitormodule_16x16_1 (
    .B1(demultiplexer_1_out0), .B1_2(demultiplexer_1_out4), .B1_3(demultiplexer_1_out1),
    .B1_4(demultiplexer_1_out5), .B1_5(demultiplexer_1_out2), .B1_6(demultiplexer_1_out6),
    .B1_7(demultiplexer_1_out3), .B1_8(demultiplexer_1_out7), .B1_9(demultiplexer_1_out8),
    .B1_10(demultiplexer_1_out12), .B1_11(demultiplexer_1_out9), .B1_12(demultiplexer_1_out13),
    .B1_13(demultiplexer_1_out10), .B1_14(demultiplexer_1_out14), .B1_15(demultiplexer_1_out11),
    .B1_16(demultiplexer_1_out15), .TICK(update_screen), .C1(capacitormodule_16x16_1_c1),
    .C1_9(capacitormodule_16x16_1_c1_9), .C1_2(capacitormodule_16x16_1_c1_2),
    .C1_10(capacitormodule_16x16_1_c1_10), .C1_3(capacitormodule_16x16_1_c1_3),
    .C1_11(capacitormodule_16x16_1_c1_11), .C1_4(capacitormodule_16x16_1_c1_4),
    .C1_12(capacitormodule_16x16_1_c1_12), .C1_5(capacitormodule_16x16_1_c1_5),
    .C1_13(capacitormodule_16x16_1_c1_13), .C1_6(capacitormodule_16x16_1_c1_6),
    .C1_14(capacitormodule_16x16_1_c1_14), .C1_7(capacitormodule_16x16_1_c1_7),
    .C1_15(capacitormodule_16x16_1_c1_15), .C1_8(capacitormodule_16x16_1_c1_8),
    .C1_16(capacitormodule_16x16_1_c1_16), .A1(demultiplexer_2_out0), .A1_9(demultiplexer_2_out8),
    .A1_3(demultiplexer_2_out1), .A1_11(demultiplexer_2_out9), .A1_5(demultiplexer_2_out2),
    .A1_13(demultiplexer_2_out10), .A1_7(demultiplexer_2_out3), .A1_15(demultiplexer_2_out11),
    .A1_2(demultiplexer_2_out4), .A1_10(demultiplexer_2_out12), .A1_4(demultiplexer_2_out5),
    .A1_12(demultiplexer_2_out13), .A1_6(demultiplexer_2_out6), .A1_14(demultiplexer_2_out14),
    .A1_8(demultiplexer_2_out7), .A1_16(demultiplexer_2_out15), .result(tailBump), .to_Zero(restart_cap));
  Demultiplexer #(.select(4), .width(16), .disabled(0)) demultiplexer_2 (
    .out0(demultiplexer_2_out0), .out1(demultiplexer_2_out1), .out2(demultiplexer_2_out2),
    .out3(demultiplexer_2_out3), .out4(demultiplexer_2_out4), .out5(demultiplexer_2_out5),
    .out6(demultiplexer_2_out6), .out7(demultiplexer_2_out7), .out8(demultiplexer_2_out8),
    .out9(demultiplexer_2_out9), .out10(demultiplexer_2_out10), .out11(demultiplexer_2_out11),
    .out12(demultiplexer_2_out12), .out13(demultiplexer_2_out13), .out14(demultiplexer_2_out14),
    .out15(demultiplexer_2_out15), .in(multiplexer_4_out), .sel(multiplexer_3_out));  // open: en
  Demultiplexer #(.select(4), .disabled(0)) demultiplexer_3 (
    .out0(demultiplexer_3_out0[0]), .out1(demultiplexer_3_out0[1]), .out2(demultiplexer_3_out0[2]),
    .out3(demultiplexer_3_out0[3]), .out4(demultiplexer_3_out0[4]), .out5(demultiplexer_3_out0[5]),
    .out6(demultiplexer_3_out0[6]), .out7(demultiplexer_3_out0[7]), .out8(demultiplexer_3_out0[8]),
    .out9(demultiplexer_3_out0[9]), .out10(demultiplexer_3_out0[10]), .out11(demultiplexer_3_out0[11]),
    .out12(demultiplexer_3_out0[12]), .out13(demultiplexer_3_out0[13]), .out14(demultiplexer_3_out0[14]),
    .out15(demultiplexer_3_out0[15]), .in(pull_resistor_2_node), .sel(APPLEY));  // open: en
  Pull_Resistor #(.pull("X")) pull_resistor_2 (.node(pull_resistor_2_node));
  Demultiplexer #(.select(4), .width(16), .disabled(0)) demultiplexer_4 (
    .out0(demultiplexer_4_out0), .out1(demultiplexer_4_out1), .out2(demultiplexer_4_out2),
    .out3(demultiplexer_4_out3), .out4(demultiplexer_4_out4), .out5(demultiplexer_4_out5),
    .out6(demultiplexer_4_out6), .out7(demultiplexer_4_out7), .out8(demultiplexer_4_out8),
    .out9(demultiplexer_4_out9), .out10(demultiplexer_4_out10), .out11(demultiplexer_4_out11),
    .out12(demultiplexer_4_out12), .out13(demultiplexer_4_out13), .out14(demultiplexer_4_out14),
    .out15(demultiplexer_4_out15), .in(demultiplexer_3_out0), .sel(APPLEX), .en(enable_apple));
  bitExtender__16_32 bitextender_16_32_1 (.in_1(smallor_16_bit_3_out_3), .out_2(out_8));
  bitExtender__16_32 bitextender_16_32_2 (.in_1(smallor_16_bit_4_out_3), .out_2(out_10));
  bitExtender__16_32 bitextender_16_32_3 (.in_1(smallor_16_bit_1_out_3), .out_2(out_9));
  bitExtender__16_32 bitextender_16_32_4 (.in_1(smallor_16_bit_2_out_3), .out_2(out_11));
  smallOR__16_bit smallor_16_bit_1 (
    .in_1(capacitormodule_16x16_1_c1_2), .in_2(demultiplexer_4_out1), .out_3(smallor_16_bit_1_out_3));
  smallOR__16_bit smallor_16_bit_2 (
    .in_1(capacitormodule_16x16_1_c1_4), .in_2(demultiplexer_4_out3), .out_3(smallor_16_bit_2_out_3));
  smallOR__16_bit smallor_16_bit_3 (
    .in_1(capacitormodule_16x16_1_c1), .in_2(demultiplexer_4_out0), .out_3(smallor_16_bit_3_out_3));
  smallOR__16_bit smallor_16_bit_4 (
    .in_1(capacitormodule_16x16_1_c1_3), .in_2(demultiplexer_4_out2), .out_3(smallor_16_bit_4_out_3));
  bitExtender__16_32 bitextender_16_32_5 (.in_1(smallor_16_bit_8_out_3), .out_2(out_14));
  bitExtender__16_32 bitextender_16_32_6 (.in_1(smallor_16_bit_6_out_3), .out_2(out_15));
  bitExtender__16_32 bitextender_16_32_7 (.in_1(smallor_16_bit_7_out_3), .out_2(out_13));
  bitExtender__16_32 bitextender_16_32_8 (.in_1(smallor_16_bit_5_out_3), .out_2(out_12));
  smallOR__16_bit smallor_16_bit_5 (
    .in_1(capacitormodule_16x16_1_c1_5), .in_2(demultiplexer_4_out4), .out_3(smallor_16_bit_5_out_3));
  smallOR__16_bit smallor_16_bit_6 (
    .in_1(capacitormodule_16x16_1_c1_8), .in_2(demultiplexer_4_out7), .out_3(smallor_16_bit_6_out_3));
  smallOR__16_bit smallor_16_bit_7 (
    .in_1(capacitormodule_16x16_1_c1_6), .in_2(demultiplexer_4_out5), .out_3(smallor_16_bit_7_out_3));
  smallOR__16_bit smallor_16_bit_8 (
    .in_1(capacitormodule_16x16_1_c1_7), .in_2(demultiplexer_4_out6), .out_3(smallor_16_bit_8_out_3));
  bitExtender__16_32 bitextender_16_32_9 (.in_1(smallor_16_bit_11_out_3), .out_2(out_18));
  bitExtender__16_32 bitextender_16_32_10 (.in_1(smallor_16_bit_9_out_3), .out_2(out_16));
  bitExtender__16_32 bitextender_16_32_11 (.in_1(smallor_16_bit_10_out_3), .out_2(out_17));
  bitExtender__16_32 bitextender_16_32_12 (.in_1(smallor_16_bit_12_out_3), .out_2(out_19));
  smallOR__16_bit smallor_16_bit_9 (
    .in_1(capacitormodule_16x16_1_c1_9), .in_2(demultiplexer_4_out8), .out_3(smallor_16_bit_9_out_3));
  smallOR__16_bit smallor_16_bit_10 (
    .in_1(capacitormodule_16x16_1_c1_10), .in_2(demultiplexer_4_out9), .out_3(smallor_16_bit_10_out_3));
  smallOR__16_bit smallor_16_bit_11 (
    .in_1(capacitormodule_16x16_1_c1_11), .in_2(demultiplexer_4_out10), .out_3(smallor_16_bit_11_out_3));
  smallOR__16_bit smallor_16_bit_12 (
    .in_1(capacitormodule_16x16_1_c1_12), .in_2(demultiplexer_4_out11), .out_3(smallor_16_bit_12_out_3));
  bitExtender__16_32 bitextender_16_32_13 (.in_1(smallor_16_bit_16_out_3), .out_2(out_21));
  bitExtender__16_32 bitextender_16_32_14 (.in_1(smallor_16_bit_15_out_3), .out_2(out_22));
  bitExtender__16_32 bitextender_16_32_15 (.in_1(smallor_16_bit_13_out_3), .out_2(out_20));
  bitExtender__16_32 bitextender_16_32_16 (.in_1(smallor_16_bit_14_out_3), .out_2(out_23));
  smallOR__16_bit smallor_16_bit_13 (
    .in_1(capacitormodule_16x16_1_c1_13), .in_2(demultiplexer_4_out12), .out_3(smallor_16_bit_13_out_3));
  smallOR__16_bit smallor_16_bit_14 (
    .in_1(capacitormodule_16x16_1_c1_16), .in_2(demultiplexer_4_out15), .out_3(smallor_16_bit_14_out_3));
  smallOR__16_bit smallor_16_bit_15 (
    .in_1(capacitormodule_16x16_1_c1_15), .in_2(demultiplexer_4_out14), .out_3(smallor_16_bit_15_out_3));
  smallOR__16_bit smallor_16_bit_16 (
    .in_1(capacitormodule_16x16_1_c1_14), .in_2(demultiplexer_4_out13), .out_3(smallor_16_bit_16_out_3));

  // Notes on the sheet:
  //   Lose
  //   Eat apple
  //   Bump wall/tail
  //   I/O interface
  //   Free draw block
  //   contents of rom_1 (hex, n*v repeats v):
  //   0 0 f f0 0 10 0 0 f f0 8 10 f f0 0 0 7 10 8 90 8 60 0 0 f f0 8 90 8 10 0 0 f0 0 0 0 10 f f0 106*0 8
  //   10 8 90 f f0 0 0 8 60 8 90 7 10 0 0 f f0 8 10 f f0 0 0 0 10 f f0
  //   Disable other drawing devices
  //   Preloaded images
  //   Draw processor
  //   Interuptions
  //   Snake head
  //   Data out
  //   Selector
  //   Snake tail
  //   Screen update
  //   Apple draw
  //   Show apple
  //   To screen
endmodule

module keyboardChip (
  input  [2:0] ADDRESS,
  input  SEL,
  input  R_W,
  input  [3:0] Control,
  input  [7:0] DATA,
  output [7:0] DATA_2
);

  wire IO_3R, IO_3W, not_1_out, not_2_out, not_3_out, not_4_out, or_1_out, t1, t2, t3, t4;
  wire [1:0] selector;
  wire [3:0] controlled_buffer_8_out, Direction, Previous_Direction;
  wire [7:0] controlled_buffer_1_out, data_out, demultiplexer_1_out0, demultiplexer_1_out1,
       demultiplexer_1_out2, demultiplexer_1_out3, register_1_q, register_2_q, register_3_q, register_4_q;

  Demultiplexer #(.select(2), .width(8)) demultiplexer_1 (
    .out0(demultiplexer_1_out0), .out1(demultiplexer_1_out1), .out2(demultiplexer_1_out2),
    .out3(demultiplexer_1_out3), .in(controlled_buffer_1_out), .sel(selector), .en(IO_3W));
  assign controlled_buffer_1_out = IO_3W ? DATA : 8'bz;  // Controlled_Buffer controlled_buffer_1
  and u_IO_3R (IO_3R, R_W, SEL, ADDRESS[0], ADDRESS[1], ~ADDRESS[2]);  // AND_Gate
  and u_IO_3W (IO_3W, ~R_W, SEL, ADDRESS[0], ADDRESS[1], ~ADDRESS[2]);  // AND_Gate
  Decoder #(.select(2)) decoder_1 (.out0(t1), .out1(t2), .out2(t3), .out3(t4), .sel(selector), .en(IO_3W));
  Counter #(.width(2), .max('h3), .ongoal("stay"), .trigger("falling")) counter_1 (
    .Q(selector), .clk(IO_3W));  // open: load, D, count, carry, clr
  Register #(.trigger("high")) register_1 (.D(demultiplexer_1_out0), .Q(register_1_q), .clk(t1));  // open: en, clr
  Register #(.trigger("high")) register_2 (.D(demultiplexer_1_out1), .Q(register_2_q), .clk(t2));  // open: en, clr
  Register #(.trigger("high")) register_3 (.D(demultiplexer_1_out2), .Q(register_3_q), .clk(t3));  // open: en, clr
  assign data_out = Direction[3] ? register_4_q : 8'bz;  // Controlled_Buffer controlled_buffer_2
  Register #(.trigger("high")) register_4 (.D(demultiplexer_1_out3), .Q(register_4_q), .clk(t4));  // open: en, clr
  assign controlled_buffer_8_out[2] = not_1_out ? Control[2] : 1'bz;  // Controlled_Buffer controlled_buffer_3
  assign controlled_buffer_8_out[3] = not_2_out ? Control[3] : 1'bz;  // Controlled_Buffer controlled_buffer_4
  not not_1 (not_1_out, Previous_Direction[3]);
  not not_2 (not_2_out, Previous_Direction[2]);
  assign data_out = Direction[0] ? register_1_q : 8'bz;  // Controlled_Buffer controlled_buffer_5
  assign data_out = Direction[1] ? register_2_q : 8'bz;  // Controlled_Buffer controlled_buffer_6
  assign data_out = Direction[2] ? register_3_q : 8'bz;  // Controlled_Buffer controlled_buffer_7
  assign controlled_buffer_8_out[0] = not_3_out ? Control[0] : 1'bz;  // Controlled_Buffer controlled_buffer_8
  assign controlled_buffer_8_out[1] = not_4_out ? Control[1] : 1'bz;  // Controlled_Buffer controlled_buffer_9
  not not_3 (not_3_out, Previous_Direction[1]);
  not not_4 (not_4_out, Previous_Direction[0]);
  Pull_Resistor pull_resistor_1 (.node(data_out));
  assign DATA_2 = IO_3R ? data_out : 8'bz;  // Controlled_Buffer controlled_buffer_10
  Pull_Resistor pull_resistor_2 (.node(controlled_buffer_8_out[0]));
  Pull_Resistor pull_resistor_3 (.node(controlled_buffer_8_out[1]));
  Pull_Resistor pull_resistor_4 (.node(controlled_buffer_8_out[2]));
  Pull_Resistor pull_resistor_5 (.node(controlled_buffer_8_out[3]));
  or or_1 (or_1_out, controlled_buffer_8_out[0], controlled_buffer_8_out[1], controlled_buffer_8_out[2], controlled_buffer_8_out[3]);
  Register #(.width(4), .trigger("falling")) register_5 (
    .D(Direction), .Q(Previous_Direction), .clk(IO_3R));  // open: en, clr
  Register #(.width(4)) register_6 (.D(controlled_buffer_8_out), .Q(Direction), .clk(or_1_out));  // open: en, clr

  // Notes on the sheet:
  //   Address storage
  //   I/O interface
  //   LEFT
  //   RIGHT
  //   UP
  //   DOWN
  //   Key controller
endmodule

module randomGenChip (
  input  [2:0] ADDR,
  input  SEL,
  input  R_W,
  output [7:0] DATA
);

  wire IO_1R_out;
  wire [7:0] random_1_out;

  and IO_1R (IO_1R_out, R_W, SEL, ADDR[0], ~ADDR[1], ~ADDR[2]);  // AND_Gate
  Random random_1 (.clk(IO_1R_out), .out(random_1_out));  // open: next, clr
  assign DATA = IO_1R_out ? random_1_out : 8'bz;  // Controlled_Buffer controlled_buffer_1
endmodule

module scoreChip (
  input  [2:0] ADDRESS,
  input  SEL,
  input  R_W,
  input  [7:0] DATA,
  input  tck,
  output [7:0] to_Score_screen,
  output [7:0] DATA_2
);

  wire IO_4R_out, IO_4W_out;
  wire [7:0] controlled_buffer_1_out, Score_q;

  and IO_4W (IO_4W_out, ~R_W, SEL, ~ADDRESS[0], ~ADDRESS[1], ADDRESS[2]);  // AND_Gate
  assign controlled_buffer_1_out = IO_4W_out ? DATA : 8'bz;  // Controlled_Buffer controlled_buffer_1
  and IO_4R (IO_4R_out, R_W, SEL, ~ADDRESS[0], ~ADDRESS[1], ADDRESS[2]);  // AND_Gate
  Register #(.trigger("falling")) Score (.D(controlled_buffer_1_out), .Q(Score_q), .clk(tck));  // open: en, clr
  assign DATA_2 = IO_4R_out ? Score_q : 8'bz;  // Controlled_Buffer controlled_buffer_2
  inc inc_1 (.in(Score_q), .out(to_Score_screen), .\disable (1'b1));
endmodule

module capacitorModule__16x16 (
  input  [15:0] B1,
  input  [15:0] B1_2,
  input  [15:0] B1_3,
  input  [15:0] B1_4,
  input  [15:0] B1_5,
  input  [15:0] B1_6,
  input  [15:0] B1_7,
  input  [15:0] B1_8,
  input  [15:0] A1,
  input  [15:0] A1_2,
  input  [15:0] A1_3,
  input  [15:0] A1_4,
  input  [15:0] A1_5,
  input  [15:0] A1_6,
  input  [15:0] A1_7,
  input  [15:0] A1_8,
  input  [15:0] B1_9,
  input  [15:0] B1_10,
  input  [15:0] B1_11,
  input  [15:0] B1_12,
  input  to_Zero,
  input  [15:0] B1_13,
  input  [15:0] B1_14,
  input  [15:0] B1_15,
  input  [15:0] B1_16,
  input  TICK,
  input  [15:0] A1_9,
  input  [15:0] A1_10,
  input  [15:0] A1_11,
  input  [15:0] A1_12,
  input  [15:0] A1_13,
  input  [15:0] A1_14,
  input  [15:0] A1_15,
  input  [15:0] A1_16,
  output [15:0] C1,
  output [15:0] C1_2,
  output [15:0] C1_3,
  output [15:0] C1_4,
  output [15:0] C1_5,
  output [15:0] C1_6,
  output [15:0] C1_7,
  output [15:0] C1_8,
  output [15:0] C1_9,
  output [15:0] C1_10,
  output [15:0] C1_11,
  output [15:0] C1_12,
  output [15:0] C1_13,
  output [15:0] C1_14,
  output [15:0] C1_15,
  output [15:0] C1_16,
  output result
);

  wire [15:0] and_1_out, and_2_out, and_3_out, and_4_out, and_5_out, and_6_out, and_7_out, and_8_out,
       and_9_out, and_10_out, and_11_out, and_12_out, and_13_out, and_14_out, and_15_out, and_16_out,
       and_17_out, and_18_out, and_19_out, and_20_out, and_21_out, and_22_out, and_23_out, and_24_out,
       and_25_out, and_26_out, and_27_out, and_28_out, and_29_out, and_30_out, and_31_out, and_32_out,
       or_1_out, or_2_out, or_3_out, or_4_out, or_5_out, or_6_out, or_7_out, or_8_out, or_9_out, or_10_out,
       or_11_out, or_12_out, or_13_out, or_14_out, or_15_out, or_16_out;

  Pull_Resistor pull_resistor_1 (.node(result));
  assign and_1_out = ~B1 & C1;  // AND_Gate and_1, 16 bits wide
  bitReducer__16_1 bitreducer_16_1_1 (.out_2(result), .in_1(and_2_out));
  assign and_2_out = and_1_out & A1;  // AND_Gate and_2, 16 bits wide
  assign and_3_out = ~B1_9 & C1_9;  // AND_Gate and_3, 16 bits wide
  Register #(.width(16)) register_1 (.D(or_1_out), .Q(C1), .clk(TICK), .clr(to_Zero));  // open: en
  assign or_1_out = and_1_out | A1;  // OR_Gate or_1, 16 bits wide
  assign or_2_out = and_3_out | A1_9;  // OR_Gate or_2, 16 bits wide
  assign and_4_out = and_3_out & A1_9;  // AND_Gate and_4, 16 bits wide
  bitReducer__16_1 bitreducer_16_1_2 (.out_2(result), .in_1(and_4_out));
  Register #(.width(16)) register_2 (.D(or_2_out), .Q(C1_9), .clk(TICK), .clr(to_Zero));  // open: en
  assign and_5_out = ~B1_3 & C1_2;  // AND_Gate and_5, 16 bits wide
  Register #(.width(16)) register_3 (.D(or_3_out), .Q(C1_2), .clk(TICK), .clr(to_Zero));  // open: en
  assign or_3_out = and_5_out | A1_3;  // OR_Gate or_3, 16 bits wide
  assign and_6_out = and_5_out & A1_3;  // AND_Gate and_6, 16 bits wide
  bitReducer__16_1 bitreducer_16_1_3 (.out_2(result), .in_1(and_6_out));
  assign and_7_out = ~B1_11 & C1_10;  // AND_Gate and_7, 16 bits wide
  assign or_4_out = and_7_out | A1_11;  // OR_Gate or_4, 16 bits wide
  bitReducer__16_1 bitreducer_16_1_4 (.out_2(result), .in_1(and_8_out));
  assign and_8_out = and_7_out & A1_11;  // AND_Gate and_8, 16 bits wide
  Register #(.width(16)) register_4 (.D(or_4_out), .Q(C1_10), .clk(TICK), .clr(to_Zero));  // open: en
  assign and_9_out = ~B1_5 & C1_3;  // AND_Gate and_9, 16 bits wide
  assign or_5_out = and_9_out | A1_5;  // OR_Gate or_5, 16 bits wide
  Register #(.width(16)) register_5 (.D(or_5_out), .Q(C1_3), .clk(TICK), .clr(to_Zero));  // open: en
  bitReducer__16_1 bitreducer_16_1_5 (.out_2(result), .in_1(and_10_out));
  assign and_10_out = and_9_out & A1_5;  // AND_Gate and_10, 16 bits wide
  assign and_11_out = ~B1_13 & C1_11;  // AND_Gate and_11, 16 bits wide
  assign or_6_out = and_11_out | A1_13;  // OR_Gate or_6, 16 bits wide
  assign and_12_out = and_11_out & A1_13;  // AND_Gate and_12, 16 bits wide
  bitReducer__16_1 bitreducer_16_1_6 (.out_2(result), .in_1(and_12_out));
  Register #(.width(16)) register_6 (.D(or_6_out), .Q(C1_11), .clk(TICK), .clr(to_Zero));  // open: en
  assign and_13_out = ~B1_7 & C1_4;  // AND_Gate and_13, 16 bits wide
  assign or_7_out = and_13_out | A1_7;  // OR_Gate or_7, 16 bits wide
  bitReducer__16_1 bitreducer_16_1_7 (.out_2(result), .in_1(and_14_out));
  assign and_14_out = and_13_out & A1_7;  // AND_Gate and_14, 16 bits wide
  assign and_15_out = ~B1_15 & C1_12;  // AND_Gate and_15, 16 bits wide
  assign and_16_out = and_15_out & A1_15;  // AND_Gate and_16, 16 bits wide
  bitReducer__16_1 bitreducer_16_1_8 (.out_2(result), .in_1(and_16_out));
  Register #(.width(16)) register_7 (.D(or_7_out), .Q(C1_4), .clk(TICK), .clr(to_Zero));  // open: en
  assign or_8_out = and_15_out | A1_15;  // OR_Gate or_8, 16 bits wide
  Register #(.width(16)) register_8 (.D(or_8_out), .Q(C1_12), .clk(TICK), .clr(to_Zero));  // open: en
  assign and_17_out = ~B1_2 & C1_5;  // AND_Gate and_17, 16 bits wide
  assign and_18_out = and_17_out & A1_2;  // AND_Gate and_18, 16 bits wide
  assign and_19_out = ~B1_10 & C1_13;  // AND_Gate and_19, 16 bits wide
  Register #(.width(16)) register_9 (.D(or_9_out), .Q(C1_5), .clk(TICK), .clr(to_Zero));  // open: en
  assign or_9_out = and_17_out | A1_2;  // OR_Gate or_9, 16 bits wide
  bitReducer__16_1 bitreducer_16_1_9 (.out_2(result), .in_1(and_18_out));
  assign or_10_out = and_19_out | A1_10;  // OR_Gate or_10, 16 bits wide
  assign and_20_out = and_19_out & A1_10;  // AND_Gate and_20, 16 bits wide
  bitReducer__16_1 bitreducer_16_1_10 (.out_2(result), .in_1(and_20_out));
  Register #(.width(16)) register_10 (.D(or_10_out), .Q(C1_13), .clk(TICK), .clr(to_Zero));  // open: en
  assign and_21_out = ~B1_4 & C1_6;  // AND_Gate and_21, 16 bits wide
  assign or_11_out = and_21_out | A1_4;  // OR_Gate or_11, 16 bits wide
  assign and_22_out = and_21_out & A1_4;  // AND_Gate and_22, 16 bits wide
  bitReducer__16_1 bitreducer_16_1_11 (.out_2(result), .in_1(and_22_out));
  assign and_23_out = ~B1_12 & C1_14;  // AND_Gate and_23, 16 bits wide
  bitReducer__16_1 bitreducer_16_1_12 (.out_2(result), .in_1(and_24_out));
  assign and_24_out = and_23_out & A1_12;  // AND_Gate and_24, 16 bits wide
  Register #(.width(16)) register_11 (.D(or_11_out), .Q(C1_6), .clk(TICK), .clr(to_Zero));  // open: en
  Register #(.width(16)) register_12 (.D(or_12_out), .Q(C1_14), .clk(TICK), .clr(to_Zero));  // open: en
  assign or_12_out = and_23_out | A1_12;  // OR_Gate or_12, 16 bits wide
  assign and_25_out = ~B1_6 & C1_7;  // AND_Gate and_25, 16 bits wide
  assign or_13_out = and_25_out | A1_6;  // OR_Gate or_13, 16 bits wide
  assign and_26_out = and_25_out & A1_6;  // AND_Gate and_26, 16 bits wide
  bitReducer__16_1 bitreducer_16_1_13 (.out_2(result), .in_1(and_26_out));
  assign and_27_out = ~B1_14 & C1_15;  // AND_Gate and_27, 16 bits wide
  assign and_28_out = and_27_out & A1_14;  // AND_Gate and_28, 16 bits wide
  bitReducer__16_1 bitreducer_16_1_14 (.out_2(result), .in_1(and_28_out));
  Register #(.width(16)) register_13 (.D(or_13_out), .Q(C1_7), .clk(TICK), .clr(to_Zero));  // open: en
  Register #(.width(16)) register_14 (.D(or_14_out), .Q(C1_15), .clk(TICK), .clr(to_Zero));  // open: en
  assign or_14_out = and_27_out | A1_14;  // OR_Gate or_14, 16 bits wide
  assign and_29_out = ~B1_8 & C1_8;  // AND_Gate and_29, 16 bits wide
  assign or_15_out = and_29_out | A1_8;  // OR_Gate or_15, 16 bits wide
  assign and_30_out = and_29_out & A1_8;  // AND_Gate and_30, 16 bits wide
  bitReducer__16_1 bitreducer_16_1_15 (.out_2(result), .in_1(and_30_out));
  assign and_31_out = ~B1_16 & C1_16;  // AND_Gate and_31, 16 bits wide
  assign and_32_out = and_31_out & A1_16;  // AND_Gate and_32, 16 bits wide
  Register #(.width(16)) register_15 (.D(or_15_out), .Q(C1_8), .clk(TICK), .clr(to_Zero));  // open: en
  assign or_16_out = and_31_out | A1_16;  // OR_Gate or_16, 16 bits wide
  Register #(.width(16)) register_16 (.D(or_16_out), .Q(C1_16), .clk(TICK), .clr(to_Zero));  // open: en
  bitReducer__16_1 bitreducer_16_1_16 (.out_2(result), .in_1(and_32_out));

  // Other names for the same wires on the sheet: res = result; zero = to_Zero
endmodule
